// Logisim project CPU 流水线数据重定向.circ as structural Verilog: 15 circuits, main circuit CPU
module CPU (
);

  wire B, Branch, Break, button_1_out, C2R, CLK, clock_1_out, Con, control_1_alusrcx, control_1_alusrcy,
       control_1_branch, control_1_c2r, control_1_cw, control_1_jal, control_1_jump, control_1_m2r,
       control_1_mw, control_1_regdst, control_1_rw, control_1_unsign, CW, Equal, EqualE, ERET, ERETD, ERETM,
       ERETW, ex_mem_1_c2r_2, ex_mem_1_cw_2, ex_mem_1_equal_2, ex_mem_1_jal_2, ex_mem_1_syscall, Halt,
       hazard_unit_1_flushd, hazard_unit_1_flushe, hazard_unit_1_pause, id_ex_1_alusrcx_2, id_ex_1_alusrcy_2,
       id_ex_1_c2r_2, id_ex_1_cw_2, id_ex_1_eret_2, id_ex_1_jal_2, id_ex_1_judgeb_2, id_ex_1_mw_2,
       id_ex_1_regdst, id_ex_1_sign_2, Int, ISR, JALW, JR, JRD, Jump, M2RE, MemtoRegM, MemtoRegW, MemWrite,
       not_1_out, or_1_out, or_2_out, or_3_out, or_4_out, or_5_out, register_2_q, RWE, RWM, RWW, SYSCALL,
       SYSCALLD, SYSCALLE, xnor_1_out, xor_1_out;
  wire [1:0] hazard_unit_1_forwarda0, hazard_unit_1_forwardxe, hazard_unit_1_forwardye;
  wire [3:0] ALUop, control_1_aluop, id_ex_1_ir_2_3;
  wire [4:0] ex_1_writereg, ex_mem_1_writereg_2, id_1_r1_num, id_1_r2_num, id_1_rd, id_1_rs, id_1_rt,
       id_1_writereg_num, id_ex_1_rd_3, id_ex_1_rs_2, id_ex_1_rt_2, multiplexer_2_out, WriteRegW;
  wire [5:0] OP;
  wire [9:0] controlled_buffer_1_out;
  wire [25:0] id_ex_1_ir_2, if_id_1_irout;
  wire [27:26] id_ex_1_ir_2_2;
  wire [31:0] a0, alu_1_result, alu_2_result, alu_3_result, bit_extender_1_out, bit_extender_2_out,
       bit_extender_3_out, cp0_1_out_8, EPC, ex_1_alux, ex_1_aluy, ex_1_writedata, ex_mem_1_aluout_2,
       ex_mem_1_ir_2, ex_mem_1_pc_4_2, ex_mem_1_writedata_2, id_ex_1_imm1_2, id_ex_1_imm2_2, id_ex_1_imm3_2,
       id_ex_1_pc_4, id_ex_1_pcout, id_ex_1_r1out, id_ex_1_r2out, if_id_1_pcout,
       instruction_counter_1_bubble, instruction_counter_1_out_6, instruction_counter_1_out_7,
       instruction_counter_1_out_8, instruction_counter_1_out_9, main_1_reg1, main_1_reg2_2,
       mem_wb_1_aluout_2, mem_wb_1_ir_2, mem_wb_1_pc_4_2, mem_wb_1_readdata_2, multiplexer_1_out,
       multiplexer_3_out, multiplexer_4_out, multiplexer_5_out, multiplexer_6_out, PC,
       pc_select_unit_1_pcout, PCAddr, ram_1_data, register_1_q, rom_2_data, shifter_1_out;

  PC_Select_Unit pc_select_unit_1 (
    .PC_4(alu_1_result), .PCBranch(alu_2_result), .PCJump({id_ex_1_ir_2_3, id_ex_1_ir_2, 2'b00}),
    .ra(id_ex_1_r1out), .EPC(EPC), .PCout(pc_select_unit_1_pcout), .B(B), .J(Jump), .Int(Int), .ERET(ERETM),
    .JR(JR));
  assign controlled_buffer_1_out = xnor_1_out ? PC[11:2] : 10'bz;  // Controlled_Buffer controlled_buffer_1
  xnor xnor_1 (xnor_1_out, Con, register_2_q);
  Button u_B (.out(Con));
  Register #(.width(32)) register_1 (.D(a0), .en(SYSCALLE), .Q(register_1_q), .clk(CLK));  // open: clr
  HALT halt_1 (
    .ISR(ISR), .Continue(Con), .Break(Break), .Equal(Equal), .SYSCALL(SYSCALL), .CLKout(CLK),
    .CLK(clock_1_out), .Halt(Halt));
  Clock clock_1 (.out(clock_1_out));
  Register #(.width(32)) \PC寄存器  (
    .D(pc_select_unit_1_pcout), .en(hazard_unit_1_pause), .Q(PC), .clk(CLK));  // open: clr
  Instruction_Counter instruction_counter_1 (
    .out_7(instruction_counter_1_out_7), .in_1(OP), .in_2(CLK), .out_6(instruction_counter_1_out_6),
    .out_8(instruction_counter_1_out_8), .out_9(instruction_counter_1_out_9), .in_4(Halt),
    .Pause(hazard_unit_1_pause), .Bubble(instruction_counter_1_bubble), .JRD(JRD));
  Hex_Digit_Display hex_digit_display_1 (.value(register_1_q[27:24]));  // open: dp
  Hex_Digit_Display hex_digit_display_2 (.value(register_1_q[31:28]));  // open: dp
  ALU alu_1 (
    .AluOP(4'b0101), .X(32'h4), .Result(alu_1_result), .Y(PC));  // open: Equal, Signed_Overflow, Result_2, UnSigned_Overflow
  // Probe on instruction_counter_1_out_6
  // Probe on instruction_counter_1_bubble
  ROM #(.addrWidth(10), .dataWidth(1)) rom_1 (.addr(controlled_buffer_1_out), .data(Break));  // open: sel
  Hex_Digit_Display hex_digit_display_3 (.value(register_1_q[19:16]));  // open: dp
  Hex_Digit_Display hex_digit_display_4 (.value(register_1_q[23:20]));  // open: dp
  ROM #(.addrWidth(10), .dataWidth(32)) rom_2 (.addr(PC[11:2]), .data(rom_2_data));  // open: sel
  Register #(.width(1)) register_2 (.D(Break), .Q(register_2_q), .clk(CLK));  // open: en, clr
  Hex_Digit_Display hex_digit_display_5 (.value(register_1_q[11:8]));  // open: dp
  Hex_Digit_Display hex_digit_display_6 (.value(register_1_q[15:12]));  // open: dp
  IF_ID if_id_1 (
    .PC(alu_1_result), .IR(rom_2_data), .PCout(if_id_1_pcout), .IRout({OP, if_id_1_irout}), .CLK(CLK),
    .Clear(hazard_unit_1_flushd), .Pause(hazard_unit_1_pause));
  Hex_Digit_Display hex_digit_display_7 (.value(register_1_q[7:4]));  // open: dp
  Hex_Digit_Display hex_digit_display_8 (.value(register_1_q[3:0]));  // open: dp
  Control control_1 (
    .OP(OP), .Funct(if_id_1_irout[5:0]), .RegDst(control_1_regdst), .Branch(control_1_branch),
    .Jump(control_1_jump), .M2R(control_1_m2r), .MW(control_1_mw), .ALUSrcY(control_1_alusrcy),
    .ALUop(control_1_aluop), .RW(control_1_rw), .JR(JRD), .ALUSrcX(control_1_alusrcx), .C2R(control_1_c2r),
    .CW(control_1_cw), .JAL(control_1_jal), .SYSCALL(SYSCALLD), .M(if_id_1_irout[25:21]),
    .UNSIGN(control_1_unsign), .ERET(ERETD));
  ID id_1 (
    .Instr({OP, if_id_1_irout}), .WriteReg(WriteRegW), .SYSCALL(SYSCALLD), .Int(Int), .ERET(ERETD),
    .R1_num(id_1_r1_num), .R2_num(id_1_r2_num), .WriteReg_num(id_1_writereg_num), .JAL(JALW), .rt(id_1_rt),
    .rd(id_1_rd), .rs(id_1_rs));
  not not_1 (not_1_out, CLK);
  assign bit_extender_1_out = {{16{1'b0}}, if_id_1_irout[15:0]};  // Bit_Extender bit_extender_1
  assign bit_extender_2_out = {{16{if_id_1_irout[15]}}, if_id_1_irout[15:0]};  // Bit_Extender bit_extender_2
  assign bit_extender_3_out = {{27{if_id_1_irout[10]}}, if_id_1_irout[10:6]};  // Bit_Extender bit_extender_3
  Multiplexer #(.width(32), .enable("false")) multiplexer_1 (
    .in0(multiplexer_5_out), .in1(mem_wb_1_pc_4_2), .out(multiplexer_1_out), .sel(JALW));
  regfile_main main_1 (
    .Reg1_num(id_1_r1_num), .Reg2(id_1_r2_num), .Write_Reg_num(id_1_writereg_num), .Din(multiplexer_1_out),
    .Write_Enable(RWW), .Clock(not_1_out), .Reg1(main_1_reg1), .Reg2_2(main_1_reg2_2));  // open: s0_Value, a0_Value, v0_Value, ra_Value
  ID_EX id_ex_1 (
    .PC(if_id_1_pcout), .R1(main_1_reg1), .R2(main_1_reg2_2), .IMM1(bit_extender_1_out),
    .IMM2(bit_extender_2_out), .IMM3(bit_extender_3_out), .RD_2(control_1_regdst), .SIGN(control_1_unsign),
    .JR(JRD), .Branch(control_1_branch), .C2R(control_1_c2r), .ALUSrcX(control_1_alusrcx),
    .JAL(control_1_jal), .JUMP(control_1_jump), .CW(control_1_cw), .ALUSrcY(control_1_alusrcy),
    .ALUop(control_1_aluop), .M2R(control_1_m2r), .ERET(ERETD), .RW(control_1_rw), .PCout(id_ex_1_pcout),
    .R1out(id_ex_1_r1out), .R2out(id_ex_1_r2out), .IMM1_2(id_ex_1_imm1_2), .IMM2_2(id_ex_1_imm2_2),
    .IMM3_2(id_ex_1_imm3_2), .RegDst(id_ex_1_regdst), .Branch_2(Branch), .Jump_2(Jump), .M2R_2(M2RE),
    .MW_2(id_ex_1_mw_2), .C2R_2(id_ex_1_c2r_2), .CW_2(id_ex_1_cw_2), .ERET_2(id_ex_1_eret_2),
    .SIGN_2(id_ex_1_sign_2), .ALUSrcX_2(id_ex_1_alusrcx_2), .ALUSrcY_2(id_ex_1_alusrcy_2), .RW_2(RWE),
    .JR_2(JR), .JAL_2(id_ex_1_jal_2), .ALUop_2(ALUop), .rd(id_1_rd), .rt(id_1_rt), .rd_3(id_ex_1_rd_3),
    .rt_2(id_ex_1_rt_2), .SYS(SYSCALLD), .Syscall(SYSCALLE), .JudgeB(OP[0]), .JudgeB_2(id_ex_1_judgeb_2),
    .MW(control_1_mw), .CLK(CLK), .IR({OP, if_id_1_irout}),
    .IR_2({id_ex_1_ir_2_3, id_ex_1_ir_2_2, id_ex_1_ir_2}), .Clear(hazard_unit_1_flushe), .rs_2(id_ex_1_rs_2),
    .rs(id_1_rs), .PC_4(id_ex_1_pc_4));
  Hazard_Unit hazard_unit_1 (
    .RsE(id_ex_1_rs_2), .WriteRegM(ex_mem_1_writereg_2), .WriteRegW(WriteRegW), .RtE(id_ex_1_rt_2),
    .WriteRegE(ex_1_writereg), .Pause(hazard_unit_1_pause), .FlushD(hazard_unit_1_flushd), .BranchE(B),
    .JumpE(Jump), .RegWriteE(RWE), .RegWriteM(RWM), .RegWriteW(RWW), .FlushE(hazard_unit_1_flushe),
    .SyscallE(SYSCALLE), .ForwardXE(hazard_unit_1_forwardxe), .ForwardYE(hazard_unit_1_forwardye),
    .M2RE(M2RE), .EqualE(EqualE), .Forwarda0(hazard_unit_1_forwarda0), .RsD(id_1_rs), .RtD(id_1_rt));
  EX ex_1 (
    .R1(id_ex_1_r1out), .R2(id_ex_1_r2out), .SignedIMM(id_ex_1_imm2_2), .UnsignedIMM(id_ex_1_imm1_2),
    .sa(id_ex_1_imm3_2), .rt(id_ex_1_rt_2), .rd(id_ex_1_rd_3), .ALUX(ex_1_alux), .ALUY(ex_1_aluy),
    .WriteReg(ex_1_writereg), .RD_2(id_ex_1_regdst), .UNSIGN(id_ex_1_sign_2), .ALUSrcY(id_ex_1_alusrcy_2),
    .SYSCALL(SYSCALLE), .ForwardX(hazard_unit_1_forwardxe), .ForwardY(hazard_unit_1_forwardye),
    .ALUoutM(ex_mem_1_aluout_2), .ResultW(EPC), .WriteData(ex_1_writedata),
    .Forwarda0(hazard_unit_1_forwarda0), .a0(a0), .ALUSrcX(id_ex_1_alusrcx_2));
  Button button_1 (.out(button_1_out));
  // Probe on {OP, if_id_1_irout}
  xor xor_1 (xor_1_out, id_ex_1_judgeb_2, EqualE);
  Shifter #(.width(32)) shifter_1 (.in(id_ex_1_imm2_2), .\dist (5'b00010), .out(shifter_1_out));
  Multiplexer #(.width(5), .enable("false")) multiplexer_2 (
    .in0(if_id_1_irout[15:11]), .in1(5'b01100), .out(multiplexer_2_out), .sel(Int));
  Multiplexer #(.width(32), .enable("false")) multiplexer_3 (
    .in0(a0), .in1({32{1'b0}}), .out(multiplexer_3_out), .sel(Int));
  // Probe on {id_ex_1_ir_2_3, id_ex_1_ir_2_2, id_ex_1_ir_2}
  and and_1 (B, Branch, xor_1_out);
  ALU alu_2 (
    .AluOP(4'b0101), .X(id_ex_1_pcout), .Result(alu_2_result), .Y(shifter_1_out));  // open: Equal, Signed_Overflow, Result_2, UnSigned_Overflow
  ALU alu_3 (
    .AluOP(ALUop), .X(ex_1_alux), .Equal(EqualE), .Result(alu_3_result), .Y(ex_1_aluy));  // open: Signed_Overflow, Result_2, UnSigned_Overflow
  CP0 cp0_1 (
    .in_2(multiplexer_3_out), .out_8(cp0_1_out_8), .in_1(multiplexer_2_out), .in_3(multiplexer_2_out),
    .in_4(or_1_out), .in_6(CLK), .in_5(button_1_out), .in_7(ERET), .out_9(PCAddr), .out_11(Int), .out_10(ISR));
  or or_1 (or_1_out, CW, Int);
  // Probe on ex_mem_1_ir_2
  EX_MEM ex_mem_1 (
    .ALUout(alu_3_result), .WriteData(ex_1_writedata), .WriteReg(ex_1_writereg), .Equal(EqualE),
    .SYS(SYSCALLE), .M2R(M2RE), .ERET(id_ex_1_eret_2), .MW(id_ex_1_mw_2), .JAL(id_ex_1_jal_2), .RW(RWE),
    .CW(id_ex_1_cw_2), .CLK(CLK), .ALUout_2(ex_mem_1_aluout_2), .WriteData_2(ex_mem_1_writedata_2),
    .ERET_2(ERETM), .Equal_2(ex_mem_1_equal_2), .Syscall(ex_mem_1_syscall), .M2R_2(MemtoRegM),
    .MW_2(MemWrite), .JAL_2(ex_mem_1_jal_2), .RW_2(RWM), .CW_2(ex_mem_1_cw_2),
    .WriteReg_2(ex_mem_1_writereg_2), .IR({id_ex_1_ir_2_3, id_ex_1_ir_2_2, id_ex_1_ir_2}),
    .IR_2(ex_mem_1_ir_2), .C2R(id_ex_1_c2r_2), .C2R_2(ex_mem_1_c2r_2), .PC_4(id_ex_1_pc_4),
    .PC_4_2(ex_mem_1_pc_4_2));
  or or_2 (or_2_out, Int, ERETM);
  Multiplexer #(.width(32), .enable("false")) multiplexer_4 (
    .in0(ex_mem_1_aluout_2), .in1(PCAddr), .out(multiplexer_4_out), .sel(or_2_out));
  Multiplexer #(.width(32), .enable("false")) multiplexer_5 (
    .in0(EPC), .in1(cp0_1_out_8), .out(multiplexer_5_out), .sel(C2R));
  // Probe on mem_wb_1_ir_2
  or or_3 (or_3_out, Int, MemWrite);
  Multiplexer #(.width(32), .enable("false")) multiplexer_6 (
    .in0(ex_mem_1_writedata_2), .in1(PC), .out(multiplexer_6_out), .sel(Int));
  or or_4 (or_4_out, ERETM, Int, MemtoRegM);
  RAM #(.addrWidth(10), .dataWidth(32), .bus("separate")) ram_1 (
    .addr(multiplexer_4_out[11:2]), .din(multiplexer_6_out), .data(ram_1_data), .str(or_3_out), .clk(CLK),
    .ld(or_4_out));  // open: sel, clr
  MEM_WB mem_wb_1 (
    .ReadData(ram_1_data), .ALUout(multiplexer_4_out), .WriteReg(ex_mem_1_writereg_2),
    .SYS(ex_mem_1_syscall), .M2R(MemtoRegM), .ERET(ERETM), .JAL(ex_mem_1_jal_2), .RW(RWM),
    .CW(ex_mem_1_cw_2), .C2R(ex_mem_1_c2r_2), .CLK(CLK), .ReadData_2(mem_wb_1_readdata_2),
    .ALUout_2(mem_wb_1_aluout_2), .WriteReg_2(WriteRegW), .ERET_2(ERETW), .Syscall(SYSCALL),
    .M2R_2(MemtoRegW), .RegWrite(RWW), .JAL_2(JALW), .CW_2(CW), .C2R_2(C2R), .IR(ex_mem_1_ir_2),
    .IR_2(mem_wb_1_ir_2), .Equal(ex_mem_1_equal_2), .Equal_2(Equal), .PC_4(ex_mem_1_pc_4_2),
    .PC_4_2(mem_wb_1_pc_4_2));
  or or_5 (or_5_out, MemtoRegW, Int, ERETW);
  Multiplexer #(.width(32), .enable("false")) multiplexer_7 (
    .in0(mem_wb_1_aluout_2), .in1(mem_wb_1_readdata_2), .out(EPC), .sel(or_5_out));

  // Notes on the sheet:
  //   Breakpoint Controller
  //   contents of rom_1 (hex, n*v repeats v):
  //   227*0 1
  //   Display Circuit
  //   contents of rom_2 (hex, n*v repeats v):
  //   2010ffff 20110000 ae300000 22100001 22310004 ae300000 22100001 22310004 ae300000 22100001 22310004
  //   ae300000 22100001 22310004 ae300000 22100001 22310004 ae300000 22100001 22310004 ae300000 22100001
  //   22310004 ae300000 22100001 22310004 ae300000 22100001 22310004 ae300000 22100001 22310004 ae300000
  //   22100001 22310004 ae300000 22100001 22310004 ae300000 22100001 22310004 ae300000 22100001 22310004
  //   ae300000 22100001 22310004 ae300000 22100001 22310004 22100001 8020 2011003c 8e130000 8e340000
  //   274402a 11000002 ae330000 ae140000 2231fffc 1611fff8 102020 20020022 c 22100004 2011003c 1611fff2
  //   2002000a c
endmodule

module Control (
  input  [4:0] M,
  input  [5:0] OP,
  input  [5:0] Funct,
  output RegDst,
  output MW,
  output JR,
  output SYSCALL,
  output Branch,
  output ALUSrcX,
  output JAL,
  output UNSIGN,
  output Jump,
  output ALUSrcY,
  output C2R,
  output ERET,
  output M2R,
  output RW,
  output CW,
  output [3:0] ALUop
);

  wire and_7_out, and_8_out, and_9_out, and_14_out, and_15_out, and_16_out, and_17_out, and_18_out,
       and_19_out, and_20_out, and_21_out, and_22_out, not_1_out, not_2_out, not_3_out, not_4_out, not_5_out,
       not_6_out, not_7_out, not_8_out, not_9_out, not_10_out, not_11_out, not_12_out, not_13_out,
       not_14_out, not_15_out, not_16_out, not_17_out, not_18_out, not_19_out, not_20_out, not_21_out,
       not_22_out, not_23_out, not_24_out, not_25_out, not_26_out, not_27_out, not_28_out, not_29_out,
       not_30_out, not_31_out, not_32_out, not_33_out, not_34_out, not_35_out, not_36_out, not_37_out,
       not_38_out, not_39_out, not_40_out, not_41_out, not_42_out, not_43_out, not_44_out, not_45_out,
       not_46_out, not_47_out, not_48_out, not_49_out, not_50_out, not_51_out, not_52_out, not_53_out,
       not_54_out, not_55_out, not_56_out, not_57_out, not_58_out, not_59_out, not_60_out, not_61_out,
       not_62_out, not_63_out, not_64_out, not_65_out, not_66_out, not_67_out, not_68_out, not_69_out,
       not_70_out, not_71_out, not_72_out, not_73_out, not_74_out, not_75_out, not_76_out, not_77_out,
       not_78_out, not_79_out, not_80_out, not_81_out, not_82_out, not_83_out, not_84_out, not_85_out,
       not_86_out, not_87_out, not_88_out, not_89_out, not_90_out, not_91_out, not_92_out, not_93_out,
       not_94_out, not_95_out, not_96_out, not_97_out, not_98_out, not_99_out, not_100_out, not_101_out,
       not_102_out, not_103_out, not_104_out, not_105_out, not_106_out, not_107_out, not_108_out,
       not_109_out, not_110_out, not_111_out, or_2_out, or_3_out;

  not not_1 (not_1_out, OP[5]);
  not not_2 (not_2_out, OP[4]);
  not not_3 (not_3_out, OP[3]);
  not not_4 (not_4_out, OP[2]);
  not not_5 (not_5_out, OP[1]);
  not not_6 (not_6_out, OP[0]);
  not not_7 (not_7_out, OP[5]);
  not not_8 (not_8_out, OP[4]);
  not not_9 (not_9_out, OP[3]);
  not not_10 (not_10_out, OP[2]);
  not not_11 (not_11_out, OP[5]);
  not not_12 (not_12_out, OP[4]);
  not not_13 (not_13_out, OP[3]);
  not not_14 (not_14_out, OP[1]);
  not not_15 (not_15_out, OP[4]);
  not not_16 (not_16_out, OP[3]);
  not not_17 (not_17_out, OP[2]);
  not not_18 (not_18_out, OP[4]);
  not not_19 (not_19_out, OP[2]);
  not not_20 (not_20_out, OP[5]);
  not not_21 (not_21_out, OP[3]);
  not not_22 (not_22_out, OP[2]);
  not not_23 (not_23_out, OP[1]);
  not not_24 (not_24_out, OP[0]);
  not not_25 (not_25_out, M[4]);
  not not_26 (not_26_out, M[3]);
  not not_27 (not_27_out, M[2]);
  not not_28 (not_28_out, M[1]);
  not not_29 (not_29_out, M[0]);
  not not_30 (not_30_out, OP[5]);
  not not_31 (not_31_out, OP[3]);
  not not_32 (not_32_out, OP[2]);
  not not_33 (not_33_out, OP[1]);
  not not_34 (not_34_out, OP[0]);
  not not_35 (not_35_out, M[4]);
  not not_36 (not_36_out, M[3]);
  not not_37 (not_37_out, M[1]);
  not not_38 (not_38_out, M[0]);
  not not_39 (not_39_out, OP[5]);
  not not_40 (not_40_out, OP[4]);
  not not_41 (not_41_out, OP[3]);
  not not_42 (not_42_out, OP[2]);
  not not_43 (not_43_out, Funct[5]);
  not not_44 (not_44_out, Funct[4]);
  not not_45 (not_45_out, Funct[2]);
  not not_46 (not_46_out, Funct[1]);
  not not_47 (not_47_out, Funct[0]);
  not not_48 (not_48_out, OP[5]);
  not not_49 (not_49_out, OP[4]);
  not not_50 (not_50_out, OP[1]);
  not not_51 (not_51_out, OP[5]);
  not not_52 (not_52_out, OP[4]);
  not not_53 (not_53_out, OP[1]);
  not not_54 (not_54_out, OP[5]);
  not not_55 (not_55_out, OP[3]);
  not not_56 (not_56_out, OP[2]);
  not not_57 (not_57_out, OP[1]);
  not not_58 (not_58_out, OP[0]);
  not not_59 (not_59_out, Funct[5]);
  not not_60 (not_60_out, Funct[2]);
  not not_61 (not_61_out, Funct[1]);
  not not_62 (not_62_out, Funct[0]);
  and and_1 (RegDst, not_1_out, not_2_out, not_3_out, not_4_out, not_5_out, not_6_out);
  and and_2 (Jump, not_7_out, not_8_out, not_9_out, not_10_out, OP[1]);
  and and_3 (Branch, not_11_out, not_12_out, not_13_out, OP[2], not_14_out);
  and and_4 (M2R, OP[5], not_15_out, not_16_out, not_17_out, OP[1], OP[0]);
  and and_5 (MW, OP[5], not_18_out, OP[3], not_19_out, OP[1], OP[0]);
  and and_6 (JAL, not_39_out, not_40_out, not_41_out, not_42_out, OP[1], OP[0]);
  and and_7 (and_7_out, not_43_out, not_44_out, Funct[3], not_45_out, not_46_out, not_47_out);
  and and_8 (and_8_out, not_48_out, not_49_out, OP[3], not_50_out, OP[0]);
  and and_9 (and_9_out, not_51_out, not_52_out, OP[3], OP[2], not_53_out);
  and and_10 (C2R, not_20_out, OP[4], not_21_out, not_22_out, not_23_out, not_24_out, not_25_out, not_26_out, not_27_out, not_28_out, not_29_out);
  and and_11 (CW, not_30_out, OP[4], not_31_out, not_32_out, not_33_out, not_34_out, not_35_out, not_36_out, M[2], not_37_out, not_38_out);
  and and_12 (JR, RegDst, and_7_out);
  or or_1 (UNSIGN, and_8_out, and_9_out);
  and and_13 (ERET, not_54_out, OP[4], not_55_out, not_56_out, not_57_out, not_58_out, not_59_out, Funct[4], Funct[3], not_60_out, not_61_out, not_62_out);
  ALU_Control alu_control_1 (
    .OP5(OP[5]), .OP4(OP[4]), .OP3(OP[3]), .OP2(OP[2]), .OP1(OP[1]), .OP0(OP[0]), .Funct5(Funct[5]),
    .Funct4(Funct[4]), .Funct3(Funct[3]), .Funct2(Funct[2]), .Sel3(ALUop[3]), .Funct1(Funct[1]),
    .Funct0(Funct[0]), .Sel2(ALUop[2]), .Sel1(ALUop[1]), .Sel0(ALUop[0]));
  not not_63 (not_63_out, OP[5]);
  not not_64 (not_64_out, OP[4]);
  not not_65 (not_65_out, OP[2]);
  not not_66 (not_66_out, OP[1]);
  not not_67 (not_67_out, OP[0]);
  not not_68 (not_68_out, OP[4]);
  not not_69 (not_69_out, OP[3]);
  not not_70 (not_70_out, OP[2]);
  not not_71 (not_71_out, OP[5]);
  not not_72 (not_72_out, OP[4]);
  not not_73 (not_73_out, OP[2]);
  not not_74 (not_74_out, OP[0]);
  not not_75 (not_75_out, OP[5]);
  not not_76 (not_76_out, OP[4]);
  not not_77 (not_77_out, OP[1]);
  not not_78 (not_78_out, OP[5]);
  not not_79 (not_79_out, OP[3]);
  not not_80 (not_80_out, OP[2]);
  not not_81 (not_81_out, OP[1]);
  not not_82 (not_82_out, OP[0]);
  not not_83 (not_83_out, M[4]);
  not not_84 (not_84_out, M[3]);
  not not_85 (not_85_out, M[2]);
  not not_86 (not_86_out, M[1]);
  not not_87 (not_87_out, M[0]);
  not not_88 (not_88_out, Funct[5]);
  not not_89 (not_89_out, Funct[4]);
  not not_90 (not_90_out, Funct[3]);
  not not_91 (not_91_out, Funct[2]);
  not not_92 (not_92_out, Funct[0]);
  not not_93 (not_93_out, Funct[5]);
  not not_94 (not_94_out, Funct[4]);
  not not_95 (not_95_out, Funct[3]);
  not not_96 (not_96_out, Funct[2]);
  not not_97 (not_97_out, OP[5]);
  not not_98 (not_98_out, OP[4]);
  not not_99 (not_99_out, OP[1]);
  not not_100 (not_100_out, OP[4]);
  not not_101 (not_101_out, OP[2]);
  not not_102 (not_102_out, OP[5]);
  not not_103 (not_103_out, OP[4]);
  not not_104 (not_104_out, OP[3]);
  not not_105 (not_105_out, OP[2]);
  not not_106 (not_106_out, OP[1]);
  not not_107 (not_107_out, OP[0]);
  not not_108 (not_108_out, Funct[5]);
  not not_109 (not_109_out, Funct[4]);
  not not_110 (not_110_out, Funct[1]);
  not not_111 (not_111_out, Funct[0]);
  and and_14 (and_14_out, not_63_out, not_64_out, not_65_out, not_66_out, not_67_out);
  and and_15 (and_15_out, not_68_out, not_69_out, not_70_out, OP[1], OP[0]);
  and and_16 (and_16_out, not_71_out, not_72_out, OP[3], not_73_out, not_74_out);
  and and_17 (and_17_out, not_75_out, not_76_out, OP[3], not_77_out);
  and and_18 (and_18_out, not_78_out, OP[4], not_79_out, not_80_out, not_81_out, not_82_out, not_83_out, not_84_out, not_85_out, not_86_out, not_87_out);
  and and_19 (and_19_out, not_88_out, not_89_out, not_90_out, not_91_out, not_92_out);
  and and_20 (and_20_out, not_93_out, not_94_out, not_95_out, not_96_out, Funct[1]);
  and and_21 (and_21_out, not_97_out, not_98_out, OP[3], not_99_out);
  and and_22 (and_22_out, OP[5], not_100_out, not_101_out, OP[1], OP[0]);
  and and_23 (SYSCALL, not_102_out, not_103_out, not_104_out, not_105_out, not_106_out, not_107_out, not_108_out, not_109_out, Funct[3], Funct[2], not_110_out, not_111_out);
  or or_2 (or_2_out, and_14_out, and_15_out, and_16_out, and_17_out);
  and and_24 (ALUSrcX, RegDst, or_3_out);
  or or_3 (or_3_out, and_19_out, and_20_out);
  or or_4 (ALUSrcY, and_21_out, and_22_out);
  or or_5 (RW, or_2_out, and_18_out);

  // Other names for the same wires on the sheet: _1 = RegDst; MemtoReg = M2R; MemWrite = MW; RegWrite = RW;
  //   SYSC = SYSCALL

  // Notes on the sheet:
  //   输入引脚
  //   输出引脚
endmodule

module ALU_Control (
  input  OP5,
  input  OP4,
  input  OP3,
  input  OP2,
  input  OP1,
  input  OP0,
  input  Funct5,
  input  Funct4,
  input  Funct3,
  input  Funct2,
  input  Funct1,
  input  Funct0,
  output Sel3,
  output Sel2,
  output Sel1,
  output Sel0
);

  wire and_1_out, and_2_out, and_3_out, and_4_out, and_5_out, and_6_out, and_7_out, and_8_out, and_9_out,
       and_10_out, and_11_out, and_12_out, and_13_out, and_14_out, and_15_out, and_16_out, and_17_out,
       and_18_out, and_19_out, and_20_out, and_21_out, and_22_out, and_23_out, and_24_out, and_25_out,
       and_26_out, and_27_out, and_28_out, and_29_out, and_30_out, and_31_out, and_32_out, and_33_out,
       and_34_out, and_35_out, and_36_out, not_1_out, not_2_out, not_3_out, not_4_out, not_5_out, not_6_out,
       not_7_out, not_8_out, not_9_out, not_10_out, not_11_out, not_12_out, not_13_out, not_14_out,
       not_15_out, not_16_out, not_17_out, not_18_out, not_19_out, not_20_out, not_21_out, not_22_out,
       not_23_out, not_24_out, not_25_out, not_26_out, not_27_out, not_28_out, not_29_out, not_30_out,
       not_31_out, not_32_out, not_33_out, not_34_out, not_35_out, not_36_out, not_37_out, not_38_out,
       not_39_out, not_40_out, not_41_out, not_42_out, not_43_out, not_44_out, not_45_out, not_46_out,
       not_47_out, not_48_out, not_49_out, not_50_out, not_51_out, not_52_out, not_53_out, not_54_out,
       not_55_out, not_56_out, not_57_out, not_58_out, not_59_out, not_60_out, not_61_out, not_62_out,
       not_63_out, not_64_out, not_65_out, not_66_out, not_67_out, not_68_out, not_69_out, not_70_out,
       not_71_out, not_72_out, not_73_out, not_74_out, not_75_out, not_76_out, not_77_out, not_78_out,
       not_79_out, not_80_out, not_81_out, not_82_out, not_83_out, not_84_out, not_85_out, not_86_out,
       not_87_out, not_88_out, not_89_out, not_90_out, not_91_out, not_92_out, not_93_out, not_94_out,
       not_95_out, not_96_out, not_97_out, not_98_out, not_99_out, not_100_out, not_101_out, not_102_out,
       not_103_out, not_104_out, not_105_out, not_106_out, not_107_out, not_108_out, not_109_out,
       not_110_out, not_111_out, not_112_out, not_113_out, not_114_out, not_115_out, not_116_out,
       not_117_out, not_118_out, not_119_out, not_120_out, not_121_out, not_122_out, not_123_out,
       not_124_out, not_125_out, not_126_out, not_127_out, not_128_out, not_129_out, not_130_out,
       not_131_out, not_132_out, not_133_out, not_134_out, not_135_out, not_136_out, not_137_out,
       not_138_out, not_139_out, not_140_out, not_141_out, not_142_out, not_143_out, not_144_out,
       not_145_out, not_146_out, not_147_out, not_148_out, not_149_out, not_150_out, not_151_out,
       not_152_out, not_153_out, not_154_out, not_155_out, not_156_out, not_157_out, not_158_out,
       not_159_out, not_160_out, not_161_out, not_162_out, not_163_out, not_164_out, not_165_out,
       not_166_out, not_167_out, not_168_out, not_169_out, not_170_out, not_171_out, not_172_out,
       not_173_out, not_174_out, not_175_out, not_176_out, not_177_out, not_178_out, not_179_out,
       not_180_out, not_181_out, not_182_out, not_183_out, not_184_out, not_185_out, not_186_out,
       not_187_out, not_188_out, not_189_out, not_190_out, not_191_out, not_192_out, not_193_out,
       not_194_out, not_195_out, not_196_out, not_197_out, not_198_out, not_199_out, not_200_out,
       not_201_out, not_202_out, not_203_out, not_204_out, not_205_out, not_206_out, not_207_out,
       not_208_out, not_209_out, not_210_out, not_211_out, not_212_out, not_213_out, not_214_out,
       not_215_out, not_216_out, not_217_out, not_218_out, not_219_out, not_220_out, not_221_out,
       not_222_out, not_223_out, not_224_out, not_225_out, not_226_out, not_227_out, not_228_out,
       not_229_out, not_230_out, not_231_out, not_232_out, not_233_out, not_234_out, not_235_out,
       not_236_out, not_237_out, not_238_out, not_239_out, not_240_out, not_241_out, not_242_out,
       not_243_out, not_244_out, not_245_out, not_246_out, not_247_out, not_248_out, not_249_out,
       not_250_out, not_251_out, not_252_out, not_253_out, not_254_out, not_255_out;

  not not_1 (not_1_out, OP5);
  not not_2 (not_2_out, OP4);
  not not_3 (not_3_out, OP3);
  not not_4 (not_4_out, OP2);
  not not_5 (not_5_out, OP1);
  not not_6 (not_6_out, OP0);
  not not_7 (not_7_out, Funct4);
  not not_8 (not_8_out, Funct3);
  not not_9 (not_9_out, OP5);
  not not_10 (not_10_out, OP4);
  not not_11 (not_11_out, OP3);
  not not_12 (not_12_out, OP2);
  not not_13 (not_13_out, OP1);
  not not_14 (not_14_out, OP0);
  not not_15 (not_15_out, Funct4);
  not not_16 (not_16_out, Funct2);
  not not_17 (not_17_out, OP5);
  not not_18 (not_18_out, OP4);
  not not_19 (not_19_out, OP2);
  not not_20 (not_20_out, OP0);
  not not_21 (not_21_out, OP5);
  not not_22 (not_22_out, OP4);
  not not_23 (not_23_out, OP1);
  not not_24 (not_24_out, OP5);
  not not_25 (not_25_out, OP4);
  not not_26 (not_26_out, OP3);
  not not_27 (not_27_out, OP2);
  not not_28 (not_28_out, OP1);
  not not_29 (not_29_out, OP0);
  not not_30 (not_30_out, Funct4);
  not not_31 (not_31_out, Funct3);
  not not_32 (not_32_out, Funct2);
  not not_33 (not_33_out, Funct1);
  not not_34 (not_34_out, Funct0);
  not not_35 (not_35_out, OP5);
  not not_36 (not_36_out, OP4);
  not not_37 (not_37_out, OP2);
  not not_38 (not_38_out, OP1);
  not not_39 (not_39_out, OP0);
  not not_40 (not_40_out, OP5);
  not not_41 (not_41_out, OP4);
  not not_42 (not_42_out, OP2);
  not not_43 (not_43_out, OP1);
  not not_44 (not_44_out, OP5);
  not not_45 (not_45_out, OP4);
  not not_46 (not_46_out, OP3);
  not not_47 (not_47_out, OP2);
  not not_48 (not_48_out, OP1);
  not not_49 (not_49_out, OP0);
  not not_50 (not_50_out, Funct4);
  not not_51 (not_51_out, Funct3);
  not not_52 (not_52_out, Funct2);
  not not_53 (not_53_out, Funct1);
  not not_54 (not_54_out, OP5);
  not not_55 (not_55_out, OP4);
  not not_56 (not_56_out, OP3);
  not not_57 (not_57_out, OP2);
  not not_58 (not_58_out, OP1);
  not not_59 (not_59_out, OP0);
  not not_60 (not_60_out, Funct4);
  not not_61 (not_61_out, Funct3);
  not not_62 (not_62_out, Funct1);
  not not_63 (not_63_out, Funct0);
  not not_64 (not_64_out, OP5);
  not not_65 (not_65_out, OP4);
  not not_66 (not_66_out, OP1);
  not not_67 (not_67_out, OP0);
  not not_68 (not_68_out, OP5);
  not not_69 (not_69_out, OP4);
  not not_70 (not_70_out, OP3);
  not not_71 (not_71_out, OP2);
  not not_72 (not_72_out, OP1);
  not not_73 (not_73_out, OP0);
  not not_74 (not_74_out, Funct4);
  not not_75 (not_75_out, Funct3);
  not not_76 (not_76_out, Funct2);
  not not_77 (not_77_out, Funct0);
  not not_78 (not_78_out, OP5);
  not not_79 (not_79_out, OP4);
  not not_80 (not_80_out, OP3);
  not not_81 (not_81_out, OP2);
  not not_82 (not_82_out, OP1);
  not not_83 (not_83_out, OP0);
  not not_84 (not_84_out, Funct5);
  not not_85 (not_85_out, Funct2);
  not not_86 (not_86_out, OP4);
  not not_87 (not_87_out, OP3);
  not not_88 (not_88_out, OP2);
  not not_89 (not_89_out, OP4);
  not not_90 (not_90_out, OP2);
  not not_91 (not_91_out, OP5);
  not not_92 (not_92_out, OP4);
  not not_93 (not_93_out, OP3);
  not not_94 (not_94_out, OP2);
  not not_95 (not_95_out, OP1);
  not not_96 (not_96_out, OP0);
  not not_97 (not_97_out, Funct4);
  not not_98 (not_98_out, Funct3);
  not not_99 (not_99_out, Funct1);
  not not_100 (not_100_out, Funct0);
  not not_101 (not_101_out, OP5);
  not not_102 (not_102_out, OP4);
  not not_103 (not_103_out, OP1);
  not not_104 (not_104_out, OP0);
  not not_105 (not_105_out, OP5);
  not not_106 (not_106_out, OP4);
  not not_107 (not_107_out, OP3);
  not not_108 (not_108_out, OP2);
  not not_109 (not_109_out, OP1);
  not not_110 (not_110_out, OP0);
  not not_111 (not_111_out, Funct5);
  not not_112 (not_112_out, Funct4);
  not not_113 (not_113_out, Funct3);
  not not_114 (not_114_out, Funct2);
  not not_115 (not_115_out, Funct0);
  not not_116 (not_116_out, OP5);
  not not_117 (not_117_out, OP4);
  not not_118 (not_118_out, OP3);
  not not_119 (not_119_out, OP2);
  not not_120 (not_120_out, OP1);
  not not_121 (not_121_out, OP0);
  not not_122 (not_122_out, Funct4);
  not not_123 (not_123_out, Funct3);
  not not_124 (not_124_out, Funct2);
  not not_125 (not_125_out, Funct0);
  not not_126 (not_126_out, OP5);
  not not_127 (not_127_out, OP4);
  not not_128 (not_128_out, OP3);
  not not_129 (not_129_out, OP2);
  not not_130 (not_130_out, OP1);
  not not_131 (not_131_out, OP0);
  not not_132 (not_132_out, Funct5);
  not not_133 (not_133_out, Funct2);
  not not_134 (not_134_out, Funct1);
  not not_135 (not_135_out, Funct0);
  not not_136 (not_136_out, OP5);
  not not_137 (not_137_out, OP4);
  not not_138 (not_138_out, OP3);
  not not_139 (not_139_out, OP2);
  not not_140 (not_140_out, OP1);
  not not_141 (not_141_out, OP0);
  not not_142 (not_142_out, Funct4);
  not not_143 (not_143_out, Funct2);
  not not_144 (not_144_out, Funct0);
  not not_145 (not_145_out, OP5);
  not not_146 (not_146_out, OP4);
  not not_147 (not_147_out, OP3);
  not not_148 (not_148_out, OP2);
  not not_149 (not_149_out, OP0);
  not not_150 (not_150_out, OP5);
  not not_151 (not_151_out, OP4);
  not not_152 (not_152_out, OP3);
  not not_153 (not_153_out, OP2);
  not not_154 (not_154_out, OP1);
  not not_155 (not_155_out, OP0);
  not not_156 (not_156_out, Funct4);
  not not_157 (not_157_out, Funct2);
  not not_158 (not_158_out, OP5);
  not not_159 (not_159_out, OP4);
  not not_160 (not_160_out, OP3);
  not not_161 (not_161_out, OP2);
  not not_162 (not_162_out, OP1);
  not not_163 (not_163_out, OP0);
  not not_164 (not_164_out, Funct4);
  not not_165 (not_165_out, Funct3);
  not not_166 (not_166_out, OP5);
  not not_167 (not_167_out, OP4);
  not not_168 (not_168_out, OP3);
  not not_169 (not_169_out, OP2);
  not not_170 (not_170_out, OP1);
  not not_171 (not_171_out, OP0);
  not not_172 (not_172_out, Funct4);
  not not_173 (not_173_out, Funct3);
  not not_174 (not_174_out, Funct2);
  not not_175 (not_175_out, Funct1);
  not not_176 (not_176_out, Funct0);
  not not_177 (not_177_out, OP5);
  not not_178 (not_178_out, OP4);
  not not_179 (not_179_out, OP2);
  not not_180 (not_180_out, OP1);
  not not_181 (not_181_out, OP0);
  not not_182 (not_182_out, OP5);
  not not_183 (not_183_out, OP4);
  not not_184 (not_184_out, OP2);
  not not_185 (not_185_out, OP1);
  not not_186 (not_186_out, OP5);
  not not_187 (not_187_out, OP4);
  not not_188 (not_188_out, OP3);
  not not_189 (not_189_out, OP2);
  not not_190 (not_190_out, OP1);
  not not_191 (not_191_out, OP0);
  not not_192 (not_192_out, Funct4);
  not not_193 (not_193_out, Funct3);
  not not_194 (not_194_out, Funct2);
  not not_195 (not_195_out, Funct1);
  not not_196 (not_196_out, OP5);
  not not_197 (not_197_out, OP4);
  not not_198 (not_198_out, OP3);
  not not_199 (not_199_out, OP2);
  not not_200 (not_200_out, OP1);
  not not_201 (not_201_out, OP0);
  not not_202 (not_202_out, Funct4);
  not not_203 (not_203_out, Funct3);
  not not_204 (not_204_out, Funct1);
  not not_205 (not_205_out, Funct0);
  not not_206 (not_206_out, OP5);
  not not_207 (not_207_out, OP4);
  not not_208 (not_208_out, OP1);
  not not_209 (not_209_out, OP0);
  not not_210 (not_210_out, OP5);
  not not_211 (not_211_out, OP4);
  not not_212 (not_212_out, OP3);
  not not_213 (not_213_out, OP2);
  not not_214 (not_214_out, OP1);
  not not_215 (not_215_out, OP0);
  not not_216 (not_216_out, Funct5);
  not not_217 (not_217_out, Funct4);
  not not_218 (not_218_out, Funct3);
  not not_219 (not_219_out, Funct2);
  not not_220 (not_220_out, OP5);
  not not_221 (not_221_out, OP4);
  not not_222 (not_222_out, OP3);
  not not_223 (not_223_out, OP2);
  not not_224 (not_224_out, OP1);
  not not_225 (not_225_out, OP0);
  not not_226 (not_226_out, Funct5);
  not not_227 (not_227_out, Funct2);
  not not_228 (not_228_out, Funct1);
  not not_229 (not_229_out, Funct0);
  not not_230 (not_230_out, OP5);
  not not_231 (not_231_out, OP4);
  not not_232 (not_232_out, OP3);
  not not_233 (not_233_out, OP2);
  not not_234 (not_234_out, OP1);
  not not_235 (not_235_out, OP0);
  not not_236 (not_236_out, Funct4);
  not not_237 (not_237_out, Funct2);
  not not_238 (not_238_out, Funct0);
  not not_239 (not_239_out, OP5);
  not not_240 (not_240_out, OP4);
  not not_241 (not_241_out, OP2);
  not not_242 (not_242_out, OP0);
  not not_243 (not_243_out, OP5);
  not not_244 (not_244_out, OP4);
  not not_245 (not_245_out, OP3);
  not not_246 (not_246_out, OP2);
  not not_247 (not_247_out, OP1);
  not not_248 (not_248_out, OP0);
  not not_249 (not_249_out, Funct4);
  not not_250 (not_250_out, Funct2);
  not not_251 (not_251_out, OP4);
  not not_252 (not_252_out, OP3);
  not not_253 (not_253_out, OP2);
  not not_254 (not_254_out, OP4);
  not not_255 (not_255_out, OP2);
  and and_1 (and_1_out, not_1_out, not_2_out, not_3_out, not_4_out, not_5_out, not_6_out, Funct5, not_7_out, not_8_out, Funct2, Funct0);
  and and_2 (and_2_out, not_9_out, not_10_out, not_11_out, not_12_out, not_13_out, not_14_out, Funct5, not_15_out, Funct3, not_16_out, Funct1);
  and and_3 (and_3_out, not_17_out, not_18_out, OP3, not_19_out, OP1, not_20_out);
  and and_4 (and_4_out, not_21_out, not_22_out, OP3, OP2, not_23_out, OP0);
  and and_5 (and_5_out, not_24_out, not_25_out, not_26_out, not_27_out, not_28_out, not_29_out, Funct5, not_30_out, not_31_out, not_32_out, not_33_out, not_34_out);
  and and_6 (and_6_out, not_35_out, not_36_out, OP3, not_37_out, not_38_out, not_39_out);
  and and_7 (and_7_out, not_40_out, not_41_out, OP3, not_42_out, not_43_out, OP0);
  and and_8 (and_8_out, not_44_out, not_45_out, not_46_out, not_47_out, not_48_out, not_49_out, Funct5, not_50_out, not_51_out, not_52_out, not_53_out, Funct0);
  and and_9 (and_9_out, not_54_out, not_55_out, not_56_out, not_57_out, not_58_out, not_59_out, Funct5, not_60_out, not_61_out, Funct2, not_62_out, not_63_out);
  and and_10 (and_10_out, not_64_out, not_65_out, OP3, OP2, not_66_out, not_67_out);
  and and_11 (and_11_out, not_68_out, not_69_out, not_70_out, not_71_out, not_72_out, not_73_out, Funct5, not_74_out, not_75_out, not_76_out, Funct1, not_77_out);
  and and_12 (and_12_out, not_78_out, not_79_out, not_80_out, not_81_out, not_82_out, not_83_out, not_84_out, Funct4, Funct3, not_85_out, Funct1, Funct0);
  and and_13 (and_13_out, OP5, not_86_out, not_87_out, not_88_out, OP1, OP0);
  and and_14 (and_14_out, OP5, not_89_out, OP3, not_90_out, OP1, OP0);
  and and_15 (and_15_out, not_91_out, not_92_out, not_93_out, not_94_out, not_95_out, not_96_out, Funct5, not_97_out, not_98_out, Funct2, not_99_out, not_100_out);
  and and_16 (and_16_out, not_101_out, not_102_out, OP3, OP2, not_103_out, not_104_out);
  and and_17 (and_17_out, not_105_out, not_106_out, not_107_out, not_108_out, not_109_out, not_110_out, not_111_out, not_112_out, not_113_out, not_114_out, Funct1, not_115_out);
  and and_18 (and_18_out, not_116_out, not_117_out, not_118_out, not_119_out, not_120_out, not_121_out, Funct5, not_122_out, not_123_out, not_124_out, Funct1, not_125_out);
  and and_19 (and_19_out, not_126_out, not_127_out, not_128_out, not_129_out, not_130_out, not_131_out, not_132_out, Funct4, Funct3, not_133_out, not_134_out, not_135_out);
  and and_20 (and_20_out, not_136_out, not_137_out, not_138_out, not_139_out, not_140_out, not_141_out, Funct5, not_142_out, Funct3, not_143_out, Funct1, not_144_out);
  and and_21 (and_21_out, not_145_out, not_146_out, not_147_out, not_148_out, OP1, not_149_out);
  and and_22 (and_22_out, not_150_out, not_151_out, not_152_out, not_153_out, not_154_out, not_155_out, Funct5, not_156_out, Funct3, not_157_out, Funct1, Funct0);
  and and_23 (and_23_out, not_158_out, not_159_out, not_160_out, not_161_out, not_162_out, not_163_out, Funct5, not_164_out, not_165_out, Funct2, Funct1, Funct0);
  and and_24 (and_24_out, not_166_out, not_167_out, not_168_out, not_169_out, not_170_out, not_171_out, Funct5, not_172_out, not_173_out, not_174_out, not_175_out, not_176_out);
  and and_25 (and_25_out, not_177_out, not_178_out, OP3, not_179_out, not_180_out, not_181_out);
  and and_26 (and_26_out, not_182_out, not_183_out, OP3, not_184_out, not_185_out, OP0);
  and and_27 (and_27_out, not_186_out, not_187_out, not_188_out, not_189_out, not_190_out, not_191_out, Funct5, not_192_out, not_193_out, not_194_out, not_195_out, Funct0);
  and and_28 (and_28_out, not_196_out, not_197_out, not_198_out, not_199_out, not_200_out, not_201_out, Funct5, not_202_out, not_203_out, Funct2, not_204_out, not_205_out);
  and and_29 (and_29_out, not_206_out, not_207_out, OP3, OP2, not_208_out, not_209_out);
  and and_30 (and_30_out, not_210_out, not_211_out, not_212_out, not_213_out, not_214_out, not_215_out, not_216_out, not_217_out, not_218_out, not_219_out, Funct1, Funct0);
  and and_31 (and_31_out, not_220_out, not_221_out, not_222_out, not_223_out, not_224_out, not_225_out, not_226_out, Funct4, Funct3, not_227_out, not_228_out, not_229_out);
  and and_32 (and_32_out, not_230_out, not_231_out, not_232_out, not_233_out, not_234_out, not_235_out, Funct5, not_236_out, Funct3, not_237_out, Funct1, not_238_out);
  and and_33 (and_33_out, not_239_out, not_240_out, OP3, not_241_out, OP1, not_242_out);
  and and_34 (and_34_out, not_243_out, not_244_out, not_245_out, not_246_out, not_247_out, not_248_out, Funct5, not_249_out, Funct3, not_250_out, Funct1, Funct0);
  and and_35 (and_35_out, OP5, not_251_out, not_252_out, not_253_out, OP1, OP0);
  and and_36 (and_36_out, OP5, not_254_out, OP3, not_255_out, OP1, OP0);
  or or_1 (Sel3, and_1_out, and_2_out, and_3_out, and_4_out);
  or or_2 (Sel2, and_5_out, and_6_out, and_7_out, and_8_out, and_9_out, and_10_out, and_11_out, and_12_out, and_13_out, and_14_out);
  or or_3 (Sel1, and_15_out, and_16_out, and_17_out, and_18_out, and_19_out, and_20_out, and_21_out, and_22_out, and_23_out);
  or or_4 (Sel0, and_24_out, and_25_out, and_26_out, and_27_out, and_28_out, and_29_out, and_30_out, and_31_out, and_32_out, and_33_out, and_34_out, and_35_out, and_36_out);
endmodule

module CP0 (
  input  [4:0] in_1,
  input  [31:0] in_2,
  input  [4:0] in_3,
  input  in_4,
  input  in_5,
  input  in_6,
  input  in_7,
  output [31:0] out_8,
  output [31:0] out_9,
  output out_10,
  output out_11
);

  wire and_1_out, and_2_out, IE, or_1_out, W1, W2, W3, xor_1_out, xor_2_out;
  wire [31:0] Cause_q, EPC_q;
  wire [31:1] Status_q;

  or or_1 (or_1_out, out_11, W1);
  Register #(.width(32)) Status (.D(in_2), .en(or_1_out), .Q({Status_q, IE}), .clk(in_6), .clr(out_11));
  Register #(.width(32)) Cause (.D(in_2), .en(W2), .Q(Cause_q), .clk(in_6));  // open: clr
  Multiplexer #(.select(5), .width(32), .enable("false")) multiplexer_1 (
    .in0({32{1'b0}}), .in1({32{1'b0}}), .in2({32{1'b0}}), .in3({32{1'b0}}), .in4({32{1'b0}}),
    .in5({32{1'b0}}), .in6({32{1'b0}}), .in7({32{1'b0}}), .in8({32{1'b0}}), .in9({32{1'b0}}),
    .in10({32{1'b0}}), .in11({32{1'b0}}), .in12({Status_q, IE}), .in13(Cause_q), .in14(EPC_q),
    .in15({32{1'b0}}), .in16({32{1'b0}}), .in17({32{1'b0}}), .in18({32{1'b0}}), .in19({32{1'b0}}),
    .in20({32{1'b0}}), .in21({32{1'b0}}), .in22({32{1'b0}}), .in23({32{1'b0}}), .in24({32{1'b0}}),
    .in25({32{1'b0}}), .in26({32{1'b0}}), .in27({32{1'b0}}), .in28({32{1'b0}}), .in29({32{1'b0}}),
    .in30({32{1'b0}}), .in31({32{1'b0}}), .out(out_8), .sel(in_3));
  Demultiplexer #(.select(5), .enable("false")) demultiplexer_1 (
    .out12(W1), .out13(W2), .out14(W3), .in(in_4), .sel(in_1));  // open: out0, out1, out2, out3, out4, out5, out6, out7, out8, out9, out10, out11, out15, out16, out17, out18, out19, out20, out21, out22, out23, out24, out25, out26, out27, out28, out29, out30, out31
  Register #(.width(32)) EPC (.D(in_2), .en(W3), .Q(EPC_q), .clk(in_6));  // open: clr
  and and_1 (and_1_out, in_5, IE);
  xor xor_1 (xor_1_out, in_7, and_1_out);
  xor xor_2 (xor_2_out, in_7, and_2_out);
  and and_2 (and_2_out, in_5, IE);
  Counter #(.width(30), .max('h3fffffff)) counter_1 (
    .load(in_7), .count(xor_1_out), .Q(out_9[31:2]), .clk(in_6));  // open: D, carry, clr
  Register #(.width(1)) register_1 (.D(out_11), .Q(out_10), .clk(in_6));  // open: en, clr
  Register #(.width(1)) IR (.D(in_5), .en(IE), .Q(out_11), .clk(in_6), .clr(out_10));
  Counter #(.width(30), .max('h3fffffff)) counter_2 (
    .load(in_7), .count(xor_2_out), .Q(out_9[31:2]), .clk(in_6));  // open: D, carry, clr

  assign out_9[1:0] = 2'b00;

  // Other names for the same wires on the sheet: Addr[4:0] = in_1; CLK = in_6; Din[31:0] = in_2; Dout[31:0] = out_8;
  //   ERET = in_7; Int = out_11; IR = in_5; ISR = out_10; PCAddr[31:2] = out_9[31:2]; R_num[4:0] = in_3; WE = in_4

  // Notes on the sheet:
  //   输入
  //   输出
endmodule

module Instruction_Counter (
  input  [5:0] in_1,
  input  in_2,
  input  Pause,
  input  in_4,
  input  JRD,
  output [31:0] out_6,
  output [31:0] out_7,
  output [31:0] out_8,
  output [31:0] out_9,
  output [31:0] Bubble
);

  wire and_1_out, and_2_out, and_3_out, and_4_out, and_5_out, and_6_out, not_1_out, not_2_out, not_3_out,
       not_4_out, not_5_out, not_6_out, not_7_out, not_8_out, not_9_out, not_10_out, not_11_out, not_12_out,
       not_13_out, not_14_out, not_15_out, not_16_out, not_17_out, not_18_out, not_19_out, not_20_out,
       not_21_out, not_22_out, not_23_out, or_1_out, or_2_out;
  wire [31:0] adder_1_out, adder_2_out, counter_2_q, counter_3_q;

  not not_1 (not_1_out, Pause);
  Counter #(.width(32), .max('hffffffff)) counter_1 (
    .count(not_1_out), .Q(Bubble), .clk(in_2));  // open: load, D, carry, clr
  // Probe on Bubble
  not not_2 (not_2_out, in_1[5]);
  not not_3 (not_3_out, in_1[4]);
  not not_4 (not_4_out, in_1[3]);
  not not_5 (not_5_out, in_1[2]);
  not not_6 (not_6_out, in_1[1]);
  not not_7 (not_7_out, in_1[0]);
  not not_8 (not_8_out, in_1[5]);
  not not_9 (not_9_out, in_1[4]);
  not not_10 (not_10_out, in_1[1]);
  not not_11 (not_11_out, in_1[5]);
  not not_12 (not_12_out, in_1[4]);
  not not_13 (not_13_out, in_1[2]);
  not not_14 (not_14_out, in_1[0]);
  not not_15 (not_15_out, in_1[5]);
  not not_16 (not_16_out, in_1[4]);
  not not_17 (not_17_out, in_1[1]);
  not not_18 (not_18_out, in_1[4]);
  not not_19 (not_19_out, in_1[2]);
  not not_20 (not_20_out, in_1[5]);
  not not_21 (not_21_out, in_1[4]);
  not not_22 (not_22_out, in_1[3]);
  not not_23 (not_23_out, in_1[2]);
  and and_1 (and_1_out, not_2_out, not_3_out, not_4_out, not_5_out, not_6_out, not_7_out);
  and and_2 (and_2_out, not_8_out, not_9_out, in_1[2], not_10_out);
  and and_3 (and_3_out, not_11_out, not_12_out, in_1[3], not_13_out, not_14_out);
  and and_4 (and_4_out, not_15_out, not_16_out, in_1[3], not_17_out);
  and and_5 (and_5_out, in_1[5], not_18_out, not_19_out, in_1[1], in_1[0]);
  and and_6 (and_6_out, not_20_out, not_21_out, not_22_out, not_23_out, in_1[1]);
  Counter #(.width(32), .max('hffffffff)) counter_2 (.Q(counter_2_q), .clk(in_2));  // open: load, D, count, carry, clr
  Counter #(.width(32), .max('hffffffff)) counter_3 (
    .count(and_1_out), .Q(counter_3_q), .clk(in_2));  // open: load, D, carry, clr
  Counter #(.width(32), .max('hffffffff)) counter_4 (
    .count(or_1_out), .Q(out_8), .clk(in_2));  // open: load, D, carry, clr
  or or_1 (or_1_out, and_2_out, and_3_out, and_4_out, and_5_out);
  or or_2 (or_2_out, and_6_out, JRD);
  Counter #(.width(32), .max('hffffffff)) counter_5 (
    .count(or_2_out), .Q(out_9), .clk(in_2));  // open: load, D, carry, clr
  Adder #(.width(32)) adder_1 (.a(counter_2_q), .b(32'h1), .out(adder_1_out));  // open: cin, cout
  Multiplexer #(.width(32), .enable("false")) multiplexer_1 (
    .in0(adder_1_out), .in1(counter_2_q), .out(out_6), .sel(in_4));
  Adder #(.width(32)) adder_2 (.a(counter_3_q), .b(32'h1), .out(adder_2_out));  // open: cin, cout
  Multiplexer #(.width(32), .enable("false")) multiplexer_2 (
    .in0(adder_2_out), .in1(counter_3_q), .out(out_7), .sel(in_4));
  // Probe on counter_2_q
  // Probe on counter_3_q
  // Probe on out_8
  // Probe on out_9

  // Other names for the same wires on the sheet: CLK = in_2; Halt = in_4; I[31:0] = out_8; J[31:0] = out_9;
  //   OP[5:0] = in_1; R[31:0] = out_7; TOTAL[31:0] = out_6
endmodule

module IF_ID (
  input  [31:0] PC,
  input  [31:0] IR,
  input  CLK,
  input  Clear,
  input  Pause,
  output [31:0] PCout,
  output [31:0] IRout
);

  wire [31:0] multiplexer_1_out, multiplexer_2_out;

  Multiplexer #(.width(32), .enable("false")) multiplexer_1 (
    .in0(PC), .in1({32{1'b0}}), .out(multiplexer_1_out), .sel(Clear));
  Register #(.width(32)) register_1 (.D(multiplexer_1_out), .en(Pause), .Q(PCout), .clk(CLK));  // open: clr
  Multiplexer #(.width(32), .enable("false")) multiplexer_2 (
    .in0(IR), .in1({32{1'b0}}), .out(multiplexer_2_out), .sel(Clear));
  Register #(.width(32)) register_2 (.D(multiplexer_2_out), .en(Pause), .Q(IRout), .clk(CLK));  // open: clr
endmodule

module ID_EX (
  input  [31:0] PC,
  input  [31:0] R1,
  input  [31:0] R2,
  input  [4:0] rd,
  input  [4:0] rs,
  input  [31:0] IMM1,
  input  [31:0] IMM2,
  input  [31:0] IMM3,
  input  [4:0] rt,
  input  CLK,
  input  Clear,
  input  RD_2,
  input  Branch,
  input  JUMP,
  input  M2R,
  input  MW,
  input  C2R,
  input  CW,
  input  ERET,
  input  SIGN,
  input  ALUSrcX,
  input  ALUSrcY,
  input  RW,
  input  JR,
  input  JAL,
  input  SYS,
  input  [3:0] ALUop,
  input  [31:0] IR,
  input  JudgeB,
  output [31:0] PC_4,
  output [31:0] PCout,
  output [31:0] R1out,
  output [31:0] R2out,
  output [4:0] rd_3,
  output [31:0] IMM1_2,
  output [31:0] IMM2_2,
  output [31:0] IMM3_2,
  output [4:0] rt_2,
  output RegDst,
  output Branch_2,
  output Jump_2,
  output M2R_2,
  output MW_2,
  output C2R_2,
  output CW_2,
  output ERET_2,
  output SIGN_2,
  output ALUSrcX_2,
  output ALUSrcY_2,
  output RW_2,
  output JR_2,
  output JAL_2,
  output Syscall,
  output [3:0] ALUop_2,
  output [4:0] rs_2,
  output [31:0] IR_2,
  output JudgeB_2
);

  wire multiplexer_1_out, multiplexer_2_out, multiplexer_3_out, multiplexer_4_out, multiplexer_5_out,
       multiplexer_6_out, multiplexer_7_out, multiplexer_8_out, multiplexer_9_out, multiplexer_11_out,
       multiplexer_12_out, multiplexer_13_out, multiplexer_14_out, multiplexer_15_out, multiplexer_16_out,
       multiplexer_17_out;
  wire [31:0] multiplexer_10_out;

  Register #(.width(32)) register_1 (.D(PC), .Q(PC_4), .clk(CLK));  // open: en, clr
  Register #(.width(32)) register_2 (.D(IMM1), .Q(IMM1_2), .clk(CLK));  // open: en, clr
  Multiplexer #(.enable("false")) multiplexer_1 (.in0(RD_2), .in1(1'b0), .out(multiplexer_1_out), .sel(Clear));
  Multiplexer #(.enable("false")) multiplexer_2 (.in0(MW), .in1(1'b0), .out(multiplexer_2_out), .sel(Clear));
  Multiplexer #(.enable("false")) multiplexer_3 (.in0(SIGN), .in1(1'b0), .out(multiplexer_3_out), .sel(Clear));
  Multiplexer #(.enable("false")) multiplexer_4 (.in0(JR), .in1(1'b0), .out(multiplexer_4_out), .sel(Clear));
  Multiplexer #(.enable("false")) multiplexer_5 (.in0(JudgeB), .in1(1'b0), .out(multiplexer_5_out), .sel(Clear));
  Register #(.width(1)) register_3 (.D(multiplexer_1_out), .Q(RegDst), .clk(CLK));  // open: en, clr
  Register #(.width(1)) register_4 (.D(multiplexer_2_out), .Q(MW_2), .clk(CLK));  // open: en, clr
  Register #(.width(1)) register_5 (.D(multiplexer_3_out), .Q(SIGN_2), .clk(CLK));  // open: en, clr
  Register #(.width(1)) register_6 (.D(multiplexer_4_out), .Q(JR_2), .clk(CLK));  // open: en, clr
  Register #(.width(1)) register_7 (.D(multiplexer_5_out), .Q(JudgeB_2), .clk(CLK));  // open: en, clr
  Register #(.width(32)) register_8 (.D(R1), .Q(R1out), .clk(CLK));  // open: en, clr
  Register #(.width(32)) register_9 (.D(IMM2), .Q(IMM2_2), .clk(CLK));  // open: en, clr
  Register #(.width(1)) register_10 (.D(multiplexer_6_out), .Q(Branch_2), .clk(CLK));  // open: en, clr
  Multiplexer #(.enable("false")) multiplexer_6 (.in0(Branch), .in1(1'b0), .out(multiplexer_6_out), .sel(Clear));
  Register #(.width(1)) register_11 (.D(multiplexer_7_out), .Q(C2R_2), .clk(CLK));  // open: en, clr
  Multiplexer #(.enable("false")) multiplexer_7 (.in0(C2R), .in1(1'b0), .out(multiplexer_7_out), .sel(Clear));
  Multiplexer #(.enable("false")) multiplexer_8 (.in0(ALUSrcX), .in1(1'b0), .out(multiplexer_8_out), .sel(Clear));
  Register #(.width(1)) register_12 (.D(multiplexer_8_out), .Q(ALUSrcX_2), .clk(CLK));  // open: en, clr
  Multiplexer #(.enable("false")) multiplexer_9 (.in0(JAL), .in1(1'b0), .out(multiplexer_9_out), .sel(Clear));
  Register #(.width(1)) register_13 (.D(multiplexer_9_out), .Q(JAL_2), .clk(CLK));  // open: en, clr
  Multiplexer #(.width(32), .enable("false")) multiplexer_10 (
    .in0(IR), .in1({32{1'b0}}), .out(multiplexer_10_out), .sel(Clear));
  Register #(.width(32)) register_14 (.D(R2), .Q(R2out), .clk(CLK));  // open: en, clr
  Register #(.width(32)) register_15 (.D(IMM3), .Q(IMM3_2), .clk(CLK));  // open: en, clr
  Multiplexer #(.enable("false")) multiplexer_11 (.in0(JUMP), .in1(1'b0), .out(multiplexer_11_out), .sel(Clear));
  Register #(.width(1)) register_16 (.D(multiplexer_11_out), .Q(Jump_2), .clk(CLK));  // open: en, clr
  Register #(.width(1)) register_17 (.D(multiplexer_12_out), .Q(CW_2), .clk(CLK));  // open: en, clr
  Multiplexer #(.enable("false")) multiplexer_12 (.in0(CW), .in1(1'b0), .out(multiplexer_12_out), .sel(Clear));
  Multiplexer #(.enable("false")) multiplexer_13 (.in0(ALUSrcY), .in1(1'b0), .out(multiplexer_13_out), .sel(Clear));
  Register #(.width(1)) register_18 (.D(multiplexer_13_out), .Q(ALUSrcY_2), .clk(CLK));  // open: en, clr
  Multiplexer #(.enable("false")) multiplexer_14 (.in0(SYS), .in1(1'b0), .out(multiplexer_14_out), .sel(Clear));
  Register #(.width(1)) register_19 (.D(multiplexer_14_out), .Q(Syscall), .clk(CLK));  // open: en, clr
  Register #(.width(32)) register_20 (.D(multiplexer_10_out), .Q(IR_2), .clk(CLK));  // open: en, clr
  Register #(.width(5)) register_21 (.D(rd), .Q(rd_3), .clk(CLK));  // open: en, clr
  Register #(.width(5)) register_22 (.D(rt), .Q(rt_2), .clk(CLK));  // open: en, clr
  Multiplexer #(.enable("false")) multiplexer_15 (.in0(M2R), .in1(1'b0), .out(multiplexer_15_out), .sel(Clear));
  Multiplexer #(.enable("false")) multiplexer_16 (.in0(ERET), .in1(1'b0), .out(multiplexer_16_out), .sel(Clear));
  Multiplexer #(.enable("false")) multiplexer_17 (.in0(RW), .in1(1'b0), .out(multiplexer_17_out), .sel(Clear));
  Register #(.width(4)) register_23 (.D(ALUop), .Q(ALUop_2), .clk(CLK));  // open: en, clr
  Register #(.width(1)) register_24 (.D(multiplexer_15_out), .Q(M2R_2), .clk(CLK));  // open: en, clr
  Register #(.width(1)) register_25 (.D(multiplexer_16_out), .Q(ERET_2), .clk(CLK));  // open: en, clr
  Register #(.width(1)) register_26 (.D(multiplexer_17_out), .Q(RW_2), .clk(CLK));  // open: en, clr
  Register #(.width(5)) register_27 (.D(rs), .Q(rs_2), .clk(CLK));  // open: en, clr

  assign PCout = PC_4;
endmodule

module EX_MEM (
  input  [31:0] ALUout,
  input  [31:0] WriteData,
  input  [4:0] WriteReg,
  input  CLK,
  input  ERET,
  input  Equal,
  input  SYS,
  input  C2R,
  input  M2R,
  input  MW,
  input  JAL,
  input  RW,
  input  CW,
  input  [31:0] IR,
  input  [31:0] PC_4,
  output [31:0] ALUout_2,
  output [31:0] WriteData_2,
  output ERET_2,
  output Equal_2,
  output Syscall,
  output C2R_2,
  output M2R_2,
  output MW_2,
  output JAL_2,
  output RW_2,
  output CW_2,
  output [4:0] WriteReg_2,
  output [31:0] IR_2,
  output [31:0] PC_4_2
);

  Register #(.width(1)) register_1 (.D(ERET), .Q(ERET_2), .clk(CLK));  // open: en, clr
  Register #(.width(1)) register_2 (.D(C2R), .Q(C2R_2), .clk(CLK));  // open: en, clr
  Register #(.width(1)) register_3 (.D(JAL), .Q(JAL_2), .clk(CLK));  // open: en, clr
  Register #(.width(5)) register_4 (.D(WriteReg), .Q(WriteReg_2), .clk(CLK));  // open: en, clr
  Register #(.width(1)) register_5 (.D(Equal), .Q(Equal_2), .clk(CLK));  // open: en, clr
  Register #(.width(1)) register_6 (.D(M2R), .Q(M2R_2), .clk(CLK));  // open: en, clr
  Register #(.width(32)) register_7 (.D(ALUout), .Q(ALUout_2), .clk(CLK));  // open: en, clr
  Register #(.width(32)) register_8 (.D(IR), .Q(IR_2), .clk(CLK));  // open: en, clr
  Register #(.width(1)) register_9 (.D(SYS), .Q(Syscall), .clk(CLK));  // open: en, clr
  Register #(.width(1)) register_10 (.D(MW), .Q(MW_2), .clk(CLK));  // open: en, clr
  Register #(.width(1)) register_11 (.D(RW), .Q(RW_2), .clk(CLK));  // open: en, clr
  Register #(.width(32)) register_12 (.D(WriteData), .Q(WriteData_2), .clk(CLK));  // open: en, clr
  Register #(.width(1)) register_13 (.D(CW), .Q(CW_2), .clk(CLK));  // open: en, clr
  Register #(.width(32)) register_14 (.D(PC_4), .Q(PC_4_2), .clk(CLK));  // open: en, clr
endmodule

module MEM_WB (
  input  [31:0] ReadData,
  input  [31:0] ALUout,
  input  [4:0] WriteReg,
  input  CLK,
  input  ERET,
  input  Equal,
  input  SYS,
  input  M2R,
  input  RW,
  input  JAL,
  input  CW,
  input  C2R,
  input  [31:0] IR,
  input  [31:0] PC_4,
  output [31:0] ReadData_2,
  output [31:0] ALUout_2,
  output [4:0] WriteReg_2,
  output ERET_2,
  output Equal_2,
  output Syscall,
  output M2R_2,
  output RegWrite,
  output JAL_2,
  output CW_2,
  output C2R_2,
  output [31:0] IR_2,
  output [31:0] PC_4_2
);

  Register #(.width(32)) register_1 (.D(ReadData), .Q(ReadData_2), .clk(CLK));  // open: en, clr
  Register #(.width(1)) register_2 (.D(ERET), .Q(ERET_2), .clk(CLK));  // open: en, clr
  Register #(.width(1)) register_3 (.D(RW), .Q(RegWrite), .clk(CLK));  // open: en, clr
  Register #(.width(1)) register_4 (.D(Equal), .Q(Equal_2), .clk(CLK));  // open: en, clr
  Register #(.width(1)) register_5 (.D(JAL), .Q(JAL_2), .clk(CLK));  // open: en, clr
  Register #(.width(32)) register_6 (.D(ALUout), .Q(ALUout_2), .clk(CLK));  // open: en, clr
  Register #(.width(32)) register_7 (.D(IR), .Q(IR_2), .clk(CLK));  // open: en, clr
  Register #(.width(1)) register_8 (.D(SYS), .Q(Syscall), .clk(CLK));  // open: en, clr
  Register #(.width(1)) register_9 (.D(CW), .Q(CW_2), .clk(CLK));  // open: en, clr
  Register #(.width(5)) register_10 (.D(WriteReg), .Q(WriteReg_2), .clk(CLK));  // open: en, clr
  Register #(.width(1)) register_11 (.D(M2R), .Q(M2R_2), .clk(CLK));  // open: en, clr
  Register #(.width(1)) register_12 (.D(C2R), .Q(C2R_2), .clk(CLK));  // open: en, clr
  Register #(.width(32)) register_13 (.D(PC_4), .Q(PC_4_2), .clk(CLK));  // open: en, clr
endmodule

module HALT (
  input  CLK,
  input  ISR,
  input  Continue,
  input  Break,
  input  SYSCALL,
  input  Equal,
  output CLKout,
  output Halt
);

  wire and_1_out, and_2_out, or_1_out;

  and and_1 (and_1_out, SYSCALL, Equal);
  and and_2 (and_2_out, ~Break, ~and_1_out);  // AND_Gate
  or or_1 (or_1_out, Continue, and_2_out);
  and and_3 (Halt, ~ISR, or_1_out);  // AND_Gate
  and and_4 (CLKout, CLK, Halt);
endmodule

// PCSel
module PC_Select_Unit (
  input  [31:0] PC_4,
  input  [31:0] PCBranch,
  input  [31:0] PCJump,
  input  [31:0] ra,
  input  [31:0] EPC,
  input  B,
  input  J,
  input  Int,
  input  ERET,
  input  JR,
  output [31:0] PCout
);

  wire [31:0] multiplexer_1_out, multiplexer_2_out, multiplexer_3_out, multiplexer_4_out;

  Multiplexer #(.width(32), .enable("false")) multiplexer_1 (
    .in0(PC_4), .in1(PCBranch), .out(multiplexer_1_out), .sel(B));
  Multiplexer #(.width(32), .enable("false")) multiplexer_2 (
    .in0(multiplexer_1_out), .in1(PCJump), .out(multiplexer_2_out), .sel(J));
  Multiplexer #(.width(32), .enable("false")) multiplexer_3 (
    .in0(multiplexer_2_out), .in1(32'h40), .out(multiplexer_3_out), .sel(Int));
  Multiplexer #(.width(32), .enable("false")) multiplexer_4 (
    .in0(multiplexer_3_out), .in1(EPC), .out(multiplexer_4_out), .sel(ERET));
  Multiplexer #(.width(32), .enable("false")) multiplexer_5 (.in0(multiplexer_4_out), .in1(ra), .out(PCout), .sel(JR));
endmodule

module ID (
  input  [31:0] Instr,
  input  [4:0] WriteReg,
  input  SYSCALL,
  input  Int,
  input  ERET,
  input  JAL,
  output [4:0] rs,
  output [4:0] R1_num,
  output [4:0] R2_num,
  output [4:0] WriteReg_num,
  output [4:0] rt,
  output [4:0] rd
);

  wire or_1_out;
  wire [4:0] multiplexer_2_out;

  Multiplexer #(.width(5), .enable("false")) multiplexer_1 (
    .in0(Instr[20:16]), .in1(5'b00100), .out(R2_num), .sel(SYSCALL));
  Multiplexer #(.width(5), .enable("false")) multiplexer_2 (
    .in0(Instr[25:21]), .in1(5'b00010), .out(multiplexer_2_out), .sel(SYSCALL));
  Multiplexer #(.width(5), .enable("false")) multiplexer_3 (
    .in0(WriteReg), .in1({5{1'b1}}), .out(WriteReg_num), .sel(JAL));
  or or_1 (or_1_out, Int, ERET);
  Multiplexer #(.width(5), .enable("false")) multiplexer_4 (
    .in0(multiplexer_2_out), .in1(5'b11101), .out(R1_num), .sel(or_1_out));

  assign rd = Instr[15:11];
  assign rs = Instr[25:21];
  assign rt = Instr[20:16];
endmodule

module EX (
  input  [31:0] R1,
  input  ALUSrcX,
  input  [31:0] R2,
  input  [31:0] SignedIMM,
  input  [31:0] UnsignedIMM,
  input  UNSIGN,
  input  ALUSrcY,
  input  SYSCALL,
  input  [31:0] sa,
  input  [4:0] rt,
  input  [4:0] rd,
  input  RD_2,
  input  [31:0] ALUoutM,
  input  [31:0] ResultW,
  input  [1:0] ForwardX,
  input  [1:0] ForwardY,
  input  [1:0] Forwarda0,
  output [31:0] ALUX,
  output [31:0] WriteData,
  output [31:0] ALUY,
  output [4:0] WriteReg,
  output [31:0] a0
);

  wire [31:0] multiplexer_1_out, multiplexer_3_out, multiplexer_4_out, multiplexer_5_out, multiplexer_6_out,
       multiplexer_9_out, multiplexer_10_out;

  Multiplexer #(.width(32), .enable("false")) multiplexer_1 (
    .in0(R2), .in1(ResultW), .out(multiplexer_1_out), .sel(ForwardY[0]));
  Multiplexer #(.width(32), .enable("false")) multiplexer_2 (
    .in0(multiplexer_1_out), .in1(ALUoutM), .out(WriteData), .sel(ForwardY[1]));
  Multiplexer #(.width(32), .enable("false")) multiplexer_3 (
    .in0(R1), .in1(WriteData), .out(multiplexer_3_out), .sel(ALUSrcX));
  Multiplexer #(.width(32), .enable("false")) multiplexer_4 (
    .in0(SignedIMM), .in1(UnsignedIMM), .out(multiplexer_4_out), .sel(UNSIGN));
  Multiplexer #(.width(32), .enable("false")) multiplexer_5 (
    .in0(R2), .in1(ALUoutM), .out(multiplexer_5_out), .sel(Forwarda0[1]));
  Multiplexer #(.width(32), .enable("false")) multiplexer_6 (
    .in0(WriteData), .in1(multiplexer_4_out), .out(multiplexer_6_out), .sel(ALUSrcY));
  Multiplexer #(.width(5), .enable("false")) multiplexer_7 (.in0(rt), .in1(rd), .out(WriteReg), .sel(RD_2));
  Multiplexer #(.width(32), .enable("false")) multiplexer_8 (
    .in0(multiplexer_5_out), .in1(ResultW), .out(a0), .sel(Forwarda0[0]));
  Multiplexer #(.width(32), .enable("false")) multiplexer_9 (
    .in0(multiplexer_3_out), .in1(ResultW), .out(multiplexer_9_out), .sel(ForwardX[0]));
  Multiplexer #(.width(32), .enable("false")) multiplexer_10 (
    .in0(multiplexer_6_out), .in1(sa), .out(multiplexer_10_out), .sel(ALUSrcX));
  Multiplexer #(.width(32), .enable("false")) multiplexer_11 (
    .in0(multiplexer_10_out), .in1(32'ha), .out(ALUY), .sel(SYSCALL));
  Multiplexer #(.width(32), .enable("false")) multiplexer_12 (
    .in0(multiplexer_9_out), .in1(ALUoutM), .out(ALUX), .sel(ForwardX[1]));

  // Other names for the same wires on the sheet: Forwarda02 = Forwarda0[0]
endmodule

module Hazard_Unit (
  input  [4:0] RsE,
  input  [4:0] WriteRegM,
  input  [4:0] WriteRegW,
  input  [4:0] RtE,
  input  RegWriteM,
  input  RegWriteW,
  input  [4:0] WriteRegE,
  input  RegWriteE,
  input  M2RE,
  input  EqualE,
  input  SyscallE,
  input  [4:0] RsD,
  input  [4:0] RtD,
  input  BranchE,
  input  JumpE,
  output [1:0] Forwarda0,
  output [1:0] ForwardXE,
  output [1:0] ForwardYE,
  output Pause,
  output FlushE,
  output FlushD
);

  wire and_1_out, and_2_out, and_3_out, and_6_out, and_7_out, and_8_out, and_9_out, comparator_1_eq,
       comparator_2_eq, comparator_3_eq, comparator_4_eq, comparator_5_eq, comparator_6_eq, comparator_7_eq,
       comparator_8_eq, comparator_9_eq, comparator_10_eq, comparator_11_eq, comparator_12_eq,
       comparator_13_eq, comparator_14_eq, not_1_out, not_2_out, not_3_out, not_4_out, not_5_out, not_6_out,
       or_1_out;

  Comparator #(.width(5)) comparator_1 (.a(WriteRegM), .b(5'b00100), .eq(comparator_1_eq));  // open: gt, lt
  Comparator #(.width(5)) comparator_2 (.a(WriteRegW), .b(5'b00100), .eq(comparator_2_eq));  // open: gt, lt
  Comparator #(.width(5)) comparator_3 (.a(WriteRegM), .b(5'b00010), .eq(comparator_3_eq));  // open: gt, lt
  Comparator #(.width(5)) comparator_4 (.a(RsE), .b({5{1'b0}}), .eq(comparator_4_eq));  // open: gt, lt
  Comparator #(.width(5)) comparator_5 (.a(RsE), .b(WriteRegM), .eq(comparator_5_eq));  // open: gt, lt
  Comparator #(.width(5)) comparator_6 (.a(RsE), .b({5{1'b0}}), .eq(comparator_6_eq));  // open: gt, lt
  Comparator #(.width(5)) comparator_7 (.a(RsE), .b(WriteRegW), .eq(comparator_7_eq));  // open: gt, lt
  Comparator #(.width(5)) comparator_8 (.a(WriteRegW), .b(5'b00010), .eq(comparator_8_eq));  // open: gt, lt
  Comparator #(.width(5)) comparator_9 (.a(RtE), .b({5{1'b0}}), .eq(comparator_9_eq));  // open: gt, lt
  Comparator #(.width(5)) comparator_10 (.a(RtE), .b(WriteRegM), .eq(comparator_10_eq));  // open: gt, lt
  Comparator #(.width(5)) comparator_11 (.a(RtE), .b({5{1'b0}}), .eq(comparator_11_eq));  // open: gt, lt
  Comparator #(.width(5)) comparator_12 (.a(RtE), .b(WriteRegW), .eq(comparator_12_eq));  // open: gt, lt
  Comparator #(.width(5)) comparator_13 (.a(RsD), .b(RtE), .eq(comparator_13_eq));  // open: gt, lt
  Comparator #(.width(5)) comparator_14 (.a(RtE), .b(RtD), .eq(comparator_14_eq));  // open: gt, lt
  not not_1 (not_1_out, EqualE);
  not not_2 (not_2_out, EqualE);
  not not_3 (not_3_out, comparator_4_eq);
  not not_4 (not_4_out, comparator_6_eq);
  not not_5 (not_5_out, comparator_9_eq);
  not not_6 (not_6_out, comparator_11_eq);
  or or_1 (or_1_out, comparator_13_eq, comparator_14_eq);
  and and_1 (and_1_out, not_1_out, comparator_1_eq);
  and and_2 (and_2_out, not_2_out, comparator_2_eq);
  and and_3 (and_3_out, M2RE, or_1_out);
  and and_4 (Forwarda0[1], SyscallE, RegWriteM, and_1_out);
  and and_5 (Forwarda0[0], SyscallE, RegWriteW, and_2_out);
  and and_6 (and_6_out, SyscallE, comparator_3_eq, RegWriteM);
  and and_7 (and_7_out, not_3_out, RegWriteM, comparator_5_eq);
  and and_8 (and_8_out, not_4_out, RegWriteW, comparator_7_eq);
  and and_9 (and_9_out, comparator_8_eq, RegWriteW, SyscallE);
  and and_10 (ForwardYE[1], not_5_out, RegWriteM, comparator_10_eq);
  and and_11 (ForwardYE[0], not_6_out, RegWriteW, comparator_12_eq);
  or or_2 (ForwardXE[1], and_6_out, and_7_out);
  or or_3 (ForwardXE[0], and_8_out, and_9_out);
  not not_7 (Pause, and_3_out);
  or or_4 (FlushE, and_3_out, FlushD);
  or or_5 (FlushD, BranchE, JumpE);
endmodule

module test (
  input  Funct5,
  input  Funct4,
  input  Funct3,
  input  Funct2,
  input  Funct1,
  input  Funct0,
  output y
);

  wire and_1_out, and_2_out, not_1_out, not_2_out, not_3_out, not_4_out, not_5_out, not_6_out, not_7_out,
       not_8_out, not_9_out, not_10_out;

  not not_1 (not_1_out, Funct5);
  not not_2 (not_2_out, Funct4);
  not not_3 (not_3_out, Funct3);
  not not_4 (not_4_out, Funct2);
  not not_5 (not_5_out, Funct1);
  not not_6 (not_6_out, Funct0);
  not not_7 (not_7_out, Funct5);
  not not_8 (not_8_out, Funct4);
  not not_9 (not_9_out, Funct3);
  not not_10 (not_10_out, Funct2);
  and and_1 (and_1_out, not_1_out, not_2_out, not_3_out, not_4_out, not_5_out, not_6_out);
  and and_2 (and_2_out, not_7_out, not_8_out, not_9_out, not_10_out, Funct1, Funct0);
  or or_1 (y, and_1_out, and_2_out);
endmodule
