// Logisim project MIPS CPU_pipelined_Redirection.circ as structural Verilog: 15 circuits, main circuit main
module main (
);

  wire ALUSrcA, ALUSrcB, and_1_out, and_2_out, and_3_out, and_4_out, Branch, CLK, clk_t,
       control_unit_1_alusrca, control_unit_1_alusrcb, control_unit_1_branch, control_unit_1_isbne,
       control_unit_1_iseret, control_unit_1_isspecial, control_unit_1_issyscall, control_unit_1_jr,
       control_unit_1_jump, control_unit_1_memread, control_unit_1_memwrite, control_unit_1_regwrite, Disp,
       Equal, ex_mem_1_haltm, HaltE, HaltW, hazard_unit_1_flushe, hazard_unit_1_forwardad,
       hazard_unit_1_forwardbd, hazard_unit_1_stallf, hazard_unit_1_statid, id_ex_1_memreade,
       id_ex_1_memwritee, IsBNE, IsERET, IsSpecial, IsSyscall, JR, Jump, MemRead, MemWrite,
       multiplexer_7_out, not_1_out, not_2_out, or_1_out, R1_num, R2_num, RegWriteE, RegWriteM, RegWriteW,
       statics_1_i, statics_1_j, statics_1_r;
  wire [1:0] control_unit_1_memtoreg, control_unit_1_regdes, ex_mem_1_memtoregm, hazard_unit_1_forwardae,
       hazard_unit_1_forwardbe, mem_wb_1_memtoregw, MemtoRegE, RegDst, S_EXT;
  wire [3:0] ALUControl, control_unit_1_aluctrl;
  wire [4:0] ex_mem_1_writeregm, id_ex_1_rde, id_ex_1_rse, id_ex_1_rte, mem_wb_1_writeregw,
       multiplexer_3_out, multiplexer_5_out, multiplexer_6_out, multiplexer_11_out;
  wire [15:0] counter_1_q, counter_2_q, counter_3_q, counter_4_q, multiplexer_4_out;
  wire [27:0] id_ex_1_pcplus4e;
  wire [31:0] a0, adder_1_out, adder_2_out, alu_1_result, bit_extender_1_out, ex_mem_1_aluoutm,
       ex_mem_1_writedatam, id_ex_1_r2e, id_ex_1_signlmme, if_id_1_pcplus4d, Instruction, main_1_reg1,
       main_1_reg2_2, mem_wb_1_aluoutw, mem_wb_1_readdataw, multiplexer_1_out, multiplexer_2_out,
       multiplexer_8_out, multiplexer_9_out, multiplexer_10_out, multiplexer_12_out, multiplexer_13_out,
       multiplexer_14_out, multiplexer_15_out, multiplexer_16_out, PC_q, ram_1_data, register_1_q,
       rom_1_data, shifter_1_out;
  wire [31:28] id_ex_1_pcplus4e_2;

  Register #(.width(32)) PC (.D(multiplexer_1_out), .en(1'b1), .Q(PC_q), .clk(CLK), .clr(hazard_unit_1_stallf));
  Hazard_Unit hazard_unit_1 (
    .StallF(hazard_unit_1_stallf), .StatID(hazard_unit_1_statid), .ForwardAD(hazard_unit_1_forwardad),
    .ForwardBD(hazard_unit_1_forwardbd), .RsD(Instruction[25:21]), .RtD(Instruction[20:16]),
    .FlushE(hazard_unit_1_flushe), .RsE(id_ex_1_rse), .RtE(id_ex_1_rte), .ForwardAE(hazard_unit_1_forwardae),
    .ForwardBE(hazard_unit_1_forwardbe), .BranchE(Branch), .WriteRegE(multiplexer_11_out),
    .WriteRegM(ex_mem_1_writeregm), .MemtoRegE(MemtoRegE), .RegWriteE(RegWriteE), .RegWriteM(RegWriteM),
    .RegWriteW(RegWriteW), .WriteRegW(mem_wb_1_writeregw));
  ROM #(.addrWidth(10), .dataWidth(32)) rom_1 (.addr(PC_q[11:2]), .data(rom_1_data));  // open: sel
  Adder #(.width(32)) adder_1 (.a(PC_q), .b(32'h4), .out(adder_1_out));  // open: cin, cout
  not not_1 (not_1_out, HaltW);
  Multiplexer #(.width(32)) multiplexer_1 (
    .in0(multiplexer_2_out), .in1(a0), .out(multiplexer_1_out), .sel(JR), .en(1'b1));
  or or_1 (or_1_out, Branch, JR, Jump);
  assign CLK = not_1_out ? clk_t : 1'bz;  // Controlled_Buffer controlled_buffer_1
  IF_ID if_id_1 (
    .InstrF(rom_1_data), .PCPlus4F(adder_1_out), .InstrD(Instruction), .PCPlus4D(if_id_1_pcplus4d),
    .CLK(CLK), .CLR(or_1_out), .EN(hazard_unit_1_statid));
  Counter #(.width(16), .max('hffff)) counter_1 (.Q(counter_1_q), .clk(CLK));  // open: load, D, count, carry, clr
  statics statics_1 (
    .op0(Instruction[31]), .op1(Instruction[30]), .op2(Instruction[29]), .op3(Instruction[28]),
    .op4(Instruction[27]), .op5(Instruction[26]), .R(statics_1_r), .I(statics_1_i), .J(statics_1_j));
  Multiplexer #(.width(32)) multiplexer_2 (
    .in0(multiplexer_8_out), .in1({id_ex_1_pcplus4e_2, Instruction[25:0], 2'b00}), .out(multiplexer_2_out),
    .sel(Jump), .en(1'b1));
  Control_Unit control_unit_1 (
    .OP(Instruction[31:26]), .Funct(Instruction[5:0]), .R1_num(R1_num), .R2_num(R2_num),
    .AluCtrl(control_unit_1_aluctrl), .RegDes(control_unit_1_regdes), .S_EXT(S_EXT),
    .AluSrcA(control_unit_1_alusrca), .AluSrcB(control_unit_1_alusrcb), .JR(control_unit_1_jr),
    .Branch(control_unit_1_branch), .Jump(control_unit_1_jump), .RegWrite(control_unit_1_regwrite),
    .MemRead(control_unit_1_memread), .MemWrite(control_unit_1_memwrite), .MemtoReg(control_unit_1_memtoreg),
    .IsBNE(control_unit_1_isbne), .IsSyscall(control_unit_1_issyscall), .IsSpecial(control_unit_1_isspecial),
    .IsERET(control_unit_1_iseret));
  and and_1 (and_1_out, not_1_out, statics_1_r);
  and and_2 (and_2_out, not_1_out, statics_1_i);
  and and_3 (and_3_out, statics_1_j, not_1_out);
  Multiplexer #(.width(5)) multiplexer_3 (
    .in0(Instruction[25:21]), .in1(Instruction[20:16]), .out(multiplexer_3_out), .sel(R1_num), .en(1'b1));
  Multiplexer #(.select(2), .width(16)) multiplexer_4 (
    .in0(Instruction[15:0]), .in1({{11{1'b0}}, Instruction[10:6]}), .in2(16'ha), .out(multiplexer_4_out),
    .sel(S_EXT), .en(1'b1));  // open: in3
  Counter #(.width(16), .max('hffff)) counter_2 (
    .count(and_1_out), .Q(counter_2_q), .clk(clk_t));  // open: load, D, carry, clr
  Counter #(.width(16), .max('hffff)) counter_3 (
    .count(and_2_out), .Q(counter_3_q), .clk(clk_t));  // open: load, D, carry, clr
  Counter #(.width(16), .max('hffff)) counter_4 (
    .count(and_3_out), .Q(counter_4_q), .clk(clk_t));  // open: load, D, carry, clr
  Shifter #(.width(32)) shifter_1 (.in(id_ex_1_signlmme), .\dist (5'b00010), .out(shifter_1_out));
  not not_2 (not_2_out, Equal);
  Multiplexer #(.width(5)) multiplexer_5 (
    .in0(multiplexer_3_out), .in1(5'b00100), .out(multiplexer_5_out), .sel(R2_num), .en(1'b1));
  Multiplexer #(.width(5)) multiplexer_6 (
    .in0(Instruction[20:16]), .in1(5'b00010), .out(multiplexer_6_out), .sel(R2_num), .en(1'b1));
  assign bit_extender_1_out = {{16{multiplexer_4_out[15]}}, multiplexer_4_out};  // Bit_Extender bit_extender_1
  Adder #(.width(32)) adder_2 (
    .a({id_ex_1_pcplus4e_2, id_ex_1_pcplus4e}), .b(shifter_1_out), .out(adder_2_out), .cin(1'b0));  // open: cout
  Multiplexer multiplexer_7 (.in0(Equal), .in1(not_2_out), .out(multiplexer_7_out), .sel(IsBNE), .en(1'b1));
  and and_4 (and_4_out, Branch, multiplexer_7_out);
  regfile_main main_1 (
    .Reg1_num(multiplexer_5_out), .Reg2(multiplexer_6_out), .Write_Reg_num(mem_wb_1_writeregw),
    .Din(multiplexer_16_out), .Write_Enable(RegWriteW), .Clock(CLK), .Reg1(main_1_reg1),
    .Reg2_2(main_1_reg2_2));  // open: s0_Value, a0_Value, v0_Value, ra_Value
  // Probe on counter_1_q
  // Probe on counter_2_q
  // Probe on counter_3_q
  // Probe on counter_4_q
  Multiplexer #(.width(32)) multiplexer_8 (
    .in0(adder_1_out), .in1(adder_2_out), .out(multiplexer_8_out), .sel(and_4_out), .en(1'b1));
  Multiplexer #(.width(32)) multiplexer_9 (
    .in0(main_1_reg1), .in1(ex_mem_1_aluoutm), .out(multiplexer_9_out), .sel(hazard_unit_1_forwardad),
    .en(1'b1));
  Comparator #(.width(32)) comparator_1 (.a(multiplexer_9_out), .b(multiplexer_10_out), .eq(Equal));  // open: gt, lt
  Multiplexer #(.width(32)) multiplexer_10 (
    .in0(main_1_reg2_2), .in1(ex_mem_1_aluoutm), .out(multiplexer_10_out), .sel(hazard_unit_1_forwardbd),
    .en(1'b1));
  ID_EX id_ex_1 (
    .CLK(CLK), .R1D(main_1_reg1), .R2D(main_1_reg2_2), .R1E(a0), .R2E(id_ex_1_r2e),
    .RegWriteD(control_unit_1_regwrite), .MemtoRegD(control_unit_1_memtoreg),
    .MemWriteD(control_unit_1_memwrite), .ALUControlD(control_unit_1_aluctrl),
    .ALUSrcAD(control_unit_1_alusrca), .ALUSrcBD(control_unit_1_alusrcb), .JRD(control_unit_1_jr),
    .BranchD(control_unit_1_branch), .JumpD(control_unit_1_jump), .MemReadD(control_unit_1_memread),
    .IsBNED(control_unit_1_isbne), .IsSyscallD(control_unit_1_issyscall),
    .IsSpecialD(control_unit_1_isspecial), .IsERETD(control_unit_1_iseret), .RegDstD(control_unit_1_regdes),
    .RegWriteE(RegWriteE), .MemtoRegE(MemtoRegE), .MemReadE(id_ex_1_memreade), .MemWriteE(id_ex_1_memwritee),
    .ALUControlE(ALUControl), .ALUSrcAE(ALUSrcA), .ALUSrcBE(ALUSrcB), .BranchE(Branch), .JRE(JR),
    .JumpE(Jump), .IsBNEE(IsBNE), .IsSyscallE(IsSyscall), .IsSpecialE(IsSpecial), .IsERETE(IsERET),
    .RegDst(RegDst), .RsD(Instruction[25:21]), .RtD(Instruction[20:16]), .RdD(Instruction[15:11]),
    .SignlmmD(bit_extender_1_out), .RsE(id_ex_1_rse), .RtE(id_ex_1_rte), .RdE(id_ex_1_rde),
    .SignlmmE(id_ex_1_signlmme), .CLR(hazard_unit_1_flushe), .PCPlus4D(if_id_1_pcplus4d),
    .PCPlus4E({id_ex_1_pcplus4e_2, id_ex_1_pcplus4e}));
  Hex_Digit_Display hex_digit_display_1 (.value(register_1_q[31:28]), .dp(1'b0));
  Register #(.width(32)) register_1 (.D(a0), .en(Disp), .Q(register_1_q), .clk(CLK), .clr(1'b0));
  // Syscall syscall_1: pin names not known; wires that end beside it: IsSyscall, CLK, id_ex_1_r2e, Disp, HaltE
  Multiplexer #(.select(2), .width(5)) multiplexer_11 (
    .in0(id_ex_1_rde), .in1(id_ex_1_rte), .in2({5{1'b1}}), .out(multiplexer_11_out), .sel(RegDst), .en(1'b1));  // open: in3
  Hex_Digit_Display hex_digit_display_2 (.value(register_1_q[23:20]), .dp(1'b0));
  Hex_Digit_Display hex_digit_display_3 (.value(register_1_q[27:24]), .dp(1'b0));
  Clock clock_1 (.out(clk_t));
  Multiplexer #(.select(2), .width(32)) multiplexer_12 (
    .in0(a0), .in1(multiplexer_16_out), .in2(ex_mem_1_aluoutm), .out(multiplexer_12_out),
    .sel(hazard_unit_1_forwardae));  // open: in3, en
  Multiplexer #(.select(2), .width(32)) multiplexer_13 (
    .in0(id_ex_1_r2e), .in1(multiplexer_16_out), .in2(ex_mem_1_aluoutm), .out(multiplexer_13_out),
    .sel(hazard_unit_1_forwardbe));  // open: in3, en
  Hex_Digit_Display hex_digit_display_4 (.value(register_1_q[15:12]), .dp(1'b0));
  Hex_Digit_Display hex_digit_display_5 (.value(register_1_q[19:16]), .dp(1'b0));
  Multiplexer #(.width(32)) multiplexer_14 (
    .in0(multiplexer_12_out), .in1(multiplexer_13_out), .out(multiplexer_14_out), .sel(ALUSrcA), .en(1'b1));
  Multiplexer #(.width(32)) multiplexer_15 (
    .in0(multiplexer_13_out), .in1(id_ex_1_signlmme), .out(multiplexer_15_out), .sel(ALUSrcB), .en(1'b1));
  Hex_Digit_Display hex_digit_display_6 (.value(register_1_q[11:8]), .dp(1'b0));
  Hex_Digit_Display hex_digit_display_7 (.value(register_1_q[7:4]), .dp(1'b0));
  ALU alu_1 (
    .AluOP(ALUControl), .X(multiplexer_14_out), .Result(alu_1_result), .Y(multiplexer_15_out));  // open: Equal, Signed_Overflow, Result_2, UnSigned_Overflow
  Hex_Digit_Display hex_digit_display_8 (.value(register_1_q[3:0]), .dp(1'b0));
  EX_MEM ex_mem_1 (
    .CLK(CLK), .ALUOutE(alu_1_result), .WriteDataE(multiplexer_13_out), .WriteRegE(multiplexer_11_out),
    .ALUOutM(ex_mem_1_aluoutm), .WriteDataM(ex_mem_1_writedatam), .WriteRegM(ex_mem_1_writeregm),
    .RegWriteE(RegWriteE), .MemtoRegE(MemtoRegE), .MemReadE(id_ex_1_memreade), .MemWriteE(id_ex_1_memwritee),
    .RegWriteM(RegWriteM), .MemtoRegM(ex_mem_1_memtoregm), .MemReadM(MemRead), .MemWriteM(MemWrite),
    .HaltE(HaltE), .HaltM(ex_mem_1_haltm));
  RAM #(.addrWidth(16), .dataWidth(32), .bus("separate")) ram_1 (
    .addr(ex_mem_1_aluoutm[17:2]), .din(ex_mem_1_writedatam), .data(ram_1_data), .str(MemWrite), .sel(1'b1),
    .clk(CLK), .ld(MemRead), .clr(1'b0));
  MEM_WB mem_wb_1 (
    .CLK(CLK), .ReadDataM(ram_1_data), .ALUOutM(ex_mem_1_aluoutm), .WriteRegM(ex_mem_1_writeregm),
    .ReadDataW(mem_wb_1_readdataw), .ALUOutW(mem_wb_1_aluoutw), .WriteRegW(mem_wb_1_writeregw),
    .RegWriteM(RegWriteM), .MemtoRegM(ex_mem_1_memtoregm), .RegWriteW(RegWriteW),
    .MemtoRegW(mem_wb_1_memtoregw), .HaltM(ex_mem_1_haltm), .HaltW(HaltW));
  Multiplexer #(.select(2), .width(32)) multiplexer_16 (
    .in0(mem_wb_1_aluoutw), .in1(mem_wb_1_readdataw), .out(multiplexer_16_out), .sel(mem_wb_1_memtoregw),
    .en(1'b1));  // open: in2, in3

  // Other names for the same wires on the sheet: rd[4:0] = Instruction[15:11]; rt[4:0] = Instruction[20:16];
  //   rs[4:0] = Instruction[25:21]

  // Notes on the sheet:
  //   StallF
  //   contents of rom_1 (hex, n*v repeats v):
  //   20100000 20110000 20120000 20130000 36100000 36310001 36520002 36730003 ae100000 ae110004 ae120008
  //   ae13000c 2002000a 20110000 20120000 20130000 c
  //   StallD
  //   FowardBD
  //   FowardAD
  //   RsD
  //   SignlmmD
  //   PCPlus4D
  //   FlushE
  //   FowardAE
  //   FowardBE
  //   ALUOutE
  //   WriteDataE
  //   WriteRegE
  //   ReadDataM
  //   ALUOutM
  //   WriteRegM
  //   ResultW
endmodule

module IF_ID (
  input  EN,
  input  CLK,
  input  [31:0] InstrF,
  input  [31:0] PCPlus4F,
  input  CLR,
  output [31:0] InstrD,
  output [31:0] PCPlus4D
);

  wire d_ff_1_q;

  Register #(.width(32)) register_1 (.D(InstrF), .en(EN), .Q(InstrD), .clk(CLK), .clr(d_ff_1_q));
  Register #(.width(32)) register_2 (.D(PCPlus4F), .en(EN), .Q(PCPlus4D), .clk(CLK), .clr(d_ff_1_q));
  D_Flip_Flop d_ff_1 (.clk(CLK), .D(CLR), .Q(d_ff_1_q), .en(EN));  // open: Qn, preset, reset
endmodule

module ID_EX (
  input  CLK,
  input  CLR,
  input  RegWriteD,
  input  [1:0] MemtoRegD,
  input  MemReadD,
  input  MemWriteD,
  input  [3:0] ALUControlD,
  input  ALUSrcAD,
  input  ALUSrcBD,
  input  BranchD,
  input  JRD,
  input  JumpD,
  input  IsBNED,
  input  IsSyscallD,
  input  IsSpecialD,
  input  IsERETD,
  input  [1:0] RegDstD,
  input  [31:0] R1D,
  input  [31:0] R2D,
  input  [4:0] RsD,
  input  [4:0] RtD,
  input  [4:0] RdD,
  input  [31:0] SignlmmD,
  input  [31:0] PCPlus4D,
  output RegWriteE,
  output [1:0] MemtoRegE,
  output MemReadE,
  output MemWriteE,
  output [3:0] ALUControlE,
  output ALUSrcAE,
  output ALUSrcBE,
  output BranchE,
  output JRE,
  output JumpE,
  output IsBNEE,
  output IsSyscallE,
  output IsSpecialE,
  output IsERETE,
  output [1:0] RegDst,
  output [31:0] R1E,
  output [31:0] R2E,
  output [4:0] RsE,
  output [4:0] RtE,
  output [4:0] RdE,
  output [31:0] SignlmmE,
  output [31:0] PCPlus4E
);

  wire d_ff_1_q;

  Register #(.width(1)) register_1 (.D(RegWriteD), .Q(RegWriteE), .clk(CLK), .clr(d_ff_1_q));  // open: en
  Register #(.width(2)) register_2 (.D(MemtoRegD), .Q(MemtoRegE), .clk(CLK), .clr(d_ff_1_q));  // open: en
  Register #(.width(1)) register_3 (.D(MemReadD), .Q(MemReadE), .clk(CLK), .clr(d_ff_1_q));  // open: en
  Register #(.width(1)) register_4 (.D(MemWriteD), .Q(MemWriteE), .clk(CLK), .clr(d_ff_1_q));  // open: en
  Register #(.width(4)) register_5 (.D(ALUControlD), .Q(ALUControlE), .clk(CLK), .clr(d_ff_1_q));  // open: en
  Register #(.width(1)) register_6 (.D(ALUSrcAD), .Q(ALUSrcAE), .clk(CLK), .clr(d_ff_1_q));  // open: en
  Register #(.width(1)) register_7 (.D(ALUSrcBD), .Q(ALUSrcBE), .clk(CLK), .clr(d_ff_1_q));  // open: en
  Register #(.width(1)) register_8 (.D(BranchD), .Q(BranchE), .clk(CLK), .clr(d_ff_1_q));  // open: en
  Register #(.width(1)) register_9 (.D(JRD), .Q(JRE), .clk(CLK), .clr(d_ff_1_q));  // open: en
  Register #(.width(1)) register_10 (.D(JumpD), .Q(JumpE), .clk(CLK), .clr(d_ff_1_q));  // open: en
  Register #(.width(1)) register_11 (.D(IsBNED), .Q(IsBNEE), .clk(CLK), .clr(d_ff_1_q));  // open: en
  Register #(.width(1)) register_12 (.D(IsSyscallD), .Q(IsSyscallE), .clk(CLK), .clr(d_ff_1_q));  // open: en
  Register #(.width(1)) register_13 (.D(IsSpecialD), .Q(IsSpecialE), .clk(CLK), .clr(d_ff_1_q));  // open: en
  Register #(.width(1)) register_14 (.D(IsERETD), .Q(IsERETE), .clk(CLK), .clr(d_ff_1_q));  // open: en
  Register #(.width(2)) register_15 (.D(RegDstD), .Q(RegDst), .clk(CLK), .clr(d_ff_1_q));  // open: en
  Register #(.width(32)) register_16 (.D(R1D), .Q(R1E), .clk(CLK), .clr(d_ff_1_q));  // open: en
  Register #(.width(32)) register_17 (.D(R2D), .Q(R2E), .clk(CLK), .clr(d_ff_1_q));  // open: en
  Register #(.width(5)) register_18 (.D(RsD), .Q(RsE), .clk(CLK), .clr(d_ff_1_q));  // open: en
  Register #(.width(5)) register_19 (.D(RtD), .Q(RtE), .clk(CLK), .clr(d_ff_1_q));  // open: en
  Register #(.width(5)) register_20 (.D(RdD), .Q(RdE), .clk(CLK), .clr(d_ff_1_q));  // open: en
  Register #(.width(32)) register_21 (.D(SignlmmD), .Q(SignlmmE), .clk(CLK), .clr(d_ff_1_q));  // open: en
  Register #(.width(32)) register_22 (.D(PCPlus4D), .Q(PCPlus4E), .clk(CLK), .clr(d_ff_1_q));  // open: en
  D_Flip_Flop d_ff_1 (.clk(CLK), .D(CLR), .Q(d_ff_1_q));  // open: Qn, preset, en, reset
endmodule

module EX_MEM (
  input  CLK,
  input  RegWriteE,
  input  [1:0] MemtoRegE,
  input  MemReadE,
  input  MemWriteE,
  input  HaltE,
  input  [31:0] ALUOutE,
  input  [31:0] WriteDataE,
  input  [4:0] WriteRegE,
  output RegWriteM,
  output [1:0] MemtoRegM,
  output MemReadM,
  output MemWriteM,
  output HaltM,
  output [31:0] ALUOutM,
  output [31:0] WriteDataM,
  output [4:0] WriteRegM
);

  Register #(.width(1)) register_1 (.D(RegWriteE), .Q(RegWriteM), .clk(CLK));  // open: en, clr
  Register #(.width(2)) register_2 (.D(MemtoRegE), .Q(MemtoRegM), .clk(CLK));  // open: en, clr
  Register #(.width(1)) register_3 (.D(MemReadE), .Q(MemReadM), .clk(CLK));  // open: en, clr
  Register #(.width(1)) register_4 (.D(MemWriteE), .Q(MemWriteM), .clk(CLK));  // open: en, clr
  Register #(.width(1)) register_5 (.D(HaltE), .Q(HaltM), .clk(CLK));  // open: en, clr
  Register #(.width(32)) register_6 (.D(ALUOutE), .Q(ALUOutM), .clk(CLK));  // open: en, clr
  Register #(.width(32)) register_7 (.D(WriteDataE), .Q(WriteDataM), .clk(CLK));  // open: en, clr
  Register #(.width(5)) register_8 (.D(WriteRegE), .Q(WriteRegM), .clk(CLK));  // open: en, clr
endmodule

module MEM_WB (
  input  CLK,
  input  RegWriteM,
  input  [1:0] MemtoRegM,
  input  HaltM,
  input  [31:0] ReadDataM,
  input  [31:0] ALUOutM,
  input  [4:0] WriteRegM,
  output RegWriteW,
  output [1:0] MemtoRegW,
  output HaltW,
  output [31:0] ReadDataW,
  output [31:0] ALUOutW,
  output [4:0] WriteRegW
);

  Register #(.width(1)) register_1 (.D(RegWriteM), .Q(RegWriteW), .clk(CLK));  // open: en, clr
  Register #(.width(2)) register_2 (.D(MemtoRegM), .Q(MemtoRegW), .clk(CLK));  // open: en, clr
  Register #(.width(1)) register_3 (.D(HaltM), .Q(HaltW), .clk(CLK));  // open: en, clr
  Register #(.width(32)) register_4 (.D(ReadDataM), .Q(ReadDataW), .clk(CLK));  // open: en, clr
  Register #(.width(32)) register_5 (.D(ALUOutM), .Q(ALUOutW), .clk(CLK));  // open: en, clr
  Register #(.width(5)) register_6 (.D(WriteRegM), .Q(WriteRegW), .clk(CLK));  // open: en, clr
endmodule

module Control_Unit (
  input  [5:0] OP,
  input  [5:0] Funct,
  output RegWrite,
  output [1:0] MemtoReg,
  output MemRead,
  output MemWrite,
  output [3:0] AluCtrl,
  output AluSrcA,
  output AluSrcB,
  output Branch,
  output JR,
  output Jump,
  output IsBNE,
  output IsSyscall,
  output IsSpecial,
  output IsERET,
  output [1:0] RegDes,
  output R1_num,
  output R2_num,
  output [1:0] S_EXT
);

  wire and_1_out, and_2_out, and_3_out, and_4_out, and_5_out, and_8_out, controlsignal_funct_decoder1_1_a,
       controlsignal_funct_decoder1_1_b, controlsignal_funct_decoder1_1_r1,
       controlsignal_funct_decoder1_1_r2, controlsignal_funct_decoder2_1_branch,
       controlsignal_funct_decoder2_1_isbne, controlsignal_funct_decoder2_1_issyscall,
       controlsignal_funct_decoder2_1_jr, controlsignal_funct_decoder2_1_jump,
       controlsignal_funct_decoder2_1_memread, controlsignal_funct_decoder2_1_memtoreg,
       controlsignal_funct_decoder2_1_memwrite, controlsignal_funct_decoder2_1_regwrite,
       controlsignal_op_decoder1_1_a, controlsignal_op_decoder1_1_b, controlsignal_op_decoder1_1_r1,
       controlsignal_op_decoder1_1_r2, controlsignal_op_decoder2_1_branch, controlsignal_op_decoder2_1_isbne,
       controlsignal_op_decoder2_1_issyscall, controlsignal_op_decoder2_1_jr,
       controlsignal_op_decoder2_1_jump, controlsignal_op_decoder2_1_memread,
       controlsignal_op_decoder2_1_memtoreg, controlsignal_op_decoder2_1_memwrite,
       controlsignal_op_decoder2_1_regwrite, Is_R_Type, MemtoReg_t, nor_2_out, not_1_out, not_2_out,
       not_3_out, not_4_out, not_5_out, not_6_out, not_7_out, not_8_out, not_9_out, not_10_out, not_11_out,
       not_12_out, not_13_out, not_14_out, not_15_out, not_16_out, not_17_out, not_18_out, not_19_out,
       not_20_out, not_21_out, not_22_out, not_23_out, not_24_out, not_25_out;
  wire [1:0] controlsignal_funct_decoder1_1_din1, controlsignal_funct_decoder1_1_sext1,
       controlsignal_funct_decoder1_1_w1, controlsignal_op_decoder1_1_din1,
       controlsignal_op_decoder1_1_sext1, controlsignal_op_decoder1_1_w1, W1;
  wire [3:0] alu_funct_decoder_1_aluop3, alu_op_decoder_1_aluop3;

  ALU_Op_Decoder alu_op_decoder_1 (
    .op0(OP[5]), .op1(OP[4]), .op2(OP[3]), .op3(OP[2]), .op4(OP[1]), .op5(OP[0]),
    .aluop0(alu_op_decoder_1_aluop3[3]), .aluop1(alu_op_decoder_1_aluop3[2]),
    .aluop2(alu_op_decoder_1_aluop3[1]), .aluop3(alu_op_decoder_1_aluop3[0]));
  ALU_Funct_Decoder alu_funct_decoder_1 (
    .funct0(Funct[5]), .funct1(Funct[4]), .funct2(Funct[3]), .funct3(Funct[2]), .funct4(Funct[1]),
    .funct5(Funct[0]), .aluop0(alu_funct_decoder_1_aluop3[3]), .aluop1(alu_funct_decoder_1_aluop3[2]),
    .aluop2(alu_funct_decoder_1_aluop3[1]), .aluop3(alu_funct_decoder_1_aluop3[0]));
  Controlsignal_Op_Decoder1 controlsignal_op_decoder1_1 (
    .op0(OP[5]), .op1(OP[4]), .op2(OP[3]), .op3(OP[2]), .op4(OP[1]), .op5(OP[0]),
    .R1(controlsignal_op_decoder1_1_r1), .R2(controlsignal_op_decoder1_1_r2),
    .W0(controlsignal_op_decoder1_1_w1[1]), .W1(controlsignal_op_decoder1_1_w1[0]),
    .Din0(controlsignal_op_decoder1_1_din1[1]), .Din1(controlsignal_op_decoder1_1_din1[0]),
    .SEXT0(controlsignal_op_decoder1_1_sext1[1]), .SEXT1(controlsignal_op_decoder1_1_sext1[0]),
    .A(controlsignal_op_decoder1_1_a), .B(controlsignal_op_decoder1_1_b));
  Controlsignal_Funct_Decoder1 controlsignal_funct_decoder1_1 (
    .funct0(Funct[5]), .funct1(Funct[4]), .funct2(Funct[3]), .funct3(Funct[2]), .funct4(Funct[1]),
    .funct5(Funct[0]), .R1(controlsignal_funct_decoder1_1_r1), .R2(controlsignal_funct_decoder1_1_r2),
    .W0(controlsignal_funct_decoder1_1_w1[1]), .W1(controlsignal_funct_decoder1_1_w1[0]),
    .Din0(controlsignal_funct_decoder1_1_din1[1]), .Din1(controlsignal_funct_decoder1_1_din1[0]),
    .SEXT0(controlsignal_funct_decoder1_1_sext1[1]), .SEXT1(controlsignal_funct_decoder1_1_sext1[0]),
    .A(controlsignal_funct_decoder1_1_a), .B(controlsignal_funct_decoder1_1_b));
  Controlsignal_Op_Decoder2 controlsignal_op_decoder2_1 (
    .op0(OP[5]), .op1(OP[4]), .op2(OP[3]), .op3(OP[2]), .op4(OP[1]), .op5(OP[0]),
    .JR(controlsignal_op_decoder2_1_jr), .Branch(controlsignal_op_decoder2_1_branch),
    .Jump(controlsignal_op_decoder2_1_jump), .RegWrite(controlsignal_op_decoder2_1_regwrite),
    .MemRead(controlsignal_op_decoder2_1_memread), .MemWrite(controlsignal_op_decoder2_1_memwrite),
    .MemtoReg(controlsignal_op_decoder2_1_memtoreg), .IsBNE(controlsignal_op_decoder2_1_isbne),
    .isSyscall(controlsignal_op_decoder2_1_issyscall));
  Controlsignal_Funct_Decoder2 controlsignal_funct_decoder2_1 (
    .funct0(Funct[5]), .funct1(Funct[4]), .funct2(Funct[3]), .funct3(Funct[2]), .funct4(Funct[1]),
    .funct5(Funct[0]), .JR(controlsignal_funct_decoder2_1_jr),
    .Branch(controlsignal_funct_decoder2_1_branch), .Jump(controlsignal_funct_decoder2_1_jump),
    .RegWrite(controlsignal_funct_decoder2_1_regwrite), .MemRead(controlsignal_funct_decoder2_1_memread),
    .MemWrite(controlsignal_funct_decoder2_1_memwrite), .MemtoReg(controlsignal_funct_decoder2_1_memtoreg),
    .IsBNE(controlsignal_funct_decoder2_1_isbne), .IsSyscall(controlsignal_funct_decoder2_1_issyscall));
  not not_1 (not_1_out, OP[5]);
  not not_2 (not_2_out, OP[3]);
  not not_3 (not_3_out, OP[2]);
  not not_4 (not_4_out, OP[1]);
  not not_5 (not_5_out, OP[0]);
  not not_6 (not_6_out, OP[5]);
  not not_7 (not_7_out, OP[3]);
  not not_8 (not_8_out, OP[2]);
  not not_9 (not_9_out, OP[1]);
  not not_10 (not_10_out, OP[0]);
  not not_11 (not_11_out, Funct[5]);
  not not_12 (not_12_out, Funct[2]);
  not not_13 (not_13_out, Funct[1]);
  not not_14 (not_14_out, Funct[0]);
  not not_15 (not_15_out, OP[5]);
  not not_16 (not_16_out, OP[3]);
  not not_17 (not_17_out, OP[2]);
  not not_18 (not_18_out, OP[1]);
  not not_19 (not_19_out, OP[0]);
  not not_20 (not_20_out, Funct[5]);
  not not_21 (not_21_out, Funct[4]);
  not not_22 (not_22_out, Funct[3]);
  not not_23 (not_23_out, Funct[2]);
  not not_24 (not_24_out, Funct[1]);
  not not_25 (not_25_out, Funct[0]);
  nor nor_1 (Is_R_Type, OP[5], OP[4], OP[3], OP[2], OP[1], OP[0]);
  and and_1 (and_1_out, not_1_out, OP[4], not_2_out, not_3_out, not_4_out, not_5_out);
  nor nor_2 (nor_2_out, Funct[5], Funct[4], Funct[3]);
  and and_2 (and_2_out, not_6_out, OP[4], not_7_out, not_8_out, not_9_out, not_10_out);
  and and_3 (and_3_out, not_11_out, Funct[4], Funct[3], not_12_out, not_13_out, not_14_out);
  and and_4 (and_4_out, not_15_out, OP[4], not_16_out, not_17_out, not_18_out, not_19_out);
  and and_5 (and_5_out, not_20_out, not_21_out, not_22_out, not_23_out, not_24_out, not_25_out);
  and and_6 (IsSpecial, and_1_out, nor_2_out);
  and and_7 (IsERET, and_2_out, and_3_out);
  and and_8 (and_8_out, and_4_out, and_5_out);
  Multiplexer #(.width(2)) multiplexer_1 (.in0(W1), .in1(2'b01), .out(RegDes), .sel(and_8_out), .en(1'b1));
  Multiplexer #(.width(4)) multiplexer_2 (
    .in0(alu_op_decoder_1_aluop3), .in1(alu_funct_decoder_1_aluop3), .out(AluCtrl), .sel(Is_R_Type), .en(1'b1));
  Multiplexer multiplexer_3 (
    .in0(controlsignal_op_decoder1_1_r1), .in1(controlsignal_funct_decoder1_1_r1), .out(R1_num),
    .sel(Is_R_Type), .en(1'b1));
  Multiplexer multiplexer_4 (
    .in0(controlsignal_op_decoder1_1_r2), .in1(controlsignal_funct_decoder1_1_r2), .out(R2_num),
    .sel(Is_R_Type), .en(1'b1));
  Multiplexer #(.width(2)) multiplexer_5 (
    .in0(controlsignal_op_decoder1_1_w1), .in1(controlsignal_funct_decoder1_1_w1), .out(W1), .sel(Is_R_Type),
    .en(1'b1));
  Multiplexer #(.width(2)) multiplexer_6 (
    .in0(controlsignal_op_decoder1_1_din1), .in1(controlsignal_funct_decoder1_1_din1), .out(MemtoReg),
    .sel(Is_R_Type), .en(1'b1));
  Multiplexer #(.width(2)) multiplexer_7 (
    .in0(controlsignal_op_decoder1_1_sext1), .in1(controlsignal_funct_decoder1_1_sext1), .out(S_EXT),
    .sel(Is_R_Type), .en(1'b1));
  Multiplexer multiplexer_8 (
    .in0(controlsignal_op_decoder1_1_a), .in1(controlsignal_funct_decoder1_1_a), .out(AluSrcA),
    .sel(Is_R_Type), .en(1'b1));
  Multiplexer multiplexer_9 (
    .in0(controlsignal_op_decoder1_1_b), .in1(controlsignal_funct_decoder1_1_b), .out(AluSrcB),
    .sel(Is_R_Type), .en(1'b1));
  Multiplexer multiplexer_10 (
    .in0(controlsignal_op_decoder2_1_jr), .in1(controlsignal_funct_decoder2_1_jr), .out(JR), .sel(Is_R_Type),
    .en(1'b1));
  Multiplexer multiplexer_11 (
    .in0(controlsignal_op_decoder2_1_branch), .in1(controlsignal_funct_decoder2_1_branch), .out(Branch),
    .sel(Is_R_Type), .en(1'b1));
  Multiplexer multiplexer_12 (
    .in0(controlsignal_op_decoder2_1_jump), .in1(controlsignal_funct_decoder2_1_jump), .out(Jump),
    .sel(Is_R_Type), .en(1'b1));
  Multiplexer multiplexer_13 (
    .in0(controlsignal_op_decoder2_1_regwrite), .in1(controlsignal_funct_decoder2_1_regwrite),
    .out(RegWrite), .sel(Is_R_Type), .en(1'b1));
  Multiplexer multiplexer_14 (
    .in0(controlsignal_op_decoder2_1_memread), .in1(controlsignal_funct_decoder2_1_memread), .out(MemRead),
    .sel(Is_R_Type), .en(1'b1));
  Multiplexer multiplexer_15 (
    .in0(controlsignal_op_decoder2_1_memwrite), .in1(controlsignal_funct_decoder2_1_memwrite),
    .out(MemWrite), .sel(Is_R_Type), .en(1'b1));
  Multiplexer multiplexer_16 (
    .in0(controlsignal_op_decoder2_1_memtoreg), .in1(controlsignal_funct_decoder2_1_memtoreg),
    .out(MemtoReg_t), .sel(Is_R_Type), .en(1'b1));
  Multiplexer multiplexer_17 (
    .in0(controlsignal_op_decoder2_1_isbne), .in1(controlsignal_funct_decoder2_1_isbne), .out(IsBNE),
    .sel(Is_R_Type), .en(1'b1));
  Multiplexer multiplexer_18 (
    .in0(controlsignal_op_decoder2_1_issyscall), .in1(controlsignal_funct_decoder2_1_issyscall),
    .out(IsSyscall), .sel(Is_R_Type), .en(1'b1));

  // Other names for the same wires on the sheet: A = AluSrcA; ALUOp[3:0] = AluCtrl; B = AluSrcB; Din[1:0] = MemtoReg;
  //   W_num[1:0] = RegDes
endmodule

// ALU_Op
module ALU_Op_Decoder (
  input  op0,
  input  op1,
  input  op2,
  input  op3,
  input  op4,
  input  op5,
  output aluop0,
  output aluop1,
  output aluop2,
  output aluop3
);

  wire and_1_out, and_2_out, and_3_out, and_4_out, and_5_out, and_6_out, and_7_out, and_8_out, and_9_out,
       and_10_out, and_11_out, not_1_out, not_2_out, not_3_out, not_4_out, not_5_out, not_6_out, not_7_out,
       not_8_out, not_9_out, not_10_out, not_11_out, not_12_out, not_13_out, not_14_out, not_15_out,
       not_16_out, not_17_out, not_18_out, not_19_out, not_20_out, not_21_out, not_22_out, not_23_out,
       not_24_out, not_25_out, not_26_out, not_27_out, not_28_out, not_29_out, not_30_out, not_31_out,
       not_32_out, not_33_out, not_34_out, not_35_out, not_36_out, not_37_out, not_38_out, not_39_out;

  not not_1 (not_1_out, op0);
  not not_2 (not_2_out, op1);
  not not_3 (not_3_out, op4);
  not not_4 (not_4_out, op0);
  not not_5 (not_5_out, op1);
  not not_6 (not_6_out, op3);
  not not_7 (not_7_out, op5);
  not not_8 (not_8_out, op0);
  not not_9 (not_9_out, op1);
  not not_10 (not_10_out, op3);
  not not_11 (not_11_out, op4);
  not not_12 (not_12_out, op0);
  not not_13 (not_13_out, op1);
  not not_14 (not_14_out, op4);
  not not_15 (not_15_out, op5);
  not not_16 (not_16_out, op1);
  not not_17 (not_17_out, op3);
  not not_18 (not_18_out, op0);
  not not_19 (not_19_out, op1);
  not not_20 (not_20_out, op4);
  not not_21 (not_21_out, op5);
  not not_22 (not_22_out, op0);
  not not_23 (not_23_out, op1);
  not not_24 (not_24_out, op3);
  not not_25 (not_25_out, op5);
  not not_26 (not_26_out, op0);
  not not_27 (not_27_out, op1);
  not not_28 (not_28_out, op3);
  not not_29 (not_29_out, op4);
  not not_30 (not_30_out, op0);
  not not_31 (not_31_out, op1);
  not not_32 (not_32_out, op3);
  not not_33 (not_33_out, op5);
  not not_34 (not_34_out, op0);
  not not_35 (not_35_out, op1);
  not not_36 (not_36_out, op4);
  not not_37 (not_37_out, op5);
  not not_38 (not_38_out, op1);
  not not_39 (not_39_out, op3);
  and and_1 (and_1_out, not_1_out, not_2_out, op2, op3, not_3_out, op5);
  and and_2 (and_2_out, not_4_out, not_5_out, op2, not_6_out, op4, not_7_out);
  and and_3 (and_3_out, not_8_out, not_9_out, op2, not_10_out, not_11_out);
  and and_4 (and_4_out, not_12_out, not_13_out, op2, not_14_out, not_15_out);
  and and_5 (and_5_out, op0, not_16_out, not_17_out, op4, op5);
  and and_6 (and_6_out, not_18_out, not_19_out, op2, op3, not_20_out, not_21_out);
  and and_7 (and_7_out, not_22_out, not_23_out, op2, not_24_out, op4, not_25_out);
  and and_8 (and_8_out, not_26_out, not_27_out, op2, not_28_out, not_29_out);
  and and_9 (and_9_out, not_30_out, not_31_out, op2, not_32_out, not_33_out);
  and and_10 (and_10_out, not_34_out, not_35_out, op2, not_36_out, not_37_out);
  and and_11 (and_11_out, op0, not_38_out, not_39_out, op4, op5);
  or or_1 (aluop0, and_1_out, and_2_out);
  or or_2 (aluop1, and_3_out, and_4_out, and_5_out);
  or or_3 (aluop2, and_6_out, and_7_out);
  or or_4 (aluop3, and_8_out, and_9_out, and_10_out, and_11_out);
endmodule

// ALU_Funct
module ALU_Funct_Decoder (
  input  funct0,
  input  funct1,
  input  funct2,
  input  funct3,
  input  funct4,
  input  funct5,
  output aluop0,
  output aluop1,
  output aluop2,
  output aluop3
);

  wire and_1_out, and_2_out, and_3_out, and_4_out, and_5_out, and_6_out, and_7_out, and_8_out, and_9_out,
       and_10_out, and_11_out, and_12_out, and_13_out, and_14_out, and_15_out, and_16_out, and_17_out,
       and_18_out, and_19_out, not_1_out, not_2_out, not_3_out, not_4_out, not_5_out, not_6_out, not_7_out,
       not_8_out, not_9_out, not_10_out, not_11_out, not_12_out, not_13_out, not_14_out, not_15_out,
       not_16_out, not_17_out, not_18_out, not_19_out, not_20_out, not_21_out, not_22_out, not_23_out,
       not_24_out, not_25_out, not_26_out, not_27_out, not_28_out, not_29_out, not_30_out, not_31_out,
       not_32_out, not_33_out, not_34_out, not_35_out, not_36_out, not_37_out, not_38_out, not_39_out,
       not_40_out, not_41_out, not_42_out, not_43_out, not_44_out, not_45_out, not_46_out, not_47_out,
       not_48_out, not_49_out, not_50_out, not_51_out, not_52_out, not_53_out, not_54_out, not_55_out,
       not_56_out, not_57_out, not_58_out, not_59_out, not_60_out, not_61_out, not_62_out, not_63_out,
       not_64_out, not_65_out, not_66_out, not_67_out;

  not not_1 (not_1_out, funct1);
  not not_2 (not_2_out, funct2);
  not not_3 (not_3_out, funct4);
  not not_4 (not_4_out, funct1);
  not not_5 (not_5_out, funct2);
  not not_6 (not_6_out, funct1);
  not not_7 (not_7_out, funct3);
  not not_8 (not_8_out, funct5);
  not not_9 (not_9_out, funct1);
  not not_10 (not_10_out, funct3);
  not not_11 (not_11_out, funct1);
  not not_12 (not_12_out, funct2);
  not not_13 (not_13_out, funct3);
  not not_14 (not_14_out, funct4);
  not not_15 (not_15_out, funct5);
  not not_16 (not_16_out, funct1);
  not not_17 (not_17_out, funct2);
  not not_18 (not_18_out, funct3);
  not not_19 (not_19_out, funct4);
  not not_20 (not_20_out, funct1);
  not not_21 (not_21_out, funct2);
  not not_22 (not_22_out, funct4);
  not not_23 (not_23_out, funct5);
  not not_24 (not_24_out, funct1);
  not not_25 (not_25_out, funct2);
  not not_26 (not_26_out, funct3);
  not not_27 (not_27_out, funct5);
  not not_28 (not_28_out, funct1);
  not not_29 (not_29_out, funct3);
  not not_30 (not_30_out, funct1);
  not not_31 (not_31_out, funct2);
  not not_32 (not_32_out, funct4);
  not not_33 (not_33_out, funct5);
  not not_34 (not_34_out, funct0);
  not not_35 (not_35_out, funct1);
  not not_36 (not_36_out, funct2);
  not not_37 (not_37_out, funct3);
  not not_38 (not_38_out, funct5);
  not not_39 (not_39_out, funct1);
  not not_40 (not_40_out, funct2);
  not not_41 (not_41_out, funct3);
  not not_42 (not_42_out, funct5);
  not not_43 (not_43_out, funct1);
  not not_44 (not_44_out, funct2);
  not not_45 (not_45_out, funct1);
  not not_46 (not_46_out, funct3);
  not not_47 (not_47_out, funct5);
  not not_48 (not_48_out, funct1);
  not not_49 (not_49_out, funct2);
  not not_50 (not_50_out, funct3);
  not not_51 (not_51_out, funct4);
  not not_52 (not_52_out, funct5);
  not not_53 (not_53_out, funct1);
  not not_54 (not_54_out, funct2);
  not not_55 (not_55_out, funct3);
  not not_56 (not_56_out, funct4);
  not not_57 (not_57_out, funct1);
  not not_58 (not_58_out, funct2);
  not not_59 (not_59_out, funct4);
  not not_60 (not_60_out, funct5);
  not not_61 (not_61_out, funct0);
  not not_62 (not_62_out, funct1);
  not not_63 (not_63_out, funct2);
  not not_64 (not_64_out, funct3);
  not not_65 (not_65_out, funct1);
  not not_66 (not_66_out, funct3);
  not not_67 (not_67_out, funct5);
  and and_1 (and_1_out, funct0, not_1_out, not_2_out, funct3, not_3_out, funct5);
  and and_2 (and_2_out, funct0, not_4_out, not_5_out, funct3, funct4, funct5);
  and and_3 (and_3_out, funct0, not_6_out, funct2, not_7_out, funct4, not_8_out);
  and and_4 (and_4_out, funct0, not_9_out, funct2, not_10_out, funct4, funct5);
  and and_5 (and_5_out, funct0, not_11_out, not_12_out, not_13_out, not_14_out, not_15_out);
  and and_6 (and_6_out, funct0, not_16_out, not_17_out, not_18_out, not_19_out, funct5);
  and and_7 (and_7_out, funct0, not_20_out, not_21_out, funct3, not_22_out, not_23_out);
  and and_8 (and_8_out, funct0, not_24_out, not_25_out, not_26_out, funct4, not_27_out);
  and and_9 (and_9_out, funct0, not_28_out, funct2, not_29_out, funct4, funct5);
  and and_10 (and_10_out, funct0, not_30_out, not_31_out, funct3, not_32_out, not_33_out);
  and and_11 (and_11_out, not_34_out, not_35_out, not_36_out, not_37_out, funct4, not_38_out);
  and and_12 (and_12_out, funct0, not_39_out, not_40_out, not_41_out, funct4, not_42_out);
  and and_13 (and_13_out, funct0, not_43_out, not_44_out, funct3, funct4, funct5);
  and and_14 (and_14_out, funct0, not_45_out, funct2, not_46_out, funct4, not_47_out);
  and and_15 (and_15_out, funct0, not_48_out, not_49_out, not_50_out, not_51_out, not_52_out);
  and and_16 (and_16_out, funct0, not_53_out, not_54_out, not_55_out, not_56_out, funct5);
  and and_17 (and_17_out, funct0, not_57_out, not_58_out, funct3, not_59_out, not_60_out);
  and and_18 (and_18_out, not_61_out, not_62_out, not_63_out, not_64_out, funct4, funct5);
  and and_19 (and_19_out, funct0, not_65_out, funct2, not_66_out, funct4, not_67_out);
  or or_1 (aluop0, and_1_out, and_2_out, and_3_out, and_4_out);
  or or_2 (aluop1, and_5_out, and_6_out, and_7_out, and_8_out, and_9_out);
  or or_3 (aluop2, and_10_out, and_11_out, and_12_out, and_13_out, and_14_out);
  or or_4 (aluop3, and_15_out, and_16_out, and_17_out, and_18_out, and_19_out);
endmodule

// Controlsignal_Op1
module Controlsignal_Op_Decoder1 (
  input  op0,
  input  op1,
  input  op2,
  input  op3,
  input  op4,
  input  op5,
  output R1,
  output R2,
  output W0,
  output W1,
  output Din0,
  output Din1,
  output SEXT0,
  output SEXT1,
  output A,
  output B
);

  wire and_2_out, and_3_out, and_4_out, and_5_out, and_6_out, and_7_out, and_10_out, and_11_out, and_12_out,
       and_13_out, and_14_out, and_15_out, and_16_out, not_1_out, not_2_out, not_3_out, not_4_out, not_5_out,
       not_6_out, not_7_out, not_8_out, not_9_out, not_10_out, not_11_out, not_12_out, not_13_out,
       not_14_out, not_15_out, not_16_out, not_17_out, not_18_out, not_19_out, not_20_out, not_21_out,
       not_22_out, not_23_out, not_24_out, not_25_out, not_26_out, not_27_out, not_28_out, not_29_out,
       not_30_out, not_31_out, not_32_out, not_33_out, not_34_out, not_35_out, not_36_out, not_37_out,
       not_38_out, not_39_out, not_40_out, not_41_out, not_42_out, not_43_out, not_44_out, not_45_out,
       not_46_out, not_47_out, not_48_out, not_49_out, not_50_out, not_51_out, not_52_out, not_53_out,
       not_54_out, not_55_out, not_56_out, not_57_out, not_58_out, not_59_out;

  not not_1 (not_1_out, op0);
  not not_2 (not_2_out, op1);
  not not_3 (not_3_out, op2);
  not not_4 (not_4_out, op3);
  not not_5 (not_5_out, op0);
  not not_6 (not_6_out, op1);
  not not_7 (not_7_out, op3);
  not not_8 (not_8_out, op4);
  not not_9 (not_9_out, op5);
  not not_10 (not_10_out, op0);
  not not_11 (not_11_out, op1);
  not not_12 (not_12_out, op3);
  not not_13 (not_13_out, op4);
  not not_14 (not_14_out, op0);
  not not_15 (not_15_out, op1);
  not not_16 (not_16_out, op4);
  not not_17 (not_17_out, op5);
  not not_18 (not_18_out, op0);
  not not_19 (not_19_out, op1);
  not not_20 (not_20_out, op4);
  not not_21 (not_21_out, op1);
  not not_22 (not_22_out, op2);
  not not_23 (not_23_out, op3);
  not not_24 (not_24_out, op0);
  not not_25 (not_25_out, op1);
  not not_26 (not_26_out, op3);
  not not_27 (not_27_out, op5);
  not not_28 (not_28_out, op0);
  not not_29 (not_29_out, op1);
  not not_30 (not_30_out, op2);
  not not_31 (not_31_out, op3);
  not not_32 (not_32_out, op1);
  not not_33 (not_33_out, op2);
  not not_34 (not_34_out, op3);
  not not_35 (not_35_out, op0);
  not not_36 (not_36_out, op1);
  not not_37 (not_37_out, op3);
  not not_38 (not_38_out, op4);
  not not_39 (not_39_out, op5);
  not not_40 (not_40_out, op0);
  not not_41 (not_41_out, op1);
  not not_42 (not_42_out, op3);
  not not_43 (not_43_out, op4);
  not not_44 (not_44_out, op0);
  not not_45 (not_45_out, op1);
  not not_46 (not_46_out, op4);
  not not_47 (not_47_out, op5);
  not not_48 (not_48_out, op0);
  not not_49 (not_49_out, op1);
  not not_50 (not_50_out, op4);
  not not_51 (not_51_out, op1);
  not not_52 (not_52_out, op2);
  not not_53 (not_53_out, op3);
  not not_54 (not_54_out, op1);
  not not_55 (not_55_out, op3);
  not not_56 (not_56_out, op0);
  not not_57 (not_57_out, op1);
  not not_58 (not_58_out, op3);
  not not_59 (not_59_out, op5);
  and and_1 (W0, not_1_out, not_2_out, not_3_out, not_4_out, op4, op5);
  and and_2 (and_2_out, not_5_out, not_6_out, op2, not_7_out, not_8_out, not_9_out);
  and and_3 (and_3_out, not_10_out, not_11_out, op2, not_12_out, not_13_out, op5);
  and and_4 (and_4_out, not_14_out, not_15_out, op2, op3, not_16_out, not_17_out);
  and and_5 (and_5_out, not_18_out, not_19_out, op2, op3, not_20_out, op5);
  and and_6 (and_6_out, op0, not_21_out, not_22_out, not_23_out, op4, op5);
  and and_7 (and_7_out, not_24_out, not_25_out, op2, not_26_out, op4, not_27_out);
  and and_8 (Din0, not_28_out, not_29_out, not_30_out, not_31_out, op4, op5);
  and and_9 (Din1, op0, not_32_out, not_33_out, not_34_out, op4, op5);
  and and_10 (and_10_out, not_35_out, not_36_out, op2, not_37_out, not_38_out, not_39_out);
  and and_11 (and_11_out, not_40_out, not_41_out, op2, not_42_out, not_43_out, op5);
  and and_12 (and_12_out, not_44_out, not_45_out, op2, op3, not_46_out, not_47_out);
  and and_13 (and_13_out, not_48_out, not_49_out, op2, op3, not_50_out, op5);
  and and_14 (and_14_out, op0, not_51_out, not_52_out, not_53_out, op4, op5);
  and and_15 (and_15_out, op0, not_54_out, op2, not_55_out, op4, op5);
  and and_16 (and_16_out, not_56_out, not_57_out, op2, not_58_out, op4, not_59_out);
  or or_1 (W1, and_2_out, and_3_out, and_4_out, and_5_out, and_6_out, and_7_out);
  or or_2 (B, and_10_out, and_11_out, and_12_out, and_13_out, and_14_out, and_15_out, and_16_out);

  assign A = 1'b0;
  assign R1 = 1'b0;
  assign R2 = 1'b0;
  assign SEXT0 = 1'b0;
  assign SEXT1 = 1'b0;
endmodule

// Controlsignal_Funct1
module Controlsignal_Funct_Decoder1 (
  input  funct0,
  input  funct1,
  input  funct2,
  input  funct3,
  input  funct4,
  input  funct5,
  output R1,
  output R2,
  output W0,
  output W1,
  output Din0,
  output Din1,
  output SEXT0,
  output SEXT1,
  output A,
  output B
);

  wire and_1_out, and_2_out, and_3_out, and_6_out, and_7_out, and_8_out, and_10_out, and_11_out, and_12_out,
       and_13_out, not_1_out, not_2_out, not_3_out, not_4_out, not_5_out, not_6_out, not_7_out, not_8_out,
       not_9_out, not_10_out, not_11_out, not_12_out, not_13_out, not_14_out, not_15_out, not_16_out,
       not_17_out, not_18_out, not_19_out, not_20_out, not_21_out, not_22_out, not_23_out, not_24_out,
       not_25_out, not_26_out, not_27_out, not_28_out, not_29_out, not_30_out, not_31_out, not_32_out,
       not_33_out, not_34_out, not_35_out, not_36_out, not_37_out, not_38_out, not_39_out, not_40_out,
       not_41_out, not_42_out, not_43_out, not_44_out, not_45_out, not_46_out, not_47_out, not_48_out,
       not_49_out, not_50_out, not_51_out, not_52_out, not_53_out, not_54_out, not_55_out, not_56_out,
       not_57_out, not_58_out, not_59_out, not_60_out, not_61_out;

  not not_1 (not_1_out, funct0);
  not not_2 (not_2_out, funct1);
  not not_3 (not_3_out, funct2);
  not not_4 (not_4_out, funct3);
  not not_5 (not_5_out, funct4);
  not not_6 (not_6_out, funct5);
  not not_7 (not_7_out, funct0);
  not not_8 (not_8_out, funct1);
  not not_9 (not_9_out, funct2);
  not not_10 (not_10_out, funct3);
  not not_11 (not_11_out, funct0);
  not not_12 (not_12_out, funct1);
  not not_13 (not_13_out, funct2);
  not not_14 (not_14_out, funct3);
  not not_15 (not_15_out, funct5);
  not not_16 (not_16_out, funct0);
  not not_17 (not_17_out, funct1);
  not not_18 (not_18_out, funct4);
  not not_19 (not_19_out, funct5);
  not not_20 (not_20_out, funct0);
  not not_21 (not_21_out, funct1);
  not not_22 (not_22_out, funct4);
  not not_23 (not_23_out, funct5);
  not not_24 (not_24_out, funct0);
  not not_25 (not_25_out, funct1);
  not not_26 (not_26_out, funct2);
  not not_27 (not_27_out, funct3);
  not not_28 (not_28_out, funct4);
  not not_29 (not_29_out, funct5);
  not not_30 (not_30_out, funct0);
  not not_31 (not_31_out, funct1);
  not not_32 (not_32_out, funct2);
  not not_33 (not_33_out, funct3);
  not not_34 (not_34_out, funct0);
  not not_35 (not_35_out, funct1);
  not not_36 (not_36_out, funct2);
  not not_37 (not_37_out, funct3);
  not not_38 (not_38_out, funct5);
  not not_39 (not_39_out, funct0);
  not not_40 (not_40_out, funct1);
  not not_41 (not_41_out, funct4);
  not not_42 (not_42_out, funct5);
  not not_43 (not_43_out, funct0);
  not not_44 (not_44_out, funct1);
  not not_45 (not_45_out, funct2);
  not not_46 (not_46_out, funct3);
  not not_47 (not_47_out, funct4);
  not not_48 (not_48_out, funct5);
  not not_49 (not_49_out, funct0);
  not not_50 (not_50_out, funct1);
  not not_51 (not_51_out, funct2);
  not not_52 (not_52_out, funct3);
  not not_53 (not_53_out, funct0);
  not not_54 (not_54_out, funct1);
  not not_55 (not_55_out, funct2);
  not not_56 (not_56_out, funct3);
  not not_57 (not_57_out, funct5);
  not not_58 (not_58_out, funct0);
  not not_59 (not_59_out, funct1);
  not not_60 (not_60_out, funct4);
  not not_61 (not_61_out, funct5);
  and and_1 (and_1_out, not_1_out, not_2_out, not_3_out, not_4_out, not_5_out, not_6_out);
  and and_2 (and_2_out, not_7_out, not_8_out, not_9_out, not_10_out, funct4, funct5);
  and and_3 (and_3_out, not_11_out, not_12_out, not_13_out, not_14_out, funct4, not_15_out);
  and and_4 (R2, not_16_out, not_17_out, funct2, funct3, not_18_out, not_19_out);
  and and_5 (SEXT0, not_20_out, not_21_out, funct2, funct3, not_22_out, not_23_out);
  and and_6 (and_6_out, not_24_out, not_25_out, not_26_out, not_27_out, not_28_out, not_29_out);
  and and_7 (and_7_out, not_30_out, not_31_out, not_32_out, not_33_out, funct4, funct5);
  and and_8 (and_8_out, not_34_out, not_35_out, not_36_out, not_37_out, funct4, not_38_out);
  and and_9 (A, not_39_out, not_40_out, funct2, funct3, not_41_out, not_42_out);
  and and_10 (and_10_out, not_43_out, not_44_out, not_45_out, not_46_out, not_47_out, not_48_out);
  and and_11 (and_11_out, not_49_out, not_50_out, not_51_out, not_52_out, funct4, funct5);
  and and_12 (and_12_out, not_53_out, not_54_out, not_55_out, not_56_out, funct4, not_57_out);
  and and_13 (and_13_out, not_58_out, not_59_out, funct2, funct3, not_60_out, not_61_out);
  or or_1 (R1, and_1_out, and_2_out, and_3_out);
  or or_2 (SEXT1, and_6_out, and_7_out, and_8_out);
  or or_3 (B, and_10_out, and_11_out, and_12_out, and_13_out);

  assign Din0 = 1'b0;
  assign Din1 = 1'b0;
  assign W0 = 1'b0;
  assign W1 = 1'b0;
endmodule

// Controlsignal_Op2
module Controlsignal_Op_Decoder2 (
  input  op0,
  input  op1,
  input  op2,
  input  op3,
  input  op4,
  input  op5,
  output JR,
  output Branch,
  output Jump,
  output RegWrite,
  output MemRead,
  output MemWrite,
  output MemtoReg,
  output IsBNE,
  output isSyscall
);

  wire and_1_out, and_2_out, and_3_out, and_4_out, and_5_out, and_6_out, and_7_out, not_1_out, not_2_out,
       not_3_out, not_4_out, not_5_out, not_6_out, not_7_out, not_8_out, not_9_out, not_10_out, not_11_out,
       not_12_out, not_13_out, not_14_out, not_15_out, not_16_out, not_17_out, not_18_out, not_19_out,
       not_20_out, not_21_out, not_22_out, not_23_out, not_24_out, not_25_out, not_26_out, not_27_out,
       not_28_out, not_29_out, not_30_out, not_31_out, not_32_out, not_33_out, not_34_out, not_35_out,
       not_36_out, not_37_out, not_38_out, not_39_out, not_40_out;

  not not_1 (not_1_out, op0);
  not not_2 (not_2_out, op1);
  not not_3 (not_3_out, op2);
  not not_4 (not_4_out, op4);
  not not_5 (not_5_out, op0);
  not not_6 (not_6_out, op1);
  not not_7 (not_7_out, op2);
  not not_8 (not_8_out, op4);
  not not_9 (not_9_out, op5);
  not not_10 (not_10_out, op0);
  not not_11 (not_11_out, op1);
  not not_12 (not_12_out, op2);
  not not_13 (not_13_out, op3);
  not not_14 (not_14_out, op5);
  not not_15 (not_15_out, op0);
  not not_16 (not_16_out, op1);
  not not_17 (not_17_out, op2);
  not not_18 (not_18_out, op3);
  not not_19 (not_19_out, op1);
  not not_20 (not_20_out, op2);
  not not_21 (not_21_out, op3);
  not not_22 (not_22_out, op0);
  not not_23 (not_23_out, op1);
  not not_24 (not_24_out, op3);
  not not_25 (not_25_out, op5);
  not not_26 (not_26_out, op0);
  not not_27 (not_27_out, op1);
  not not_28 (not_28_out, op4);
  not not_29 (not_29_out, op1);
  not not_30 (not_30_out, op2);
  not not_31 (not_31_out, op3);
  not not_32 (not_32_out, op1);
  not not_33 (not_33_out, op3);
  not not_34 (not_34_out, op1);
  not not_35 (not_35_out, op2);
  not not_36 (not_36_out, op3);
  not not_37 (not_37_out, op0);
  not not_38 (not_38_out, op1);
  not not_39 (not_39_out, op2);
  not not_40 (not_40_out, op4);
  and and_1 (and_1_out, not_1_out, not_2_out, not_3_out, op3, not_4_out, op5);
  and and_2 (and_2_out, not_5_out, not_6_out, not_7_out, op3, not_8_out, not_9_out);
  and and_3 (and_3_out, not_10_out, not_11_out, not_12_out, not_13_out, op4, not_14_out);
  and and_4 (and_4_out, not_15_out, not_16_out, not_17_out, not_18_out, op4, op5);
  and and_5 (and_5_out, not_19_out, not_20_out, not_21_out, op4, op5);
  and and_6 (and_6_out, not_22_out, not_23_out, op2, not_24_out, not_25_out);
  and and_7 (and_7_out, not_26_out, not_27_out, op2, not_28_out);
  and and_8 (MemRead, op0, not_29_out, not_30_out, not_31_out, op4, op5);
  and and_9 (MemWrite, op0, not_32_out, op2, not_33_out, op4, op5);
  and and_10 (MemtoReg, op0, not_34_out, not_35_out, not_36_out, op4, op5);
  and and_11 (IsBNE, not_37_out, not_38_out, not_39_out, op3, not_40_out, op5);
  or or_1 (Branch, and_1_out, and_2_out);
  or or_2 (Jump, and_3_out, and_4_out);
  or or_3 (RegWrite, and_5_out, and_6_out, and_7_out);

  assign isSyscall = 1'b0;
  assign JR = 1'b0;
endmodule

// Controlsignal_Funct2
module Controlsignal_Funct_Decoder2 (
  input  funct0,
  input  funct1,
  input  funct2,
  input  funct3,
  input  funct4,
  input  funct5,
  output JR,
  output Branch,
  output Jump,
  output RegWrite,
  output MemRead,
  output MemWrite,
  output MemtoReg,
  output IsBNE,
  output IsSyscall
);

  wire and_2_out, and_3_out, and_4_out, and_5_out, and_6_out, not_1_out, not_2_out, not_3_out, not_4_out,
       not_5_out, not_6_out, not_7_out, not_8_out, not_9_out, not_10_out, not_11_out, not_12_out, not_13_out,
       not_14_out, not_15_out, not_16_out, not_17_out, not_18_out, not_19_out, not_20_out, not_21_out,
       not_22_out, not_23_out, not_24_out;

  not not_1 (not_1_out, funct0);
  not not_2 (not_2_out, funct1);
  not not_3 (not_3_out, funct3);
  not not_4 (not_4_out, funct4);
  not not_5 (not_5_out, funct5);
  not not_6 (not_6_out, funct1);
  not not_7 (not_7_out, funct2);
  not not_8 (not_8_out, funct3);
  not not_9 (not_9_out, funct5);
  not not_10 (not_10_out, funct0);
  not not_11 (not_11_out, funct1);
  not not_12 (not_12_out, funct2);
  not not_13 (not_13_out, funct3);
  not not_14 (not_14_out, funct1);
  not not_15 (not_15_out, funct2);
  not not_16 (not_16_out, funct4);
  not not_17 (not_17_out, funct1);
  not not_18 (not_18_out, funct2);
  not not_19 (not_19_out, funct1);
  not not_20 (not_20_out, funct3);
  not not_21 (not_21_out, funct0);
  not not_22 (not_22_out, funct1);
  not not_23 (not_23_out, funct4);
  not not_24 (not_24_out, funct5);
  and and_1 (JR, not_1_out, not_2_out, funct2, not_3_out, not_4_out, not_5_out);
  and and_2 (and_2_out, not_6_out, not_7_out, not_8_out, not_9_out);
  and and_3 (and_3_out, not_10_out, not_11_out, not_12_out, not_13_out, funct4);
  and and_4 (and_4_out, funct0, not_14_out, not_15_out, not_16_out);
  and and_5 (and_5_out, funct0, not_17_out, not_18_out, funct3, funct5);
  and and_6 (and_6_out, funct0, not_19_out, funct2, not_20_out, funct4);
  and and_7 (IsSyscall, not_21_out, not_22_out, funct2, funct3, not_23_out, not_24_out);
  or or_1 (RegWrite, and_2_out, and_3_out, and_4_out, and_5_out, and_6_out);

  assign Branch = 1'b0;
  assign IsBNE = 1'b0;
  assign Jump = 1'b0;
  assign MemRead = 1'b0;
  assign MemtoReg = 1'b0;
  assign MemWrite = 1'b0;
endmodule

module Syscall (
  input  IsSyscall,
  input  CLK,
  input  [31:0] v0,
  output Disp,
  output Halt
);

  wire and_2_out, comparator_1_eq, not_1_out;

  not not_1 (not_1_out, comparator_1_eq);
  Comparator #(.width(32)) comparator_1 (.a(32'ha), .b(v0), .eq(comparator_1_eq));  // open: gt, lt
  and and_1 (Disp, IsSyscall, not_1_out);
  and and_2 (and_2_out, IsSyscall, comparator_1_eq);
  D_Flip_Flop d_ff_1 (.clk(CLK), .D(and_2_out), .Q(Halt));  // open: Qn, preset, en, reset
endmodule

module Hazard_Unit (
  input  [4:0] RsD,
  input  [4:0] WriteRegM,
  input  [4:0] RtD,
  input  [1:0] MemtoRegE,
  input  [4:0] RsE,
  input  RegWriteE,
  input  [4:0] RtE,
  input  RegWriteM,
  input  BranchE,
  input  RegWriteW,
  input  [4:0] WriteRegE,
  input  [4:0] WriteRegW,
  output StallF,
  output StatID,
  output ForwardAD,
  output ForwardBD,
  output FlushE,
  output [1:0] ForwardAE,
  output [1:0] ForwardBE
);

  wire and_1_out, and_2_out, and_3_out, and_4_out, and_5_out, and_6_out, comparator_1_gt, comparator_1_lt,
       comparator_2_eq, comparator_3_gt, comparator_3_lt, comparator_4_eq, comparator_5_gt, comparator_5_lt,
       comparator_6_eq, comparator_7_gt, comparator_7_lt, comparator_8_eq, comparator_9_gt, comparator_9_lt,
       comparator_10_eq, comparator_11_gt, comparator_11_lt, comparator_12_eq, or_1_out, or_2_out, or_3_out,
       or_4_out, or_5_out, or_6_out;

  Comparator #(.width(5)) comparator_1 (
    .a(RsD), .b({5{1'b0}}), .gt(comparator_1_gt), .lt(comparator_1_lt));  // open: eq
  Comparator #(.width(5)) comparator_2 (.a(RsD), .b(WriteRegW), .eq(comparator_2_eq));  // open: gt, lt
  Comparator #(.width(5)) comparator_3 (
    .a(RsD), .b({5{1'b0}}), .gt(comparator_3_gt), .lt(comparator_3_lt));  // open: eq
  Comparator #(.width(5)) comparator_4 (.a(RsD), .b(WriteRegM), .eq(comparator_4_eq));  // open: gt, lt
  Comparator #(.width(5)) comparator_5 (
    .a(RsD), .b({5{1'b0}}), .gt(comparator_5_gt), .lt(comparator_5_lt));  // open: eq
  Comparator #(.width(5)) comparator_6 (.a(RsD), .b(WriteRegE), .eq(comparator_6_eq));  // open: gt, lt
  Comparator #(.width(5)) comparator_7 (
    .a(RtD), .b({5{1'b0}}), .gt(comparator_7_gt), .lt(comparator_7_lt));  // open: eq
  Comparator #(.width(5)) comparator_8 (.a(RtD), .b(WriteRegW), .eq(comparator_8_eq));  // open: gt, lt
  Comparator #(.width(5)) comparator_9 (
    .a(RtD), .b({5{1'b0}}), .gt(comparator_9_gt), .lt(comparator_9_lt));  // open: eq
  Comparator #(.width(5)) comparator_10 (.a(RtD), .b(WriteRegM), .eq(comparator_10_eq));  // open: gt, lt
  Comparator #(.width(5)) comparator_11 (
    .a(RtD), .b({5{1'b0}}), .gt(comparator_11_gt), .lt(comparator_11_lt));  // open: eq
  Comparator #(.width(5)) comparator_12 (.a(RtD), .b(WriteRegE), .eq(comparator_12_eq));  // open: gt, lt
  or or_1 (or_1_out, comparator_1_gt, comparator_1_lt);
  or or_2 (or_2_out, comparator_3_gt, comparator_3_lt);
  or or_3 (or_3_out, comparator_5_gt, comparator_5_lt);
  or or_4 (or_4_out, comparator_7_gt, comparator_7_lt);
  or or_5 (or_5_out, comparator_9_gt, comparator_9_lt);
  or or_6 (or_6_out, comparator_11_gt, comparator_11_lt);
  and and_1 (and_1_out, or_1_out, comparator_2_eq, RegWriteW);
  and and_2 (and_2_out, or_2_out, comparator_4_eq, RegWriteM);
  and and_3 (and_3_out, or_3_out, comparator_6_eq, RegWriteE);
  and and_4 (and_4_out, or_4_out, comparator_8_eq, RegWriteW);
  and and_5 (and_5_out, or_5_out, comparator_10_eq, RegWriteM);
  and and_6 (and_6_out, or_6_out, comparator_12_eq, RegWriteE);
  or or_7 (FlushE, and_1_out, and_2_out, and_3_out, and_4_out, and_5_out, and_6_out);
  not not_1 (StallF, FlushE);

  assign StatID = StallF;

  // Other names for the same wires on the sheet: StallD = StallF
endmodule

module statics (
  input  op0,
  input  op1,
  input  op2,
  input  op3,
  input  op4,
  input  op5,
  output R,
  output I,
  output J
);

  wire and_2_out, and_3_out, and_4_out, and_5_out, and_6_out, and_7_out, and_8_out, and_9_out, and_10_out,
       and_11_out, and_12_out, not_1_out, not_2_out, not_3_out, not_4_out, not_5_out, not_6_out, not_7_out,
       not_8_out, not_9_out, not_10_out, not_11_out, not_12_out, not_13_out, not_14_out, not_15_out,
       not_16_out, not_17_out, not_18_out, not_19_out, not_20_out, not_21_out, not_22_out, not_23_out,
       not_24_out, not_25_out, not_26_out, not_27_out, not_28_out, not_29_out, not_30_out, not_31_out,
       not_32_out, not_33_out, not_34_out, not_35_out, not_36_out, not_37_out, not_38_out, not_39_out,
       not_40_out, not_41_out, not_42_out, not_43_out, not_44_out, not_45_out, not_46_out, not_47_out,
       not_48_out, not_49_out;

  not not_1 (not_1_out, op0);
  not not_2 (not_2_out, op1);
  not not_3 (not_3_out, op2);
  not not_4 (not_4_out, op3);
  not not_5 (not_5_out, op4);
  not not_6 (not_6_out, op5);
  not not_7 (not_7_out, op0);
  not not_8 (not_8_out, op1);
  not not_9 (not_9_out, op3);
  not not_10 (not_10_out, op4);
  not not_11 (not_11_out, op5);
  not not_12 (not_12_out, op0);
  not not_13 (not_13_out, op1);
  not not_14 (not_14_out, op3);
  not not_15 (not_15_out, op4);
  not not_16 (not_16_out, op0);
  not not_17 (not_17_out, op1);
  not not_18 (not_18_out, op4);
  not not_19 (not_19_out, op5);
  not not_20 (not_20_out, op0);
  not not_21 (not_21_out, op1);
  not not_22 (not_22_out, op4);
  not not_23 (not_23_out, op1);
  not not_24 (not_24_out, op2);
  not not_25 (not_25_out, op3);
  not not_26 (not_26_out, op1);
  not not_27 (not_27_out, op3);
  not not_28 (not_28_out, op0);
  not not_29 (not_29_out, op1);
  not not_30 (not_30_out, op2);
  not not_31 (not_31_out, op4);
  not not_32 (not_32_out, op0);
  not not_33 (not_33_out, op1);
  not not_34 (not_34_out, op2);
  not not_35 (not_35_out, op4);
  not not_36 (not_36_out, op5);
  not not_37 (not_37_out, op0);
  not not_38 (not_38_out, op1);
  not not_39 (not_39_out, op3);
  not not_40 (not_40_out, op5);
  not not_41 (not_41_out, op0);
  not not_42 (not_42_out, op1);
  not not_43 (not_43_out, op2);
  not not_44 (not_44_out, op3);
  not not_45 (not_45_out, op0);
  not not_46 (not_46_out, op1);
  not not_47 (not_47_out, op2);
  not not_48 (not_48_out, op3);
  not not_49 (not_49_out, op5);
  and and_1 (R, not_1_out, not_2_out, not_3_out, not_4_out, not_5_out, not_6_out);
  and and_2 (and_2_out, not_7_out, not_8_out, op2, not_9_out, not_10_out, not_11_out);
  and and_3 (and_3_out, not_12_out, not_13_out, op2, not_14_out, not_15_out, op5);
  and and_4 (and_4_out, not_16_out, not_17_out, op2, op3, not_18_out, not_19_out);
  and and_5 (and_5_out, not_20_out, not_21_out, op2, op3, not_22_out, op5);
  and and_6 (and_6_out, op0, not_23_out, not_24_out, not_25_out, op4, op5);
  and and_7 (and_7_out, op0, not_26_out, op2, not_27_out, op4, op5);
  and and_8 (and_8_out, not_28_out, not_29_out, not_30_out, op3, not_31_out, op5);
  and and_9 (and_9_out, not_32_out, not_33_out, not_34_out, op3, not_35_out, not_36_out);
  and and_10 (and_10_out, not_37_out, not_38_out, op2, not_39_out, op4, not_40_out);
  and and_11 (and_11_out, not_41_out, not_42_out, not_43_out, not_44_out, op4, op5);
  and and_12 (and_12_out, not_45_out, not_46_out, not_47_out, not_48_out, op4, not_49_out);
  or or_1 (I, and_2_out, and_3_out, and_4_out, and_5_out, and_6_out, and_7_out, and_8_out, and_9_out, and_10_out);
  or or_2 (J, and_11_out, and_12_out);
endmodule
