// Logisim project MIPS CPU_pipelined_redirection_withinterruption.circ as structural Verilog: 20 circuits, main circuit main
module main (
);

  wire ALUSrcA, ALUSrcB, Branch, BranchE, Button1, Button2, Button3, Cause, CLK, clk_t, comparator_1_eq,
       comparator_2_eq, control_unit_1_alusrca, control_unit_1_alusrcb, control_unit_1_branch,
       control_unit_1_isbne, control_unit_1_iseret, control_unit_1_isspecial, control_unit_1_jr,
       control_unit_1_jump, control_unit_1_memread, control_unit_1_memwrite, control_unit_1_r1_num,
       control_unit_1_r2_num, control_unit_1_regwrite, Disp, EqualE, ex_mem_1_eretm, ex_mem_1_issyscallm,
       ex_mem_1_mfc0m, Halt, HaltW, hazard_unit_1_flushd, hazard_unit_1_flushe, hazard_unit_1_flushm,
       hazard_unit_1_stalld, hazard_unit_1_stallex, hazard_unit_1_stallf, hazard_unit_1_stallmem,
       id_ex_1_memwritee, Interrupt, IsBNE, IsERET, IsERETW, IsSpecial, IsSyscallD, IsSyscallE, JR, Jump,
       mem_wb_1_issyscallw, MemReadE, MemReadM, MemWriteM, MFC0, MFC0W, MTC0, multiplexer_2_out,
       multiplexer_7_out, not_1_out, not_2_out, not_3_out, not_4_out, RegWriteE, RegWriteM, RegWriteW,
       RsRead, RtRead, Shield;
  wire [1:0] control_unit_1_memtoreg, control_unit_1_regdes, ex_mem_1_memtoregm, hazard_unit_1_redirr1,
       hazard_unit_1_redirr2, mem_wb_1_memtoregw, MemtoRegE, RegDst, S_EXT;
  wire [3:0] ALUControl, control_unit_1_aluctrl;
  wire [4:0] ex_mem_1_writeregm, id_ex_1_rte, if_id_1_instrd_2, mem_wb_1_writeregw, multiplexer_11_out, rd,
       regdst_1_r1_dst, regdst_1_r2_dst, rs, rt;
  wire [9:0] demultiplexer_1_out0, demultiplexer_1_out1;
  wire [15:0] counter_1_q, multiplexer_6_out;
  wire [27:0] id_ex_1_pcplus4e;
  wire [31:0] a0, adder_1_out, adder_2_out, alu_1_result, bit_extender_1_out, CP0R1, CP0R1W,
       ex_mem_1_aluoutm, ex_mem_1_cp0r1m, ex_mem_1_pcplus4m, ex_mem_1_writedatam, id_ex_1_jumpaddre,
       id_ex_1_r1e, id_ex_1_signlmme, if_id_1_instrd, if_id_1_pcplus4d, Instruction, InterruptNumButton,
       InterruptNumCP0, main_1_reg1, main_1_reg2_2, mem_wb_1_aluoutw, mem_wb_1_pcplus4w, mem_wb_1_readdataw,
       multiplexer_1_out, multiplexer_4_out, multiplexer_5_out, multiplexer_8_out, multiplexer_9_out,
       multiplexer_10_out, multiplexer_12_out, multiplexer_13_out, multiplexer_14_out, multiplexer_15_out,
       PC_4, PC_q, PCout, R2, ram_1_data, register_2_q, rom_1_data, rom_2_data, shifter_1_out, v0;

  not not_1 (not_1_out, Halt);
  Multiplexer #(.width(32)) multiplexer_1 (
    .in0(multiplexer_4_out), .in1(PCout), .out(multiplexer_1_out), .sel(IsERETW), .en(1'b1));
  assign CLK = not_1_out ? clk_t : 1'bz;  // Controlled_Buffer controlled_buffer_1
  Register #(.width(32)) PC (
    .D(multiplexer_1_out), .en(hazard_unit_1_stallf), .Q(PC_q), .clk(multiplexer_2_out), .clr(Cause));
  Multiplexer multiplexer_2 (.in0(CLK), .in1(not_2_out), .out(multiplexer_2_out), .sel(IsERETW), .en(1'b1));
  not not_2 (not_2_out, CLK);
  Counter #(.width(16), .max('hffff)) counter_1 (.Q(counter_1_q), .clk(CLK));  // open: load, D, count, carry, clr
  Demultiplexer #(.width(10)) demultiplexer_1 (
    .out0(demultiplexer_1_out0), .out1(demultiplexer_1_out1), .in(PC_q[11:2]), .sel(Interrupt), .en(1'b1));
  Hazard_Unit hazard_unit_1 (
    .StallF(hazard_unit_1_stallf), .StallD(hazard_unit_1_stalld), .RsD(regdst_1_r1_dst), .RtD(rt),
    .FlushE(hazard_unit_1_flushe), .RsE(rs), .RtE(id_ex_1_rte), .BranchE(BranchE),
    .WriteRegE(multiplexer_11_out), .WriteRegM(ex_mem_1_writeregm), .MemtoRegE(MemtoRegE),
    .RegWriteE(RegWriteE), .RegWriteM(RegWriteM), .RegWriteW(RegWriteW), .WriteRegW(mem_wb_1_writeregw),
    .MemWriteM(MemWriteM), .FlushD(hazard_unit_1_flushd), .FlushM(hazard_unit_1_flushm),
    .StallEX(hazard_unit_1_stallex), .IsSyscallE(IsSyscallE), .IsSyscallD(IsSyscallD), .CLK(CLK),
    .StallMem(hazard_unit_1_stallmem), .Jump(Jump), .JR(JR), .RsRead(RsRead), .RtRead(RtRead),
    .RedirR1(hazard_unit_1_redirr1), .RedirR2(hazard_unit_1_redirr2), .MemReadE(MemReadE), .MemReadM(MemReadM));
  Adder #(.width(32)) adder_1 (.a(PC_q), .b(32'h4), .out(adder_1_out));  // open: cin, cout
  Clock clock_1 (.out(clk_t));
  ROM #(.addrWidth(10), .dataWidth(32)) rom_1 (.addr(demultiplexer_1_out0), .data(rom_1_data));  // open: sel
  ROM #(.addrWidth(10), .dataWidth(32)) rom_2 (.addr(demultiplexer_1_out1), .data(rom_2_data));  // open: sel
  Comparator #(.width(16)) comparator_1 (.a(counter_1_q), .b(16'h1aff), .eq(comparator_1_eq));  // open: gt, lt
  Multiplexer #(.width(32)) multiplexer_3 (
    .in0(rom_1_data), .in1(rom_2_data), .out(Instruction), .sel(Interrupt), .en(1'b1));
  Register #(.width(32)) register_1 (.D(adder_1_out), .en(1'b1), .Q(PC_4), .clk(Cause));  // open: clr
  ButtonCtrl buttonctrl_1 (
    .Button1(Button1), .Button2(Button2), .Shield(Shield), .Button3(Button3), .Halt(Halt),
    .InterruptNumOut(InterruptNumButton), .Cause(Cause), .InterruptNumIn(InterruptNumCP0));
  or or_1 (Halt, comparator_1_eq, HaltW);
  Multiplexer #(.width(32)) multiplexer_4 (
    .in0(multiplexer_5_out), .in1(id_ex_1_r1e), .out(multiplexer_4_out), .sel(JR), .en(1'b1));
  // Probe on counter_1_q
  Comparator #(.width(32)) comparator_2 (
    .a({32{1'b0}}), .b({if_id_1_instrd[31:26], if_id_1_instrd_2, rt, if_id_1_instrd[15:0]}),
    .eq(comparator_2_eq));  // open: gt, lt
  IF_ID if_id_1 (
    .InstrF(Instruction), .PCPlus4F(adder_1_out),
    .InstrD({if_id_1_instrd[31:26], if_id_1_instrd_2, rt, if_id_1_instrd[15:0]}),
    .PCPlus4D(if_id_1_pcplus4d), .CLK(CLK), .CLR(hazard_unit_1_flushd), .EN(hazard_unit_1_stalld));
  Multiplexer #(.width(32)) multiplexer_5 (
    .in0(multiplexer_8_out), .in1(id_ex_1_jumpaddre), .out(multiplexer_5_out), .sel(Jump), .en(1'b1));
  Control_Unit control_unit_1 (
    .OP(if_id_1_instrd[31:26]), .Funct(if_id_1_instrd[5:0]), .R1_num(control_unit_1_r1_num),
    .R2_num(control_unit_1_r2_num), .AluCtrl(control_unit_1_aluctrl), .RegDes(control_unit_1_regdes),
    .S_EXT(S_EXT), .AluSrcA(control_unit_1_alusrca), .AluSrcB(control_unit_1_alusrcb),
    .JR(control_unit_1_jr), .Branch(control_unit_1_branch), .Jump(control_unit_1_jump),
    .RegWrite(control_unit_1_regwrite), .MemRead(control_unit_1_memread), .MemWrite(control_unit_1_memwrite),
    .MemtoReg(control_unit_1_memtoreg), .IsBNE(control_unit_1_isbne), .IsSyscall(IsSyscallD),
    .IsSpecial(control_unit_1_isspecial), .IsERET(control_unit_1_iseret), .CLR(comparator_2_eq),
    .RsRead(RsRead), .RtRead(RtRead), .Rs(if_id_1_instrd_2));
  RegDst regdst_1 (
    .Rs(if_id_1_instrd_2), .Rt(rt), .R1_Dst(regdst_1_r1_dst), .R2_Dst(regdst_1_r2_dst),
    .R1_num(control_unit_1_r1_num), .R2_num(control_unit_1_r2_num));
  Multiplexer #(.select(2), .width(16)) multiplexer_6 (
    .in0(if_id_1_instrd[15:0]), .in1({{11{1'b0}}, if_id_1_instrd[10:6]}), .in2(16'ha),
    .out(multiplexer_6_out), .sel(S_EXT), .en(1'b1));  // open: in3
  Shifter #(.width(32)) shifter_1 (.in(id_ex_1_signlmme), .\dist (5'b00010), .out(shifter_1_out));
  not not_3 (not_3_out, EqualE);
  assign bit_extender_1_out = {{16{multiplexer_6_out[15]}}, multiplexer_6_out};  // Bit_Extender bit_extender_1
  Adder #(.width(32)) adder_2 (
    .a({id_ex_1_jumpaddre[31:28], id_ex_1_pcplus4e}), .b(shifter_1_out), .out(adder_2_out), .cin(1'b0));  // open: cout
  Multiplexer multiplexer_7 (.in0(EqualE), .in1(not_3_out), .out(multiplexer_7_out), .sel(IsBNE), .en(1'b1));
  not not_4 (not_4_out, CLK);
  CP0 cp0_1 (
    .IsERET(IsERETW), .CP0Din(R2), .PCin(PC_4), .CP0R1(CP0R1), .IsSpecial(IsSpecial), .CP0R1_num(rd),
    .CP0W_num(rd), .Cause(Cause), .PCout(PCout), .Clk(CLK), .Instruction(rs), .Shield(Shield), .MFC0(MFC0),
    .MTC0(MTC0), .Interrupt(Interrupt), .InterruptNumIn(InterruptNumButton), .InterruptNumOut(InterruptNumCP0));
  and and_1 (BranchE, Branch, multiplexer_7_out);
  regfile_main main_1 (
    .Reg1_num(regdst_1_r1_dst), .Reg2(regdst_1_r2_dst), .Write_Reg_num(mem_wb_1_writeregw),
    .Din(multiplexer_15_out), .Write_Enable(RegWriteW), .Clock(not_4_out), .Reg1(main_1_reg1),
    .Reg2_2(main_1_reg2_2), .a0_Value(a0), .v0_Value(v0));  // open: s0_Value, ra_Value
  Multiplexer #(.width(32)) multiplexer_8 (
    .in0(adder_1_out), .in1(adder_2_out), .out(multiplexer_8_out), .sel(BranchE), .en(1'b1));
  Multiplexer #(.select(2), .width(32)) multiplexer_9 (
    .in0(main_1_reg1), .in1(ex_mem_1_aluoutm), .in2(ram_1_data), .in3(multiplexer_14_out),
    .out(multiplexer_9_out), .sel(hazard_unit_1_redirr1), .en(1'b1));
  Multiplexer #(.select(2), .width(32)) multiplexer_10 (
    .in0(main_1_reg2_2), .in1(ex_mem_1_aluoutm), .in2(ram_1_data), .in3(multiplexer_14_out),
    .out(multiplexer_10_out), .sel(hazard_unit_1_redirr2), .en(1'b1));
  ID_EX id_ex_1 (
    .CLK(CLK), .R1D(multiplexer_9_out), .R2D(multiplexer_10_out), .R1E(id_ex_1_r1e), .R2E(R2),
    .RegWriteD(control_unit_1_regwrite), .MemtoRegD(control_unit_1_memtoreg),
    .MemWriteD(control_unit_1_memwrite), .ALUControlD(control_unit_1_aluctrl),
    .ALUSrcAD(control_unit_1_alusrca), .ALUSrcBD(control_unit_1_alusrcb), .JRD(control_unit_1_jr),
    .BranchD(control_unit_1_branch), .JumpD(control_unit_1_jump), .MemReadD(control_unit_1_memread),
    .IsBNED(control_unit_1_isbne), .IsSyscallD(IsSyscallD), .IsSpecialD(control_unit_1_isspecial),
    .IsERETD(control_unit_1_iseret), .RegDstD(control_unit_1_regdes), .RegWriteE(RegWriteE),
    .MemtoRegE(MemtoRegE), .MemReadE(MemReadE), .MemWriteE(id_ex_1_memwritee), .ALUControlE(ALUControl),
    .ALUSrcAE(ALUSrcA), .ALUSrcBE(ALUSrcB), .BranchE(Branch), .JRE(JR), .JumpE(Jump), .IsBNEE(IsBNE),
    .IsSyscallE(IsSyscallE), .IsSpecialE(IsSpecial), .IsERETE(IsERET), .RegDst(RegDst),
    .RsD(regdst_1_r1_dst), .RtD(rt), .RdD(if_id_1_instrd[15:11]), .SignlmmD(bit_extender_1_out), .RsE(rs),
    .RtE(id_ex_1_rte), .RdE(rd), .SignlmmE(id_ex_1_signlmme), .CLR(hazard_unit_1_flushe),
    .PCPlus4D(if_id_1_pcplus4d), .PCPlus4E({id_ex_1_jumpaddre[31:28], id_ex_1_pcplus4e}),
    .JumpAddrD({if_id_1_instrd_2, rt, if_id_1_instrd[15:0], 2'b00}), .JumpAddrE(id_ex_1_jumpaddre[27:0]),
    .EN(hazard_unit_1_stallex));
  Hex_Digit_Display hex_digit_display_1 (.value(register_2_q[31:28]), .dp(1'b0));
  Register #(.width(32)) register_2 (.D(a0), .en(Disp), .Q(register_2_q), .clk(CLK), .clr(1'b0));
  Hex_Digit_Display hex_digit_display_2 (.value(register_2_q[23:20]), .dp(1'b0));
  Hex_Digit_Display hex_digit_display_3 (.value(register_2_q[27:24]), .dp(1'b0));
  Multiplexer #(.select(2), .width(5)) multiplexer_11 (
    .in0(rd), .in1(id_ex_1_rte), .in2({5{1'b1}}), .out(multiplexer_11_out), .sel(RegDst), .en(1'b1));  // open: in3
  Hex_Digit_Display hex_digit_display_4 (.value(register_2_q[15:12]), .dp(1'b0));
  Hex_Digit_Display hex_digit_display_5 (.value(register_2_q[19:16]), .dp(1'b0));
  Multiplexer #(.width(32)) multiplexer_12 (
    .in0(id_ex_1_r1e), .in1(R2), .out(multiplexer_12_out), .sel(ALUSrcA), .en(1'b1));
  Multiplexer #(.width(32)) multiplexer_13 (
    .in0(R2), .in1(id_ex_1_signlmme), .out(multiplexer_13_out), .sel(ALUSrcB), .en(1'b1));
  Hex_Digit_Display hex_digit_display_6 (.value(register_2_q[7:4]), .dp(1'b0));
  Hex_Digit_Display hex_digit_display_7 (.value(register_2_q[11:8]), .dp(1'b0));
  Comparator #(.width(32)) comparator_3 (.a(id_ex_1_r1e), .b(R2), .eq(EqualE));  // open: gt, lt
  ALU alu_1 (
    .AluOP(ALUControl), .X(multiplexer_12_out), .Result(alu_1_result), .Y(multiplexer_13_out));  // open: Equal, Signed_Overflow, Result_2, UnSigned_Overflow
  Hex_Digit_Display hex_digit_display_8 (.value(register_2_q[3:0]), .dp(1'b0));
  Multiplexer #(.width(32)) multiplexer_14 (
    .in0(alu_1_result), .in1(CP0R1), .out(multiplexer_14_out), .sel(MFC0), .en(1'b1));
  Button button_1 (.out(Button1));
  EX_MEM ex_mem_1 (
    .CLK(CLK), .ALUOutE(multiplexer_14_out), .WriteDataE(R2), .WriteRegE(multiplexer_11_out),
    .ALUOutM(ex_mem_1_aluoutm), .WriteDataM(ex_mem_1_writedatam), .WriteRegM(ex_mem_1_writeregm),
    .RegWriteE(RegWriteE), .MemtoRegE(MemtoRegE), .MemReadE(MemReadE), .MemWriteE(id_ex_1_memwritee),
    .RegWriteM(RegWriteM), .MemtoRegM(ex_mem_1_memtoregm), .MemReadM(MemReadM), .MemWriteM(MemWriteM),
    .CLR(hazard_unit_1_flushm), .PCPlus4E({id_ex_1_jumpaddre[31:28], id_ex_1_pcplus4e}),
    .PCPlus4M(ex_mem_1_pcplus4m), .EN(hazard_unit_1_stallmem), .IsSyscallE(IsSyscallE),
    .IsSyscallM(ex_mem_1_issyscallm), .MFC0E(MFC0), .MFC0M(ex_mem_1_mfc0m), .ERETE(IsERET),
    .ERETM(ex_mem_1_eretm), .CP0R1E(CP0R1), .CP0R1M(ex_mem_1_cp0r1m));
  Button button_2 (.out(Button2));
  Button button_3 (.out(Button3));
  RAM #(.addrWidth(16), .dataWidth(32), .bus("separate")) ram_1 (
    .addr(ex_mem_1_aluoutm[17:2]), .din(ex_mem_1_writedatam), .data(ram_1_data), .str(MemWriteM), .sel(1'b1),
    .clk(CLK), .ld(MemReadM), .clr(1'b0));
  MEM_WB mem_wb_1 (
    .CLK(CLK), .ReadDataM(ram_1_data), .ALUOutM(ex_mem_1_aluoutm), .WriteRegM(ex_mem_1_writeregm),
    .ReadDataW(mem_wb_1_readdataw), .ALUOutW(mem_wb_1_aluoutw), .WriteRegW(mem_wb_1_writeregw),
    .RegWriteM(RegWriteM), .MemtoRegM(ex_mem_1_memtoregm), .RegWriteW(RegWriteW),
    .MemtoRegW(mem_wb_1_memtoregw), .PCPlus4M(ex_mem_1_pcplus4m), .PCPlus4W(mem_wb_1_pcplus4w),
    .IsSyscallM(ex_mem_1_issyscallm), .IsSyscallW(mem_wb_1_issyscallw), .MFC0M(ex_mem_1_mfc0m),
    .MFC0W(MFC0W), .ERETM(ex_mem_1_eretm), .ERETW(IsERETW), .CP0R1M(ex_mem_1_cp0r1m), .CP0R1W(CP0R1W));
  Syscall syscall_1 (.IsSyscall(mem_wb_1_issyscallw), .v0(v0), .Disp(Disp), .CLK(CLK), .Halt(HaltW));
  Multiplexer #(.select(2), .width(32)) multiplexer_15 (
    .in0(mem_wb_1_aluoutw), .in1(mem_wb_1_readdataw), .in2(mem_wb_1_pcplus4w), .out(multiplexer_15_out),
    .sel(mem_wb_1_memtoregw), .en(1'b1));  // open: in3

  // Notes on the sheet:
  //   StallF
  //   contents of rom_1 (hex, n*v repeats v):
  //   20100001 109fc0 139fc3 8021 2012000c 24160003 26100001 3210000f 20080008 20090001 139900 2709825
  //   132020 20020022 c 1094022 1500fff9 22100001 2018000f 2188024 108700 20080008 20090001 139902 2709825
  //   132021 20020022 c 1094022 1500fff9 108702 2c9b022 12c00001 8000c06 4020 1084027 84400 3508ffff 82021
  //   20020022 c 2002000a c
  //   contents of rom_2 (hex, n*v repeats v):
  //   201a0001 409af000 201c0040 39df020 afd00000 23bd0004 23de0004 afd20000 23bd0004 23de0004 afd30000
  //   23bd0004 23de0004 afd40000 23bd0004 23de0004 afd50000 23bd0004 23de0004 afd60000 23bd0004 23de0004
  //   afc80000 23bd0004 23de0004 afc90000 23bd0004 23de0004 afc40000 23bd0004 23de0004 afc20000 23bd0004
  //   23de0004 4009f800 afc90000 23de0004 23bd0004 201a0000 409af000 4016b000 20140005 20150001 168020
  //   102020 20020022 c 108100 1600fffb 295a022 1680fff8 201a0001 409af000 23defffc 23bdfffc 8fc90000
  //   4089f800 23defffc 23bdfffc 8fc20000 23defffc 23bdfffc 8fc40000 23defffc 23bdfffc 8fc90000 23defffc
  //   23bdfffc 8fc80000 23defffc 23bdfffc 8fd60000 23defffc 23bdfffc 8fd50000 23defffc 23bdfffc 8fd40000
  //   23defffc 23bdfffc 8fd30000 23defffc 23bdfffc 8fd20000 23defffc 23bdfffc 8fd00000 201a0000 409af000
  //   42000018
  //   FlushD
  //   StallD
  //   RsD
  //   SignlmmD
  //   PCPlus4D
  //   FlushE
  //   WriteDataE
  //   WriteRegE
  //   ALUOutE
  //   PCPlus4E
  //   ReadDataM
  //   ALUOutM
  //   WriteRegM
  //   PCPlus4M
  //   ResultW
endmodule

module RegDst (
  input  [4:0] Rs,
  input  [4:0] Rt,
  input  R1_num,
  input  R2_num,
  output [4:0] R1_Dst,
  output [4:0] R2_Dst
);

  wire [4:0] multiplexer_1_out;

  Multiplexer #(.width(5)) multiplexer_1 (.in0(Rs), .in1(Rt), .out(multiplexer_1_out), .sel(R1_num), .en(1'b1));
  Multiplexer #(.width(5)) multiplexer_2 (
    .in0(multiplexer_1_out), .in1(5'b00100), .out(R1_Dst), .sel(R2_num), .en(1'b1));
  Multiplexer #(.width(5)) multiplexer_3 (.in0(Rt), .in1(5'b00010), .out(R2_Dst), .sel(R2_num), .en(1'b1));
endmodule

module IF_ID (
  input  CLR,
  input  EN,
  input  CLK,
  input  [31:0] InstrF,
  input  [31:0] PCPlus4F,
  output [31:0] InstrD,
  output [31:0] PCPlus4D
);

  wire [31:0] multiplexer_1_out, multiplexer_2_out;

  Multiplexer #(.width(32)) multiplexer_1 (
    .in0(InstrF), .in1({32{1'b0}}), .out(multiplexer_1_out), .sel(CLR), .en(1'b1));
  Multiplexer #(.width(32)) multiplexer_2 (
    .in0(PCPlus4F), .in1({32{1'b0}}), .out(multiplexer_2_out), .sel(CLR), .en(1'b1));
  Register #(.width(32)) register_1 (.D(multiplexer_1_out), .en(EN), .Q(InstrD), .clk(CLK));  // open: clr
  Register #(.width(32)) register_2 (.D(multiplexer_2_out), .en(EN), .Q(PCPlus4D), .clk(CLK));  // open: clr
endmodule

module ID_EX (
  input  CLR,
  input  EN,
  input  CLK,
  input  RegWriteD,
  input  [1:0] MemtoRegD,
  input  MemReadD,
  input  MemWriteD,
  input  [3:0] ALUControlD,
  input  ALUSrcAD,
  input  ALUSrcBD,
  input  BranchD,
  input  JRD,
  input  JumpD,
  input  IsBNED,
  input  IsSyscallD,
  input  IsSpecialD,
  input  IsERETD,
  input  [1:0] RegDstD,
  input  [31:0] R1D,
  input  [31:0] R2D,
  input  [4:0] RsD,
  input  [4:0] RtD,
  input  [4:0] RdD,
  input  [31:0] SignlmmD,
  input  [31:0] PCPlus4D,
  input  [27:0] JumpAddrD,
  output RegWriteE,
  output [1:0] MemtoRegE,
  output MemReadE,
  output MemWriteE,
  output [3:0] ALUControlE,
  output ALUSrcAE,
  output ALUSrcBE,
  output BranchE,
  output JRE,
  output JumpE,
  output IsBNEE,
  output IsSyscallE,
  output IsSpecialE,
  output IsERETE,
  output [1:0] RegDst,
  output [31:0] R1E,
  output [31:0] R2E,
  output [4:0] RsE,
  output [4:0] RtE,
  output [4:0] RdE,
  output [31:0] SignlmmE,
  output [31:0] PCPlus4E,
  output [27:0] JumpAddrE
);

  wire multiplexer_1_out, multiplexer_3_out, multiplexer_4_out, multiplexer_6_out, multiplexer_7_out,
       multiplexer_8_out, multiplexer_9_out, multiplexer_10_out, multiplexer_11_out, multiplexer_12_out,
       multiplexer_13_out, multiplexer_14_out;
  wire [1:0] multiplexer_2_out, multiplexer_15_out;
  wire [3:0] multiplexer_5_out;
  wire [4:0] multiplexer_18_out, multiplexer_19_out, multiplexer_20_out;
  wire [27:0] multiplexer_23_out;
  wire [31:0] multiplexer_16_out, multiplexer_17_out, multiplexer_21_out, multiplexer_22_out;

  Multiplexer multiplexer_1 (.in0(RegWriteD), .in1(1'b0), .out(multiplexer_1_out), .sel(CLR), .en(1'b1));
  Multiplexer #(.width(2)) multiplexer_2 (.in0(MemtoRegD), .in1(2'b00), .out(multiplexer_2_out), .sel(CLR), .en(1'b1));
  Multiplexer multiplexer_3 (.in0(MemReadD), .in1(1'b0), .out(multiplexer_3_out), .sel(CLR), .en(1'b1));
  Multiplexer multiplexer_4 (.in0(MemWriteD), .in1(1'b0), .out(multiplexer_4_out), .sel(CLR), .en(1'b1));
  Multiplexer #(.width(4)) multiplexer_5 (
    .in0(ALUControlD), .in1(4'b0000), .out(multiplexer_5_out), .sel(CLR), .en(1'b1));
  Multiplexer multiplexer_6 (.in0(ALUSrcAD), .in1(1'b0), .out(multiplexer_6_out), .sel(CLR), .en(1'b1));
  Multiplexer multiplexer_7 (.in0(ALUSrcBD), .in1(1'b1), .out(multiplexer_7_out), .sel(CLR), .en(1'b1));
  Multiplexer multiplexer_8 (.in0(BranchD), .in1(1'b0), .out(multiplexer_8_out), .sel(CLR), .en(1'b1));
  Multiplexer multiplexer_9 (.in0(JRD), .in1(1'b0), .out(multiplexer_9_out), .sel(CLR), .en(1'b1));
  Multiplexer multiplexer_10 (.in0(JumpD), .in1(1'b0), .out(multiplexer_10_out), .sel(CLR), .en(1'b1));
  Multiplexer multiplexer_11 (.in0(IsBNED), .in1(1'b0), .out(multiplexer_11_out), .sel(CLR), .en(1'b1));
  Multiplexer multiplexer_12 (.in0(IsSyscallD), .in1(1'b0), .out(multiplexer_12_out), .sel(CLR), .en(1'b1));
  Multiplexer multiplexer_13 (.in0(IsSpecialD), .in1(1'b0), .out(multiplexer_13_out), .sel(CLR), .en(1'b1));
  Multiplexer multiplexer_14 (.in0(IsERETD), .in1(1'b0), .out(multiplexer_14_out), .sel(CLR), .en(1'b1));
  Multiplexer #(.width(2)) multiplexer_15 (.in0(RegDstD), .in1(2'b00), .out(multiplexer_15_out), .sel(CLR), .en(1'b1));
  Multiplexer #(.width(32)) multiplexer_16 (
    .in0(R1D), .in1({32{1'b0}}), .out(multiplexer_16_out), .sel(CLR), .en(1'b1));
  Multiplexer #(.width(32)) multiplexer_17 (
    .in0(R2D), .in1({32{1'b0}}), .out(multiplexer_17_out), .sel(CLR), .en(1'b1));
  Multiplexer #(.width(5)) multiplexer_18 (.in0(RsD), .in1({5{1'b0}}), .out(multiplexer_18_out), .sel(CLR), .en(1'b1));
  Multiplexer #(.width(5)) multiplexer_19 (.in0(RtD), .in1({5{1'b0}}), .out(multiplexer_19_out), .sel(CLR), .en(1'b1));
  Multiplexer #(.width(5)) multiplexer_20 (.in0(RdD), .in1({5{1'b0}}), .out(multiplexer_20_out), .sel(CLR), .en(1'b1));
  Multiplexer #(.width(32)) multiplexer_21 (
    .in0(SignlmmD), .in1({32{1'b0}}), .out(multiplexer_21_out), .sel(CLR), .en(1'b1));
  Multiplexer #(.width(32)) multiplexer_22 (
    .in0(PCPlus4D), .in1({32{1'b0}}), .out(multiplexer_22_out), .sel(CLR), .en(1'b1));
  Multiplexer #(.width(28)) multiplexer_23 (
    .in0(JumpAddrD), .in1({28{1'b0}}), .out(multiplexer_23_out), .sel(CLR), .en(1'b1));
  Register #(.width(1)) register_1 (.D(multiplexer_1_out), .en(EN), .Q(RegWriteE), .clk(CLK));  // open: clr
  Register #(.width(2)) register_2 (.D(multiplexer_2_out), .en(EN), .Q(MemtoRegE), .clk(CLK));  // open: clr
  Register #(.width(1)) register_3 (.D(multiplexer_3_out), .en(EN), .Q(MemReadE), .clk(CLK));  // open: clr
  Register #(.width(1)) register_4 (.D(multiplexer_4_out), .en(EN), .Q(MemWriteE), .clk(CLK));  // open: clr
  Register #(.width(4)) register_5 (.D(multiplexer_5_out), .en(EN), .Q(ALUControlE), .clk(CLK));  // open: clr
  Register #(.width(1)) register_6 (.D(multiplexer_6_out), .en(EN), .Q(ALUSrcAE), .clk(CLK));  // open: clr
  Register #(.width(1)) register_7 (.D(multiplexer_7_out), .en(EN), .Q(ALUSrcBE), .clk(CLK));  // open: clr
  Register #(.width(1)) register_8 (.D(multiplexer_8_out), .en(EN), .Q(BranchE), .clk(CLK));  // open: clr
  Register #(.width(1)) register_9 (.D(multiplexer_9_out), .en(EN), .Q(JRE), .clk(CLK));  // open: clr
  Register #(.width(1)) register_10 (.D(multiplexer_10_out), .en(EN), .Q(JumpE), .clk(CLK));  // open: clr
  Register #(.width(1)) register_11 (.D(multiplexer_11_out), .en(EN), .Q(IsBNEE), .clk(CLK));  // open: clr
  Register #(.width(1)) register_12 (.D(multiplexer_12_out), .en(EN), .Q(IsSyscallE), .clk(CLK));  // open: clr
  Register #(.width(1)) register_13 (.D(multiplexer_13_out), .en(EN), .Q(IsSpecialE), .clk(CLK));  // open: clr
  Register #(.width(1)) register_14 (.D(multiplexer_14_out), .en(EN), .Q(IsERETE), .clk(CLK));  // open: clr
  Register #(.width(2)) register_15 (.D(multiplexer_15_out), .en(EN), .Q(RegDst), .clk(CLK));  // open: clr
  Register #(.width(32)) register_16 (.D(multiplexer_16_out), .en(EN), .Q(R1E), .clk(CLK));  // open: clr
  Register #(.width(32)) register_17 (.D(multiplexer_17_out), .en(EN), .Q(R2E), .clk(CLK));  // open: clr
  Register #(.width(5)) register_18 (.D(multiplexer_18_out), .en(EN), .Q(RsE), .clk(CLK));  // open: clr
  Register #(.width(5)) register_19 (.D(multiplexer_19_out), .en(EN), .Q(RtE), .clk(CLK));  // open: clr
  Register #(.width(5)) register_20 (.D(multiplexer_20_out), .en(EN), .Q(RdE), .clk(CLK));  // open: clr
  Register #(.width(32)) register_21 (.D(multiplexer_21_out), .en(EN), .Q(SignlmmE), .clk(CLK));  // open: clr
  Register #(.width(32)) register_22 (.D(multiplexer_22_out), .en(EN), .Q(PCPlus4E), .clk(CLK));  // open: clr
  Register #(.width(28)) register_23 (.D(multiplexer_23_out), .en(EN), .Q(JumpAddrE), .clk(CLK));  // open: clr
endmodule

module EX_MEM (
  input  CLR,
  input  EN,
  input  CLK,
  input  RegWriteE,
  input  [1:0] MemtoRegE,
  input  MemReadE,
  input  MemWriteE,
  input  [31:0] ALUOutE,
  input  [31:0] WriteDataE,
  input  [4:0] WriteRegE,
  input  [31:0] PCPlus4E,
  input  IsSyscallE,
  input  MFC0E,
  input  ERETE,
  input  [31:0] CP0R1E,
  output RegWriteM,
  output [1:0] MemtoRegM,
  output MemReadM,
  output MemWriteM,
  output [31:0] ALUOutM,
  output [31:0] WriteDataM,
  output [4:0] WriteRegM,
  output [31:0] PCPlus4M,
  output IsSyscallM,
  output MFC0M,
  output ERETM,
  output [31:0] CP0R1M
);

  wire multiplexer_1_out, multiplexer_3_out, multiplexer_4_out, multiplexer_9_out, multiplexer_10_out,
       multiplexer_11_out;
  wire [1:0] multiplexer_2_out;
  wire [4:0] multiplexer_7_out;
  wire [31:0] multiplexer_5_out, multiplexer_6_out, multiplexer_8_out, multiplexer_12_out;

  Multiplexer multiplexer_1 (.in0(RegWriteE), .in1(1'b0), .out(multiplexer_1_out), .sel(CLR), .en(1'b1));
  Multiplexer #(.width(2)) multiplexer_2 (.in0(MemtoRegE), .in1(2'b00), .out(multiplexer_2_out), .sel(CLR), .en(1'b1));
  Multiplexer multiplexer_3 (.in0(MemReadE), .in1(1'b0), .out(multiplexer_3_out), .sel(CLR), .en(1'b1));
  Multiplexer multiplexer_4 (.in0(MemWriteE), .in1(1'b0), .out(multiplexer_4_out), .sel(CLR), .en(1'b1));
  Multiplexer #(.width(32)) multiplexer_5 (
    .in0(ALUOutE), .in1({32{1'b0}}), .out(multiplexer_5_out), .sel(CLR), .en(1'b1));
  Multiplexer #(.width(32)) multiplexer_6 (
    .in0(WriteDataE), .in1({32{1'b0}}), .out(multiplexer_6_out), .sel(CLR), .en(1'b1));
  Multiplexer #(.width(5)) multiplexer_7 (
    .in0(WriteRegE), .in1({5{1'b0}}), .out(multiplexer_7_out), .sel(CLR), .en(1'b1));
  Multiplexer #(.width(32)) multiplexer_8 (
    .in0(PCPlus4E), .in1({32{1'b0}}), .out(multiplexer_8_out), .sel(CLR), .en(1'b1));
  Multiplexer multiplexer_9 (.in0(IsSyscallE), .in1(1'b0), .out(multiplexer_9_out), .sel(CLR), .en(1'b1));
  Multiplexer multiplexer_10 (.in0(MFC0E), .in1(1'b0), .out(multiplexer_10_out), .sel(CLR), .en(1'b1));
  Multiplexer multiplexer_11 (.in0(ERETE), .in1(1'b0), .out(multiplexer_11_out), .sel(CLR), .en(1'b1));
  Multiplexer #(.width(32)) multiplexer_12 (
    .in0(CP0R1E), .in1({32{1'b0}}), .out(multiplexer_12_out), .sel(CLR), .en(1'b1));
  Register #(.width(1)) register_1 (.D(multiplexer_1_out), .en(EN), .Q(RegWriteM), .clk(CLK));  // open: clr
  Register #(.width(2)) register_2 (.D(multiplexer_2_out), .en(EN), .Q(MemtoRegM), .clk(CLK));  // open: clr
  Register #(.width(1)) register_3 (.D(multiplexer_3_out), .en(EN), .Q(MemReadM), .clk(CLK));  // open: clr
  Register #(.width(1)) register_4 (.D(multiplexer_4_out), .en(EN), .Q(MemWriteM), .clk(CLK));  // open: clr
  Register #(.width(32)) register_5 (.D(multiplexer_5_out), .en(EN), .Q(ALUOutM), .clk(CLK));  // open: clr
  Register #(.width(32)) register_6 (.D(multiplexer_6_out), .en(EN), .Q(WriteDataM), .clk(CLK));  // open: clr
  Register #(.width(5)) register_7 (.D(multiplexer_7_out), .en(EN), .Q(WriteRegM), .clk(CLK));  // open: clr
  Register #(.width(32)) register_8 (.D(multiplexer_8_out), .en(EN), .Q(PCPlus4M), .clk(CLK));  // open: clr
  Register #(.width(1)) register_9 (.D(multiplexer_9_out), .en(EN), .Q(IsSyscallM), .clk(CLK));  // open: clr
  Register #(.width(1)) register_10 (.D(multiplexer_10_out), .en(EN), .Q(MFC0M), .clk(CLK));  // open: clr
  Register #(.width(1)) register_11 (.D(multiplexer_11_out), .en(EN), .Q(ERETM), .clk(CLK));  // open: clr
  Register #(.width(32)) register_12 (.D(multiplexer_12_out), .en(EN), .Q(CP0R1M), .clk(CLK));  // open: clr
endmodule

module MEM_WB (
  input  CLK,
  input  RegWriteM,
  input  [1:0] MemtoRegM,
  input  [31:0] ReadDataM,
  input  [31:0] ALUOutM,
  input  [4:0] WriteRegM,
  input  [31:0] PCPlus4M,
  input  IsSyscallM,
  input  MFC0M,
  input  ERETM,
  input  [31:0] CP0R1M,
  output RegWriteW,
  output [1:0] MemtoRegW,
  output [31:0] ReadDataW,
  output [31:0] ALUOutW,
  output [4:0] WriteRegW,
  output [31:0] PCPlus4W,
  output IsSyscallW,
  output MFC0W,
  output ERETW,
  output [31:0] CP0R1W
);

  Register #(.width(1)) register_1 (.D(RegWriteM), .Q(RegWriteW), .clk(CLK));  // open: en, clr
  Register #(.width(2)) register_2 (.D(MemtoRegM), .Q(MemtoRegW), .clk(CLK));  // open: en, clr
  Register #(.width(32)) register_3 (.D(ReadDataM), .Q(ReadDataW), .clk(CLK));  // open: en, clr
  Register #(.width(32)) register_4 (.D(ALUOutM), .Q(ALUOutW), .clk(CLK));  // open: en, clr
  Register #(.width(5)) register_5 (.D(WriteRegM), .Q(WriteRegW), .clk(CLK));  // open: en, clr
  Register #(.width(32)) register_6 (.D(PCPlus4M), .Q(PCPlus4W), .clk(CLK));  // open: en, clr
  Register #(.width(1)) register_7 (.D(IsSyscallM), .Q(IsSyscallW), .clk(CLK));  // open: en, clr
  Register #(.width(1)) register_8 (.D(MFC0M), .Q(MFC0W), .clk(CLK));  // open: en, clr
  Register #(.width(1)) register_9 (.D(ERETM), .Q(ERETW), .clk(CLK));  // open: en, clr
  Register #(.width(32)) register_10 (.D(CP0R1M), .Q(CP0R1W), .clk(CLK));  // open: en, clr
endmodule

module Control_Unit (
  input  [5:0] OP,
  input  CLR,
  input  [5:0] Funct,
  input  [4:0] Rs,
  output RegWrite,
  output [1:0] MemtoReg,
  output MemRead,
  output MemWrite,
  output [3:0] AluCtrl,
  output AluSrcA,
  output AluSrcB,
  output Branch,
  output JR,
  output Jump,
  output IsBNE,
  output IsSyscall,
  output IsSpecial,
  output IsERET,
  output [1:0] RegDes,
  output R1_num,
  output R2_num,
  output [1:0] S_EXT,
  output RsRead,
  output RtRead
);

  wire and_1_out, and_2_out, and_3_out, and_4_out, and_5_out, and_6_out, and_7_out, and_8_out, and_12_out,
       controlsignal_funct_decoder1_1_a, controlsignal_funct_decoder1_1_b, controlsignal_funct_decoder1_1_r1,
       controlsignal_funct_decoder1_1_r2, controlsignal_funct_decoder2_1_branch,
       controlsignal_funct_decoder2_1_isbne, controlsignal_funct_decoder2_1_issyscall,
       controlsignal_funct_decoder2_1_jr, controlsignal_funct_decoder2_1_jump,
       controlsignal_funct_decoder2_1_memread, controlsignal_funct_decoder2_1_memtoreg,
       controlsignal_funct_decoder2_1_memwrite, controlsignal_funct_decoder2_1_regwrite,
       controlsignal_op_decoder1_1_a, controlsignal_op_decoder1_1_b, controlsignal_op_decoder1_1_r1,
       controlsignal_op_decoder1_1_r2, controlsignal_op_decoder2_1_branch, controlsignal_op_decoder2_1_isbne,
       controlsignal_op_decoder2_1_issyscall, controlsignal_op_decoder2_1_jr,
       controlsignal_op_decoder2_1_jump, controlsignal_op_decoder2_1_memread,
       controlsignal_op_decoder2_1_memtoreg, controlsignal_op_decoder2_1_memwrite,
       controlsignal_op_decoder2_1_regwrite, Is_R_Type, MemtoReg_t, MFC0, multiplexer_13_out,
       multiplexer_20_out, nor_2_out, not_1_out, not_2_out, not_3_out, not_4_out, not_5_out, not_6_out,
       not_7_out, not_8_out, not_9_out, not_10_out, not_11_out, not_12_out, not_13_out, not_14_out,
       not_15_out, not_16_out, not_17_out, not_18_out, not_19_out, not_20_out, not_21_out, not_22_out,
       not_23_out, not_24_out, not_25_out, not_26_out, not_27_out, not_28_out, not_29_out, not_30_out,
       not_31_out, not_32_out, not_33_out, not_34_out, RegWrite_t, rtrsread_funct_1_rsread,
       rtrsread_funct_1_rtread, rtrsread_op_1_rsread, rtrsread_op_1_rtread;
  wire [1:0] controlsignal_funct_decoder1_1_din1, controlsignal_funct_decoder1_1_sext1,
       controlsignal_funct_decoder1_1_w1, controlsignal_op_decoder1_1_din1,
       controlsignal_op_decoder1_1_sext1, controlsignal_op_decoder1_1_w1, W1;
  wire [3:0] alu_funct_decoder_1_aluop3, alu_op_decoder_1_aluop3;

  ALU_Op_Decoder alu_op_decoder_1 (
    .op0(OP[5]), .op1(OP[4]), .op2(OP[3]), .op3(OP[2]), .op4(OP[1]), .op5(OP[0]),
    .aluop0(alu_op_decoder_1_aluop3[3]), .aluop1(alu_op_decoder_1_aluop3[2]),
    .aluop2(alu_op_decoder_1_aluop3[1]), .aluop3(alu_op_decoder_1_aluop3[0]));
  ALU_Funct_Decoder alu_funct_decoder_1 (
    .funct0(Funct[5]), .funct1(Funct[4]), .funct2(Funct[3]), .funct3(Funct[2]), .funct4(Funct[1]),
    .funct5(Funct[0]), .aluop0(alu_funct_decoder_1_aluop3[3]), .aluop1(alu_funct_decoder_1_aluop3[2]),
    .aluop2(alu_funct_decoder_1_aluop3[1]), .aluop3(alu_funct_decoder_1_aluop3[0]));
  Controlsignal_Op_Decoder1 controlsignal_op_decoder1_1 (
    .op0(OP[5]), .op1(OP[4]), .op2(OP[3]), .op3(OP[2]), .op4(OP[1]), .op5(OP[0]),
    .R1(controlsignal_op_decoder1_1_r1), .R2(controlsignal_op_decoder1_1_r2),
    .W0(controlsignal_op_decoder1_1_w1[1]), .W1(controlsignal_op_decoder1_1_w1[0]),
    .Din0(controlsignal_op_decoder1_1_din1[1]), .Din1(controlsignal_op_decoder1_1_din1[0]),
    .SEXT0(controlsignal_op_decoder1_1_sext1[1]), .SEXT1(controlsignal_op_decoder1_1_sext1[0]),
    .A(controlsignal_op_decoder1_1_a), .B(controlsignal_op_decoder1_1_b));
  Controlsignal_Funct_Decoder1 controlsignal_funct_decoder1_1 (
    .funct0(Funct[5]), .funct1(Funct[4]), .funct2(Funct[3]), .funct3(Funct[2]), .funct4(Funct[1]),
    .funct5(Funct[0]), .R1(controlsignal_funct_decoder1_1_r1), .R2(controlsignal_funct_decoder1_1_r2),
    .W0(controlsignal_funct_decoder1_1_w1[1]), .W1(controlsignal_funct_decoder1_1_w1[0]),
    .Din0(controlsignal_funct_decoder1_1_din1[1]), .Din1(controlsignal_funct_decoder1_1_din1[0]),
    .SEXT0(controlsignal_funct_decoder1_1_sext1[1]), .SEXT1(controlsignal_funct_decoder1_1_sext1[0]),
    .A(controlsignal_funct_decoder1_1_a), .B(controlsignal_funct_decoder1_1_b));
  Controlsignal_Op_Decoder2 controlsignal_op_decoder2_1 (
    .op0(OP[5]), .op1(OP[4]), .op2(OP[3]), .op3(OP[2]), .op4(OP[1]), .op5(OP[0]),
    .JR(controlsignal_op_decoder2_1_jr), .Branch(controlsignal_op_decoder2_1_branch),
    .Jump(controlsignal_op_decoder2_1_jump), .RegWrite(controlsignal_op_decoder2_1_regwrite),
    .MemRead(controlsignal_op_decoder2_1_memread), .MemWrite(controlsignal_op_decoder2_1_memwrite),
    .MemtoReg(controlsignal_op_decoder2_1_memtoreg), .IsBNE(controlsignal_op_decoder2_1_isbne),
    .isSyscall(controlsignal_op_decoder2_1_issyscall));
  Controlsignal_Funct_Decoder2 controlsignal_funct_decoder2_1 (
    .funct0(Funct[5]), .funct1(Funct[4]), .funct2(Funct[3]), .funct3(Funct[2]), .funct4(Funct[1]),
    .funct5(Funct[0]), .JR(controlsignal_funct_decoder2_1_jr),
    .Branch(controlsignal_funct_decoder2_1_branch), .Jump(controlsignal_funct_decoder2_1_jump),
    .RegWrite(controlsignal_funct_decoder2_1_regwrite), .MemRead(controlsignal_funct_decoder2_1_memread),
    .MemWrite(controlsignal_funct_decoder2_1_memwrite), .MemtoReg(controlsignal_funct_decoder2_1_memtoreg),
    .IsBNE(controlsignal_funct_decoder2_1_isbne), .IsSyscall(controlsignal_funct_decoder2_1_issyscall));
  RtRsRead_Op rtrsread_op_1 (
    .op0(OP[5]), .op1(OP[4]), .op2(OP[3]), .op3(OP[2]), .op4(OP[1]), .op5(OP[0]),
    .rsread(rtrsread_op_1_rsread), .rtread(rtrsread_op_1_rtread));
  RtRsRead_Funct rtrsread_funct_1 (
    .funct0(Funct[5]), .funct1(Funct[4]), .funct2(Funct[3]), .funct3(Funct[2]), .funct4(Funct[1]),
    .funct5(Funct[0]), .rsread(rtrsread_funct_1_rsread), .rtread(rtrsread_funct_1_rtread));
  not not_1 (not_1_out, Rs[4]);
  not not_2 (not_2_out, Rs[3]);
  not not_3 (not_3_out, Rs[1]);
  not not_4 (not_4_out, Rs[0]);
  not not_5 (not_5_out, Rs[4]);
  not not_6 (not_6_out, Rs[3]);
  not not_7 (not_7_out, Rs[2]);
  not not_8 (not_8_out, Rs[1]);
  not not_9 (not_9_out, Rs[0]);
  not not_10 (not_10_out, OP[5]);
  not not_11 (not_11_out, OP[3]);
  not not_12 (not_12_out, OP[2]);
  not not_13 (not_13_out, OP[1]);
  not not_14 (not_14_out, OP[0]);
  not not_15 (not_15_out, OP[5]);
  not not_16 (not_16_out, OP[3]);
  not not_17 (not_17_out, OP[2]);
  not not_18 (not_18_out, OP[1]);
  not not_19 (not_19_out, OP[0]);
  not not_20 (not_20_out, Funct[5]);
  not not_21 (not_21_out, Funct[2]);
  not not_22 (not_22_out, Funct[1]);
  not not_23 (not_23_out, Funct[0]);
  not not_24 (not_24_out, OP[5]);
  not not_25 (not_25_out, OP[3]);
  not not_26 (not_26_out, OP[2]);
  not not_27 (not_27_out, OP[1]);
  not not_28 (not_28_out, OP[0]);
  not not_29 (not_29_out, Funct[5]);
  not not_30 (not_30_out, Funct[4]);
  not not_31 (not_31_out, Funct[3]);
  not not_32 (not_32_out, Funct[2]);
  not not_33 (not_33_out, Funct[1]);
  not not_34 (not_34_out, Funct[0]);
  nor nor_1 (Is_R_Type, OP[5], OP[4], OP[3], OP[2], OP[1], OP[0]);
  and and_1 (and_1_out, not_1_out, not_2_out, Rs[2], not_3_out, not_4_out);
  and and_2 (and_2_out, not_5_out, not_6_out, not_7_out, not_8_out, not_9_out);
  and and_3 (and_3_out, not_10_out, OP[4], not_11_out, not_12_out, not_13_out, not_14_out);
  nor nor_2 (nor_2_out, Funct[5], Funct[4], Funct[3]);
  and and_4 (and_4_out, not_15_out, OP[4], not_16_out, not_17_out, not_18_out, not_19_out);
  and and_5 (and_5_out, not_20_out, Funct[4], Funct[3], not_21_out, not_22_out, not_23_out);
  and and_6 (and_6_out, not_24_out, OP[4], not_25_out, not_26_out, not_27_out, not_28_out);
  and and_7 (and_7_out, not_29_out, not_30_out, not_31_out, not_32_out, not_33_out, not_34_out);
  and and_8 (and_8_out, and_1_out, IsSpecial);
  and and_9 (MFC0, and_2_out, IsSpecial);
  and and_10 (IsSpecial, and_3_out, nor_2_out);
  and and_11 (IsERET, and_4_out, and_5_out);
  and and_12 (and_12_out, and_6_out, and_7_out);
  Multiplexer #(.width(2)) multiplexer_1 (.in0(W1), .in1(2'b01), .out(RegDes), .sel(and_12_out), .en(1'b1));
  Multiplexer #(.width(4)) multiplexer_2 (
    .in0(alu_op_decoder_1_aluop3), .in1(alu_funct_decoder_1_aluop3), .out(AluCtrl), .sel(Is_R_Type), .en(1'b1));
  Multiplexer multiplexer_3 (
    .in0(controlsignal_op_decoder1_1_r1), .in1(controlsignal_funct_decoder1_1_r1), .out(R1_num),
    .sel(Is_R_Type), .en(1'b1));
  Multiplexer multiplexer_4 (
    .in0(controlsignal_op_decoder1_1_r2), .in1(controlsignal_funct_decoder1_1_r2), .out(R2_num),
    .sel(Is_R_Type), .en(1'b1));
  Multiplexer #(.width(2)) multiplexer_5 (
    .in0(controlsignal_op_decoder1_1_w1), .in1(controlsignal_funct_decoder1_1_w1), .out(W1), .sel(Is_R_Type),
    .en(1'b1));
  Multiplexer #(.width(2)) multiplexer_6 (
    .in0(controlsignal_op_decoder1_1_din1), .in1(controlsignal_funct_decoder1_1_din1), .out(MemtoReg),
    .sel(Is_R_Type), .en(1'b1));
  Multiplexer #(.width(2)) multiplexer_7 (
    .in0(controlsignal_op_decoder1_1_sext1), .in1(controlsignal_funct_decoder1_1_sext1), .out(S_EXT),
    .sel(Is_R_Type), .en(1'b1));
  Multiplexer multiplexer_8 (
    .in0(controlsignal_op_decoder1_1_a), .in1(controlsignal_funct_decoder1_1_a), .out(AluSrcA),
    .sel(Is_R_Type), .en(1'b1));
  Multiplexer multiplexer_9 (
    .in0(controlsignal_op_decoder1_1_b), .in1(controlsignal_funct_decoder1_1_b), .out(AluSrcB),
    .sel(Is_R_Type), .en(1'b1));
  Multiplexer multiplexer_10 (
    .in0(controlsignal_op_decoder2_1_jr), .in1(controlsignal_funct_decoder2_1_jr), .out(JR), .sel(Is_R_Type),
    .en(1'b1));
  Multiplexer multiplexer_11 (
    .in0(controlsignal_op_decoder2_1_branch), .in1(controlsignal_funct_decoder2_1_branch), .out(Branch),
    .sel(Is_R_Type), .en(1'b1));
  Multiplexer multiplexer_12 (
    .in0(controlsignal_op_decoder2_1_jump), .in1(controlsignal_funct_decoder2_1_jump), .out(Jump),
    .sel(Is_R_Type), .en(1'b1));
  Multiplexer multiplexer_13 (
    .in0(controlsignal_op_decoder2_1_regwrite), .in1(controlsignal_funct_decoder2_1_regwrite),
    .out(multiplexer_13_out), .sel(Is_R_Type), .en(1'b1));
  Multiplexer multiplexer_14 (
    .in0(controlsignal_op_decoder2_1_memread), .in1(controlsignal_funct_decoder2_1_memread), .out(MemRead),
    .sel(Is_R_Type), .en(1'b1));
  Multiplexer multiplexer_15 (
    .in0(controlsignal_op_decoder2_1_memwrite), .in1(controlsignal_funct_decoder2_1_memwrite),
    .out(MemWrite), .sel(Is_R_Type), .en(1'b1));
  Multiplexer multiplexer_16 (
    .in0(controlsignal_op_decoder2_1_memtoreg), .in1(controlsignal_funct_decoder2_1_memtoreg),
    .out(MemtoReg_t), .sel(Is_R_Type), .en(1'b1));
  Multiplexer multiplexer_17 (
    .in0(controlsignal_op_decoder2_1_isbne), .in1(controlsignal_funct_decoder2_1_isbne), .out(IsBNE),
    .sel(Is_R_Type), .en(1'b1));
  Multiplexer multiplexer_18 (
    .in0(controlsignal_op_decoder2_1_issyscall), .in1(controlsignal_funct_decoder2_1_issyscall),
    .out(IsSyscall), .sel(Is_R_Type), .en(1'b1));
  Multiplexer multiplexer_19 (
    .in0(rtrsread_op_1_rsread), .in1(rtrsread_funct_1_rsread), .out(RsRead), .sel(Is_R_Type), .en(1'b1));
  Multiplexer multiplexer_20 (
    .in0(rtrsread_op_1_rtread), .in1(rtrsread_funct_1_rtread), .out(multiplexer_20_out), .sel(Is_R_Type),
    .en(1'b1));
  or or_1 (RegWrite_t, MFC0, multiplexer_13_out);
  or or_2 (RtRead, multiplexer_20_out, and_8_out);
  Multiplexer multiplexer_21 (.in0(RegWrite_t), .in1(1'b0), .out(RegWrite), .sel(CLR), .en(1'b1));

  // Other names for the same wires on the sheet: A = AluSrcA; ALUOp[3:0] = AluCtrl; B = AluSrcB; Din[1:0] = MemtoReg;
  //   W_num[1:0] = RegDes
endmodule

// ALU_Op
module ALU_Op_Decoder (
  input  op0,
  input  op1,
  input  op2,
  input  op3,
  input  op4,
  input  op5,
  output aluop0,
  output aluop1,
  output aluop2,
  output aluop3
);

  wire and_1_out, and_2_out, and_3_out, and_4_out, and_5_out, and_6_out, and_7_out, and_8_out, and_9_out,
       and_10_out, and_11_out, not_1_out, not_2_out, not_3_out, not_4_out, not_5_out, not_6_out, not_7_out,
       not_8_out, not_9_out, not_10_out, not_11_out, not_12_out, not_13_out, not_14_out, not_15_out,
       not_16_out, not_17_out, not_18_out, not_19_out, not_20_out, not_21_out, not_22_out, not_23_out,
       not_24_out, not_25_out, not_26_out, not_27_out, not_28_out, not_29_out, not_30_out, not_31_out,
       not_32_out, not_33_out, not_34_out, not_35_out, not_36_out, not_37_out, not_38_out, not_39_out;

  not not_1 (not_1_out, op0);
  not not_2 (not_2_out, op1);
  not not_3 (not_3_out, op4);
  not not_4 (not_4_out, op0);
  not not_5 (not_5_out, op1);
  not not_6 (not_6_out, op3);
  not not_7 (not_7_out, op5);
  not not_8 (not_8_out, op0);
  not not_9 (not_9_out, op1);
  not not_10 (not_10_out, op3);
  not not_11 (not_11_out, op4);
  not not_12 (not_12_out, op0);
  not not_13 (not_13_out, op1);
  not not_14 (not_14_out, op4);
  not not_15 (not_15_out, op5);
  not not_16 (not_16_out, op1);
  not not_17 (not_17_out, op3);
  not not_18 (not_18_out, op0);
  not not_19 (not_19_out, op1);
  not not_20 (not_20_out, op4);
  not not_21 (not_21_out, op5);
  not not_22 (not_22_out, op0);
  not not_23 (not_23_out, op1);
  not not_24 (not_24_out, op3);
  not not_25 (not_25_out, op5);
  not not_26 (not_26_out, op0);
  not not_27 (not_27_out, op1);
  not not_28 (not_28_out, op3);
  not not_29 (not_29_out, op4);
  not not_30 (not_30_out, op0);
  not not_31 (not_31_out, op1);
  not not_32 (not_32_out, op3);
  not not_33 (not_33_out, op5);
  not not_34 (not_34_out, op0);
  not not_35 (not_35_out, op1);
  not not_36 (not_36_out, op4);
  not not_37 (not_37_out, op5);
  not not_38 (not_38_out, op1);
  not not_39 (not_39_out, op3);
  and and_1 (and_1_out, not_1_out, not_2_out, op2, op3, not_3_out, op5);
  and and_2 (and_2_out, not_4_out, not_5_out, op2, not_6_out, op4, not_7_out);
  and and_3 (and_3_out, not_8_out, not_9_out, op2, not_10_out, not_11_out);
  and and_4 (and_4_out, not_12_out, not_13_out, op2, not_14_out, not_15_out);
  and and_5 (and_5_out, op0, not_16_out, not_17_out, op4, op5);
  and and_6 (and_6_out, not_18_out, not_19_out, op2, op3, not_20_out, not_21_out);
  and and_7 (and_7_out, not_22_out, not_23_out, op2, not_24_out, op4, not_25_out);
  and and_8 (and_8_out, not_26_out, not_27_out, op2, not_28_out, not_29_out);
  and and_9 (and_9_out, not_30_out, not_31_out, op2, not_32_out, not_33_out);
  and and_10 (and_10_out, not_34_out, not_35_out, op2, not_36_out, not_37_out);
  and and_11 (and_11_out, op0, not_38_out, not_39_out, op4, op5);
  or or_1 (aluop0, and_1_out, and_2_out);
  or or_2 (aluop1, and_3_out, and_4_out, and_5_out);
  or or_3 (aluop2, and_6_out, and_7_out);
  or or_4 (aluop3, and_8_out, and_9_out, and_10_out, and_11_out);
endmodule

// ALU_Funct
module ALU_Funct_Decoder (
  input  funct0,
  input  funct1,
  input  funct2,
  input  funct3,
  input  funct4,
  input  funct5,
  output aluop0,
  output aluop1,
  output aluop2,
  output aluop3
);

  wire and_1_out, and_2_out, and_3_out, and_4_out, and_5_out, and_6_out, and_7_out, and_8_out, and_9_out,
       and_10_out, and_11_out, and_12_out, and_13_out, and_14_out, and_15_out, and_16_out, and_17_out,
       and_18_out, and_19_out, not_1_out, not_2_out, not_3_out, not_4_out, not_5_out, not_6_out, not_7_out,
       not_8_out, not_9_out, not_10_out, not_11_out, not_12_out, not_13_out, not_14_out, not_15_out,
       not_16_out, not_17_out, not_18_out, not_19_out, not_20_out, not_21_out, not_22_out, not_23_out,
       not_24_out, not_25_out, not_26_out, not_27_out, not_28_out, not_29_out, not_30_out, not_31_out,
       not_32_out, not_33_out, not_34_out, not_35_out, not_36_out, not_37_out, not_38_out, not_39_out,
       not_40_out, not_41_out, not_42_out, not_43_out, not_44_out, not_45_out, not_46_out, not_47_out,
       not_48_out, not_49_out, not_50_out, not_51_out, not_52_out, not_53_out, not_54_out, not_55_out,
       not_56_out, not_57_out, not_58_out, not_59_out, not_60_out, not_61_out, not_62_out, not_63_out,
       not_64_out, not_65_out, not_66_out, not_67_out;

  not not_1 (not_1_out, funct1);
  not not_2 (not_2_out, funct2);
  not not_3 (not_3_out, funct4);
  not not_4 (not_4_out, funct1);
  not not_5 (not_5_out, funct2);
  not not_6 (not_6_out, funct1);
  not not_7 (not_7_out, funct3);
  not not_8 (not_8_out, funct5);
  not not_9 (not_9_out, funct1);
  not not_10 (not_10_out, funct3);
  not not_11 (not_11_out, funct1);
  not not_12 (not_12_out, funct2);
  not not_13 (not_13_out, funct3);
  not not_14 (not_14_out, funct4);
  not not_15 (not_15_out, funct5);
  not not_16 (not_16_out, funct1);
  not not_17 (not_17_out, funct2);
  not not_18 (not_18_out, funct3);
  not not_19 (not_19_out, funct4);
  not not_20 (not_20_out, funct1);
  not not_21 (not_21_out, funct2);
  not not_22 (not_22_out, funct4);
  not not_23 (not_23_out, funct5);
  not not_24 (not_24_out, funct1);
  not not_25 (not_25_out, funct2);
  not not_26 (not_26_out, funct3);
  not not_27 (not_27_out, funct5);
  not not_28 (not_28_out, funct1);
  not not_29 (not_29_out, funct3);
  not not_30 (not_30_out, funct1);
  not not_31 (not_31_out, funct2);
  not not_32 (not_32_out, funct4);
  not not_33 (not_33_out, funct5);
  not not_34 (not_34_out, funct0);
  not not_35 (not_35_out, funct1);
  not not_36 (not_36_out, funct2);
  not not_37 (not_37_out, funct3);
  not not_38 (not_38_out, funct5);
  not not_39 (not_39_out, funct1);
  not not_40 (not_40_out, funct2);
  not not_41 (not_41_out, funct3);
  not not_42 (not_42_out, funct5);
  not not_43 (not_43_out, funct1);
  not not_44 (not_44_out, funct2);
  not not_45 (not_45_out, funct1);
  not not_46 (not_46_out, funct3);
  not not_47 (not_47_out, funct5);
  not not_48 (not_48_out, funct1);
  not not_49 (not_49_out, funct2);
  not not_50 (not_50_out, funct3);
  not not_51 (not_51_out, funct4);
  not not_52 (not_52_out, funct5);
  not not_53 (not_53_out, funct1);
  not not_54 (not_54_out, funct2);
  not not_55 (not_55_out, funct3);
  not not_56 (not_56_out, funct4);
  not not_57 (not_57_out, funct1);
  not not_58 (not_58_out, funct2);
  not not_59 (not_59_out, funct4);
  not not_60 (not_60_out, funct5);
  not not_61 (not_61_out, funct0);
  not not_62 (not_62_out, funct1);
  not not_63 (not_63_out, funct2);
  not not_64 (not_64_out, funct3);
  not not_65 (not_65_out, funct1);
  not not_66 (not_66_out, funct3);
  not not_67 (not_67_out, funct5);
  and and_1 (and_1_out, funct0, not_1_out, not_2_out, funct3, not_3_out, funct5);
  and and_2 (and_2_out, funct0, not_4_out, not_5_out, funct3, funct4, funct5);
  and and_3 (and_3_out, funct0, not_6_out, funct2, not_7_out, funct4, not_8_out);
  and and_4 (and_4_out, funct0, not_9_out, funct2, not_10_out, funct4, funct5);
  and and_5 (and_5_out, funct0, not_11_out, not_12_out, not_13_out, not_14_out, not_15_out);
  and and_6 (and_6_out, funct0, not_16_out, not_17_out, not_18_out, not_19_out, funct5);
  and and_7 (and_7_out, funct0, not_20_out, not_21_out, funct3, not_22_out, not_23_out);
  and and_8 (and_8_out, funct0, not_24_out, not_25_out, not_26_out, funct4, not_27_out);
  and and_9 (and_9_out, funct0, not_28_out, funct2, not_29_out, funct4, funct5);
  and and_10 (and_10_out, funct0, not_30_out, not_31_out, funct3, not_32_out, not_33_out);
  and and_11 (and_11_out, not_34_out, not_35_out, not_36_out, not_37_out, funct4, not_38_out);
  and and_12 (and_12_out, funct0, not_39_out, not_40_out, not_41_out, funct4, not_42_out);
  and and_13 (and_13_out, funct0, not_43_out, not_44_out, funct3, funct4, funct5);
  and and_14 (and_14_out, funct0, not_45_out, funct2, not_46_out, funct4, not_47_out);
  and and_15 (and_15_out, funct0, not_48_out, not_49_out, not_50_out, not_51_out, not_52_out);
  and and_16 (and_16_out, funct0, not_53_out, not_54_out, not_55_out, not_56_out, funct5);
  and and_17 (and_17_out, funct0, not_57_out, not_58_out, funct3, not_59_out, not_60_out);
  and and_18 (and_18_out, not_61_out, not_62_out, not_63_out, not_64_out, funct4, funct5);
  and and_19 (and_19_out, funct0, not_65_out, funct2, not_66_out, funct4, not_67_out);
  or or_1 (aluop0, and_1_out, and_2_out, and_3_out, and_4_out);
  or or_2 (aluop1, and_5_out, and_6_out, and_7_out, and_8_out, and_9_out);
  or or_3 (aluop2, and_10_out, and_11_out, and_12_out, and_13_out, and_14_out);
  or or_4 (aluop3, and_15_out, and_16_out, and_17_out, and_18_out, and_19_out);
endmodule

// Controlsignal_Op1
module Controlsignal_Op_Decoder1 (
  input  op0,
  input  op1,
  input  op2,
  input  op3,
  input  op4,
  input  op5,
  output R1,
  output R2,
  output W0,
  output W1,
  output Din0,
  output Din1,
  output SEXT0,
  output SEXT1,
  output A,
  output B
);

  wire and_2_out, and_3_out, and_4_out, and_5_out, and_6_out, and_7_out, and_10_out, and_11_out, and_12_out,
       and_13_out, and_14_out, and_15_out, and_16_out, not_1_out, not_2_out, not_3_out, not_4_out, not_5_out,
       not_6_out, not_7_out, not_8_out, not_9_out, not_10_out, not_11_out, not_12_out, not_13_out,
       not_14_out, not_15_out, not_16_out, not_17_out, not_18_out, not_19_out, not_20_out, not_21_out,
       not_22_out, not_23_out, not_24_out, not_25_out, not_26_out, not_27_out, not_28_out, not_29_out,
       not_30_out, not_31_out, not_32_out, not_33_out, not_34_out, not_35_out, not_36_out, not_37_out,
       not_38_out, not_39_out, not_40_out, not_41_out, not_42_out, not_43_out, not_44_out, not_45_out,
       not_46_out, not_47_out, not_48_out, not_49_out, not_50_out, not_51_out, not_52_out, not_53_out,
       not_54_out, not_55_out, not_56_out, not_57_out, not_58_out, not_59_out;

  not not_1 (not_1_out, op0);
  not not_2 (not_2_out, op1);
  not not_3 (not_3_out, op2);
  not not_4 (not_4_out, op3);
  not not_5 (not_5_out, op0);
  not not_6 (not_6_out, op1);
  not not_7 (not_7_out, op3);
  not not_8 (not_8_out, op4);
  not not_9 (not_9_out, op5);
  not not_10 (not_10_out, op0);
  not not_11 (not_11_out, op1);
  not not_12 (not_12_out, op3);
  not not_13 (not_13_out, op4);
  not not_14 (not_14_out, op0);
  not not_15 (not_15_out, op1);
  not not_16 (not_16_out, op4);
  not not_17 (not_17_out, op5);
  not not_18 (not_18_out, op0);
  not not_19 (not_19_out, op1);
  not not_20 (not_20_out, op4);
  not not_21 (not_21_out, op1);
  not not_22 (not_22_out, op2);
  not not_23 (not_23_out, op3);
  not not_24 (not_24_out, op0);
  not not_25 (not_25_out, op1);
  not not_26 (not_26_out, op3);
  not not_27 (not_27_out, op5);
  not not_28 (not_28_out, op0);
  not not_29 (not_29_out, op1);
  not not_30 (not_30_out, op2);
  not not_31 (not_31_out, op3);
  not not_32 (not_32_out, op1);
  not not_33 (not_33_out, op2);
  not not_34 (not_34_out, op3);
  not not_35 (not_35_out, op0);
  not not_36 (not_36_out, op1);
  not not_37 (not_37_out, op3);
  not not_38 (not_38_out, op4);
  not not_39 (not_39_out, op5);
  not not_40 (not_40_out, op0);
  not not_41 (not_41_out, op1);
  not not_42 (not_42_out, op3);
  not not_43 (not_43_out, op4);
  not not_44 (not_44_out, op0);
  not not_45 (not_45_out, op1);
  not not_46 (not_46_out, op4);
  not not_47 (not_47_out, op5);
  not not_48 (not_48_out, op0);
  not not_49 (not_49_out, op1);
  not not_50 (not_50_out, op4);
  not not_51 (not_51_out, op1);
  not not_52 (not_52_out, op2);
  not not_53 (not_53_out, op3);
  not not_54 (not_54_out, op1);
  not not_55 (not_55_out, op3);
  not not_56 (not_56_out, op0);
  not not_57 (not_57_out, op1);
  not not_58 (not_58_out, op3);
  not not_59 (not_59_out, op5);
  and and_1 (W0, not_1_out, not_2_out, not_3_out, not_4_out, op4, op5);
  and and_2 (and_2_out, not_5_out, not_6_out, op2, not_7_out, not_8_out, not_9_out);
  and and_3 (and_3_out, not_10_out, not_11_out, op2, not_12_out, not_13_out, op5);
  and and_4 (and_4_out, not_14_out, not_15_out, op2, op3, not_16_out, not_17_out);
  and and_5 (and_5_out, not_18_out, not_19_out, op2, op3, not_20_out, op5);
  and and_6 (and_6_out, op0, not_21_out, not_22_out, not_23_out, op4, op5);
  and and_7 (and_7_out, not_24_out, not_25_out, op2, not_26_out, op4, not_27_out);
  and and_8 (Din0, not_28_out, not_29_out, not_30_out, not_31_out, op4, op5);
  and and_9 (Din1, op0, not_32_out, not_33_out, not_34_out, op4, op5);
  and and_10 (and_10_out, not_35_out, not_36_out, op2, not_37_out, not_38_out, not_39_out);
  and and_11 (and_11_out, not_40_out, not_41_out, op2, not_42_out, not_43_out, op5);
  and and_12 (and_12_out, not_44_out, not_45_out, op2, op3, not_46_out, not_47_out);
  and and_13 (and_13_out, not_48_out, not_49_out, op2, op3, not_50_out, op5);
  and and_14 (and_14_out, op0, not_51_out, not_52_out, not_53_out, op4, op5);
  and and_15 (and_15_out, op0, not_54_out, op2, not_55_out, op4, op5);
  and and_16 (and_16_out, not_56_out, not_57_out, op2, not_58_out, op4, not_59_out);
  or or_1 (W1, and_2_out, and_3_out, and_4_out, and_5_out, and_6_out, and_7_out);
  or or_2 (B, and_10_out, and_11_out, and_12_out, and_13_out, and_14_out, and_15_out, and_16_out);

  assign A = 1'b0;
  assign R1 = 1'b0;
  assign R2 = 1'b0;
  assign SEXT0 = 1'b0;
  assign SEXT1 = 1'b0;
endmodule

// Controlsignal_Funct1
module Controlsignal_Funct_Decoder1 (
  input  funct0,
  input  funct1,
  input  funct2,
  input  funct3,
  input  funct4,
  input  funct5,
  output R1,
  output R2,
  output W0,
  output W1,
  output Din0,
  output Din1,
  output SEXT0,
  output SEXT1,
  output A,
  output B
);

  wire and_1_out, and_2_out, and_3_out, and_6_out, and_7_out, and_8_out, and_10_out, and_11_out, and_12_out,
       and_13_out, not_1_out, not_2_out, not_3_out, not_4_out, not_5_out, not_6_out, not_7_out, not_8_out,
       not_9_out, not_10_out, not_11_out, not_12_out, not_13_out, not_14_out, not_15_out, not_16_out,
       not_17_out, not_18_out, not_19_out, not_20_out, not_21_out, not_22_out, not_23_out, not_24_out,
       not_25_out, not_26_out, not_27_out, not_28_out, not_29_out, not_30_out, not_31_out, not_32_out,
       not_33_out, not_34_out, not_35_out, not_36_out, not_37_out, not_38_out, not_39_out, not_40_out,
       not_41_out, not_42_out, not_43_out, not_44_out, not_45_out, not_46_out, not_47_out, not_48_out,
       not_49_out, not_50_out, not_51_out, not_52_out, not_53_out, not_54_out, not_55_out, not_56_out,
       not_57_out, not_58_out, not_59_out, not_60_out, not_61_out;

  not not_1 (not_1_out, funct0);
  not not_2 (not_2_out, funct1);
  not not_3 (not_3_out, funct2);
  not not_4 (not_4_out, funct3);
  not not_5 (not_5_out, funct4);
  not not_6 (not_6_out, funct5);
  not not_7 (not_7_out, funct0);
  not not_8 (not_8_out, funct1);
  not not_9 (not_9_out, funct2);
  not not_10 (not_10_out, funct3);
  not not_11 (not_11_out, funct0);
  not not_12 (not_12_out, funct1);
  not not_13 (not_13_out, funct2);
  not not_14 (not_14_out, funct3);
  not not_15 (not_15_out, funct5);
  not not_16 (not_16_out, funct0);
  not not_17 (not_17_out, funct1);
  not not_18 (not_18_out, funct4);
  not not_19 (not_19_out, funct5);
  not not_20 (not_20_out, funct0);
  not not_21 (not_21_out, funct1);
  not not_22 (not_22_out, funct4);
  not not_23 (not_23_out, funct5);
  not not_24 (not_24_out, funct0);
  not not_25 (not_25_out, funct1);
  not not_26 (not_26_out, funct2);
  not not_27 (not_27_out, funct3);
  not not_28 (not_28_out, funct4);
  not not_29 (not_29_out, funct5);
  not not_30 (not_30_out, funct0);
  not not_31 (not_31_out, funct1);
  not not_32 (not_32_out, funct2);
  not not_33 (not_33_out, funct3);
  not not_34 (not_34_out, funct0);
  not not_35 (not_35_out, funct1);
  not not_36 (not_36_out, funct2);
  not not_37 (not_37_out, funct3);
  not not_38 (not_38_out, funct5);
  not not_39 (not_39_out, funct0);
  not not_40 (not_40_out, funct1);
  not not_41 (not_41_out, funct4);
  not not_42 (not_42_out, funct5);
  not not_43 (not_43_out, funct0);
  not not_44 (not_44_out, funct1);
  not not_45 (not_45_out, funct2);
  not not_46 (not_46_out, funct3);
  not not_47 (not_47_out, funct4);
  not not_48 (not_48_out, funct5);
  not not_49 (not_49_out, funct0);
  not not_50 (not_50_out, funct1);
  not not_51 (not_51_out, funct2);
  not not_52 (not_52_out, funct3);
  not not_53 (not_53_out, funct0);
  not not_54 (not_54_out, funct1);
  not not_55 (not_55_out, funct2);
  not not_56 (not_56_out, funct3);
  not not_57 (not_57_out, funct5);
  not not_58 (not_58_out, funct0);
  not not_59 (not_59_out, funct1);
  not not_60 (not_60_out, funct4);
  not not_61 (not_61_out, funct5);
  and and_1 (and_1_out, not_1_out, not_2_out, not_3_out, not_4_out, not_5_out, not_6_out);
  and and_2 (and_2_out, not_7_out, not_8_out, not_9_out, not_10_out, funct4, funct5);
  and and_3 (and_3_out, not_11_out, not_12_out, not_13_out, not_14_out, funct4, not_15_out);
  and and_4 (R2, not_16_out, not_17_out, funct2, funct3, not_18_out, not_19_out);
  and and_5 (SEXT0, not_20_out, not_21_out, funct2, funct3, not_22_out, not_23_out);
  and and_6 (and_6_out, not_24_out, not_25_out, not_26_out, not_27_out, not_28_out, not_29_out);
  and and_7 (and_7_out, not_30_out, not_31_out, not_32_out, not_33_out, funct4, funct5);
  and and_8 (and_8_out, not_34_out, not_35_out, not_36_out, not_37_out, funct4, not_38_out);
  and and_9 (A, not_39_out, not_40_out, funct2, funct3, not_41_out, not_42_out);
  and and_10 (and_10_out, not_43_out, not_44_out, not_45_out, not_46_out, not_47_out, not_48_out);
  and and_11 (and_11_out, not_49_out, not_50_out, not_51_out, not_52_out, funct4, funct5);
  and and_12 (and_12_out, not_53_out, not_54_out, not_55_out, not_56_out, funct4, not_57_out);
  and and_13 (and_13_out, not_58_out, not_59_out, funct2, funct3, not_60_out, not_61_out);
  or or_1 (R1, and_1_out, and_2_out, and_3_out);
  or or_2 (SEXT1, and_6_out, and_7_out, and_8_out);
  or or_3 (B, and_10_out, and_11_out, and_12_out, and_13_out);

  assign Din0 = 1'b0;
  assign Din1 = 1'b0;
  assign W0 = 1'b0;
  assign W1 = 1'b0;
endmodule

// Controlsignal_Op2
module Controlsignal_Op_Decoder2 (
  input  op0,
  input  op1,
  input  op2,
  input  op3,
  input  op4,
  input  op5,
  output JR,
  output Branch,
  output Jump,
  output RegWrite,
  output MemRead,
  output MemWrite,
  output MemtoReg,
  output IsBNE,
  output isSyscall
);

  wire and_1_out, and_2_out, and_3_out, and_4_out, and_5_out, and_6_out, and_7_out, not_1_out, not_2_out,
       not_3_out, not_4_out, not_5_out, not_6_out, not_7_out, not_8_out, not_9_out, not_10_out, not_11_out,
       not_12_out, not_13_out, not_14_out, not_15_out, not_16_out, not_17_out, not_18_out, not_19_out,
       not_20_out, not_21_out, not_22_out, not_23_out, not_24_out, not_25_out, not_26_out, not_27_out,
       not_28_out, not_29_out, not_30_out, not_31_out, not_32_out, not_33_out, not_34_out, not_35_out,
       not_36_out, not_37_out, not_38_out, not_39_out, not_40_out;

  not not_1 (not_1_out, op0);
  not not_2 (not_2_out, op1);
  not not_3 (not_3_out, op2);
  not not_4 (not_4_out, op4);
  not not_5 (not_5_out, op0);
  not not_6 (not_6_out, op1);
  not not_7 (not_7_out, op2);
  not not_8 (not_8_out, op4);
  not not_9 (not_9_out, op5);
  not not_10 (not_10_out, op0);
  not not_11 (not_11_out, op1);
  not not_12 (not_12_out, op2);
  not not_13 (not_13_out, op3);
  not not_14 (not_14_out, op5);
  not not_15 (not_15_out, op0);
  not not_16 (not_16_out, op1);
  not not_17 (not_17_out, op2);
  not not_18 (not_18_out, op3);
  not not_19 (not_19_out, op1);
  not not_20 (not_20_out, op2);
  not not_21 (not_21_out, op3);
  not not_22 (not_22_out, op0);
  not not_23 (not_23_out, op1);
  not not_24 (not_24_out, op3);
  not not_25 (not_25_out, op5);
  not not_26 (not_26_out, op0);
  not not_27 (not_27_out, op1);
  not not_28 (not_28_out, op4);
  not not_29 (not_29_out, op1);
  not not_30 (not_30_out, op2);
  not not_31 (not_31_out, op3);
  not not_32 (not_32_out, op1);
  not not_33 (not_33_out, op3);
  not not_34 (not_34_out, op1);
  not not_35 (not_35_out, op2);
  not not_36 (not_36_out, op3);
  not not_37 (not_37_out, op0);
  not not_38 (not_38_out, op1);
  not not_39 (not_39_out, op2);
  not not_40 (not_40_out, op4);
  and and_1 (and_1_out, not_1_out, not_2_out, not_3_out, op3, not_4_out, op5);
  and and_2 (and_2_out, not_5_out, not_6_out, not_7_out, op3, not_8_out, not_9_out);
  and and_3 (and_3_out, not_10_out, not_11_out, not_12_out, not_13_out, op4, not_14_out);
  and and_4 (and_4_out, not_15_out, not_16_out, not_17_out, not_18_out, op4, op5);
  and and_5 (and_5_out, not_19_out, not_20_out, not_21_out, op4, op5);
  and and_6 (and_6_out, not_22_out, not_23_out, op2, not_24_out, not_25_out);
  and and_7 (and_7_out, not_26_out, not_27_out, op2, not_28_out);
  and and_8 (MemRead, op0, not_29_out, not_30_out, not_31_out, op4, op5);
  and and_9 (MemWrite, op0, not_32_out, op2, not_33_out, op4, op5);
  and and_10 (MemtoReg, op0, not_34_out, not_35_out, not_36_out, op4, op5);
  and and_11 (IsBNE, not_37_out, not_38_out, not_39_out, op3, not_40_out, op5);
  or or_1 (Branch, and_1_out, and_2_out);
  or or_2 (Jump, and_3_out, and_4_out);
  or or_3 (RegWrite, and_5_out, and_6_out, and_7_out);

  assign isSyscall = 1'b0;
  assign JR = 1'b0;
endmodule

// Controlsignal_Funct2
module Controlsignal_Funct_Decoder2 (
  input  funct0,
  input  funct1,
  input  funct2,
  input  funct3,
  input  funct4,
  input  funct5,
  output JR,
  output Branch,
  output Jump,
  output RegWrite,
  output MemRead,
  output MemWrite,
  output MemtoReg,
  output IsBNE,
  output IsSyscall
);

  wire and_2_out, and_3_out, and_4_out, and_5_out, and_6_out, not_1_out, not_2_out, not_3_out, not_4_out,
       not_5_out, not_6_out, not_7_out, not_8_out, not_9_out, not_10_out, not_11_out, not_12_out, not_13_out,
       not_14_out, not_15_out, not_16_out, not_17_out, not_18_out, not_19_out, not_20_out, not_21_out,
       not_22_out, not_23_out, not_24_out;

  not not_1 (not_1_out, funct0);
  not not_2 (not_2_out, funct1);
  not not_3 (not_3_out, funct3);
  not not_4 (not_4_out, funct4);
  not not_5 (not_5_out, funct5);
  not not_6 (not_6_out, funct1);
  not not_7 (not_7_out, funct2);
  not not_8 (not_8_out, funct3);
  not not_9 (not_9_out, funct5);
  not not_10 (not_10_out, funct0);
  not not_11 (not_11_out, funct1);
  not not_12 (not_12_out, funct2);
  not not_13 (not_13_out, funct3);
  not not_14 (not_14_out, funct1);
  not not_15 (not_15_out, funct2);
  not not_16 (not_16_out, funct4);
  not not_17 (not_17_out, funct1);
  not not_18 (not_18_out, funct2);
  not not_19 (not_19_out, funct1);
  not not_20 (not_20_out, funct3);
  not not_21 (not_21_out, funct0);
  not not_22 (not_22_out, funct1);
  not not_23 (not_23_out, funct4);
  not not_24 (not_24_out, funct5);
  and and_1 (JR, not_1_out, not_2_out, funct2, not_3_out, not_4_out, not_5_out);
  and and_2 (and_2_out, not_6_out, not_7_out, not_8_out, not_9_out);
  and and_3 (and_3_out, not_10_out, not_11_out, not_12_out, not_13_out, funct4);
  and and_4 (and_4_out, funct0, not_14_out, not_15_out, not_16_out);
  and and_5 (and_5_out, funct0, not_17_out, not_18_out, funct3, funct5);
  and and_6 (and_6_out, funct0, not_19_out, funct2, not_20_out, funct4);
  and and_7 (IsSyscall, not_21_out, not_22_out, funct2, funct3, not_23_out, not_24_out);
  or or_1 (RegWrite, and_2_out, and_3_out, and_4_out, and_5_out, and_6_out);

  assign Branch = 1'b0;
  assign IsBNE = 1'b0;
  assign Jump = 1'b0;
  assign MemRead = 1'b0;
  assign MemtoReg = 1'b0;
  assign MemWrite = 1'b0;
endmodule

module RtRsRead_Op (
  input  op0,
  input  op1,
  input  op2,
  input  op3,
  input  op4,
  input  op5,
  output rsread,
  output rtread
);

  wire and_1_out, and_2_out, and_3_out, and_4_out, and_5_out, and_6_out, and_7_out, and_8_out, and_9_out,
       and_10_out, and_11_out, and_12_out, not_1_out, not_2_out, not_3_out, not_4_out, not_5_out, not_6_out,
       not_7_out, not_8_out, not_9_out, not_10_out, not_11_out, not_12_out, not_13_out, not_14_out,
       not_15_out, not_16_out, not_17_out, not_18_out, not_19_out, not_20_out, not_21_out, not_22_out,
       not_23_out, not_24_out, not_25_out, not_26_out, not_27_out, not_28_out, not_29_out, not_30_out,
       not_31_out, not_32_out, not_33_out, not_34_out, not_35_out, not_36_out, not_37_out, not_38_out,
       not_39_out, not_40_out, not_41_out, not_42_out, not_43_out, not_44_out, not_45_out;

  not not_1 (not_1_out, op0);
  not not_2 (not_2_out, op1);
  not not_3 (not_3_out, op3);
  not not_4 (not_4_out, op4);
  not not_5 (not_5_out, op5);
  not not_6 (not_6_out, op0);
  not not_7 (not_7_out, op1);
  not not_8 (not_8_out, op3);
  not not_9 (not_9_out, op4);
  not not_10 (not_10_out, op0);
  not not_11 (not_11_out, op1);
  not not_12 (not_12_out, op4);
  not not_13 (not_13_out, op5);
  not not_14 (not_14_out, op0);
  not not_15 (not_15_out, op1);
  not not_16 (not_16_out, op4);
  not not_17 (not_17_out, op1);
  not not_18 (not_18_out, op2);
  not not_19 (not_19_out, op3);
  not not_20 (not_20_out, op1);
  not not_21 (not_21_out, op3);
  not not_22 (not_22_out, op0);
  not not_23 (not_23_out, op1);
  not not_24 (not_24_out, op2);
  not not_25 (not_25_out, op4);
  not not_26 (not_26_out, op0);
  not not_27 (not_27_out, op1);
  not not_28 (not_28_out, op2);
  not not_29 (not_29_out, op4);
  not not_30 (not_30_out, op5);
  not not_31 (not_31_out, op0);
  not not_32 (not_32_out, op1);
  not not_33 (not_33_out, op3);
  not not_34 (not_34_out, op5);
  not not_35 (not_35_out, op1);
  not not_36 (not_36_out, op3);
  not not_37 (not_37_out, op0);
  not not_38 (not_38_out, op1);
  not not_39 (not_39_out, op2);
  not not_40 (not_40_out, op4);
  not not_41 (not_41_out, op0);
  not not_42 (not_42_out, op1);
  not not_43 (not_43_out, op2);
  not not_44 (not_44_out, op4);
  not not_45 (not_45_out, op5);
  and and_1 (and_1_out, not_1_out, not_2_out, op2, not_3_out, not_4_out, not_5_out);
  and and_2 (and_2_out, not_6_out, not_7_out, op2, not_8_out, not_9_out, op5);
  and and_3 (and_3_out, not_10_out, not_11_out, op2, op3, not_12_out, not_13_out);
  and and_4 (and_4_out, not_14_out, not_15_out, op2, op3, not_16_out, op5);
  and and_5 (and_5_out, op0, not_17_out, not_18_out, not_19_out, op4, op5);
  and and_6 (and_6_out, op0, not_20_out, op2, not_21_out, op4, op5);
  and and_7 (and_7_out, not_22_out, not_23_out, not_24_out, op3, not_25_out, op5);
  and and_8 (and_8_out, not_26_out, not_27_out, not_28_out, op3, not_29_out, not_30_out);
  and and_9 (and_9_out, not_31_out, not_32_out, op2, not_33_out, op4, not_34_out);
  and and_10 (and_10_out, op0, not_35_out, op2, not_36_out, op4, op5);
  and and_11 (and_11_out, not_37_out, not_38_out, not_39_out, op3, not_40_out, op5);
  and and_12 (and_12_out, not_41_out, not_42_out, not_43_out, op3, not_44_out, not_45_out);
  or or_1 (rsread, and_1_out, and_2_out, and_3_out, and_4_out, and_5_out, and_6_out, and_7_out, and_8_out, and_9_out);
  or or_2 (rtread, and_10_out, and_11_out, and_12_out);
endmodule

module RtRsRead_Funct (
  input  funct0,
  input  funct1,
  input  funct2,
  input  funct3,
  input  funct4,
  input  funct5,
  output rsread,
  output rtread
);

  wire and_1_out, and_2_out, and_3_out, and_4_out, and_5_out, and_6_out, and_7_out, and_8_out, and_9_out,
       and_10_out, and_11_out, and_12_out, and_13_out, and_14_out, and_15_out, and_16_out, not_1_out,
       not_2_out, not_3_out, not_4_out, not_5_out, not_6_out, not_7_out, not_8_out, not_9_out, not_10_out,
       not_11_out, not_12_out, not_13_out, not_14_out, not_15_out, not_16_out, not_17_out, not_18_out,
       not_19_out, not_20_out, not_21_out, not_22_out, not_23_out, not_24_out, not_25_out, not_26_out,
       not_27_out, not_28_out, not_29_out, not_30_out, not_31_out, not_32_out, not_33_out, not_34_out,
       not_35_out, not_36_out, not_37_out, not_38_out, not_39_out, not_40_out, not_41_out, not_42_out,
       not_43_out, not_44_out, not_45_out, not_46_out, not_47_out, not_48_out, not_49_out, not_50_out,
       not_51_out, not_52_out, not_53_out, not_54_out, not_55_out, not_56_out, not_57_out, not_58_out;

  not not_1 (not_1_out, funct1);
  not not_2 (not_2_out, funct2);
  not not_3 (not_3_out, funct3);
  not not_4 (not_4_out, funct4);
  not not_5 (not_5_out, funct5);
  not not_6 (not_6_out, funct1);
  not not_7 (not_7_out, funct2);
  not not_8 (not_8_out, funct3);
  not not_9 (not_9_out, funct4);
  not not_10 (not_10_out, funct1);
  not not_11 (not_11_out, funct2);
  not not_12 (not_12_out, funct4);
  not not_13 (not_13_out, funct5);
  not not_14 (not_14_out, funct0);
  not not_15 (not_15_out, funct1);
  not not_16 (not_16_out, funct2);
  not not_17 (not_17_out, funct3);
  not not_18 (not_18_out, funct4);
  not not_19 (not_19_out, funct5);
  not not_20 (not_20_out, funct0);
  not not_21 (not_21_out, funct1);
  not not_22 (not_22_out, funct2);
  not not_23 (not_23_out, funct3);
  not not_24 (not_24_out, funct0);
  not not_25 (not_25_out, funct1);
  not not_26 (not_26_out, funct2);
  not not_27 (not_27_out, funct3);
  not not_28 (not_28_out, funct5);
  not not_29 (not_29_out, funct1);
  not not_30 (not_30_out, funct2);
  not not_31 (not_31_out, funct3);
  not not_32 (not_32_out, funct5);
  not not_33 (not_33_out, funct1);
  not not_34 (not_34_out, funct2);
  not not_35 (not_35_out, funct4);
  not not_36 (not_36_out, funct1);
  not not_37 (not_37_out, funct2);
  not not_38 (not_38_out, funct1);
  not not_39 (not_39_out, funct3);
  not not_40 (not_40_out, funct5);
  not not_41 (not_41_out, funct1);
  not not_42 (not_42_out, funct3);
  not not_43 (not_43_out, funct0);
  not not_44 (not_44_out, funct1);
  not not_45 (not_45_out, funct3);
  not not_46 (not_46_out, funct4);
  not not_47 (not_47_out, funct5);
  not not_48 (not_48_out, funct1);
  not not_49 (not_49_out, funct2);
  not not_50 (not_50_out, funct3);
  not not_51 (not_51_out, funct5);
  not not_52 (not_52_out, funct1);
  not not_53 (not_53_out, funct2);
  not not_54 (not_54_out, funct4);
  not not_55 (not_55_out, funct1);
  not not_56 (not_56_out, funct2);
  not not_57 (not_57_out, funct1);
  not not_58 (not_58_out, funct3);
  and and_1 (and_1_out, funct0, not_1_out, not_2_out, not_3_out, not_4_out, not_5_out);
  and and_2 (and_2_out, funct0, not_6_out, not_7_out, not_8_out, not_9_out, funct5);
  and and_3 (and_3_out, funct0, not_10_out, not_11_out, funct3, not_12_out, not_13_out);
  and and_4 (and_4_out, not_14_out, not_15_out, not_16_out, not_17_out, not_18_out, not_19_out);
  and and_5 (and_5_out, not_20_out, not_21_out, not_22_out, not_23_out, funct4, funct5);
  and and_6 (and_6_out, not_24_out, not_25_out, not_26_out, not_27_out, funct4, not_28_out);
  and and_7 (and_7_out, funct0, not_29_out, not_30_out, not_31_out, funct4, not_32_out);
  and and_8 (and_8_out, funct0, not_33_out, not_34_out, funct3, not_35_out, funct5);
  and and_9 (and_9_out, funct0, not_36_out, not_37_out, funct3, funct4, funct5);
  and and_10 (and_10_out, funct0, not_38_out, funct2, not_39_out, funct4, not_40_out);
  and and_11 (and_11_out, funct0, not_41_out, funct2, not_42_out, funct4, funct5);
  and and_12 (and_12_out, not_43_out, not_44_out, funct2, not_45_out, not_46_out, not_47_out);
  and and_13 (and_13_out, funct0, not_48_out, not_49_out, not_50_out, not_51_out);
  and and_14 (and_14_out, funct0, not_52_out, not_53_out, not_54_out);
  and and_15 (and_15_out, funct0, not_55_out, not_56_out, funct3, funct5);
  and and_16 (and_16_out, funct0, not_57_out, funct2, not_58_out, funct4);
  or or_1 (rtread, and_13_out, and_14_out, and_15_out, and_16_out);
  or or_2 (rsread, and_1_out, and_2_out, and_3_out, and_4_out, and_5_out, and_6_out, and_7_out, and_8_out, and_9_out, and_10_out, and_11_out, and_12_out);
endmodule

module Syscall (
  input  IsSyscall,
  input  CLK,
  input  [31:0] v0,
  output Disp,
  output Halt
);

  wire and_2_out, comparator_1_eq, not_1_out;

  not not_1 (not_1_out, comparator_1_eq);
  Comparator #(.width(32)) comparator_1 (.a(32'ha), .b(v0), .eq(comparator_1_eq));  // open: gt, lt
  and and_1 (Disp, IsSyscall, not_1_out);
  and and_2 (and_2_out, IsSyscall, comparator_1_eq);
  D_Flip_Flop d_ff_1 (.clk(CLK), .D(and_2_out), .Q(Halt));  // open: Qn, preset, en, reset
endmodule

module Hazard_Unit (
  input  [4:0] WriteRegM,
  input  CLK,
  input  [1:0] MemtoRegE,
  input  [4:0] RsD,
  input  RegWriteE,
  input  [4:0] RtD,
  input  RegWriteM,
  input  [4:0] RsE,
  input  RegWriteW,
  input  [4:0] RtE,
  input  [4:0] WriteRegW,
  input  BranchE,
  input  MemWriteM,
  input  [4:0] WriteRegE,
  input  Jump,
  input  IsSyscallE,
  input  JR,
  input  IsSyscallD,
  input  MemReadE,
  input  RsRead,
  input  MemReadM,
  input  RtRead,
  output StallF,
  output StallD,
  output StallEX,
  output StallMem,
  output FlushE,
  output FlushD,
  output FlushM,
  output [1:0] RedirR1,
  output [1:0] RedirR2
);

  wire and_1_out, and_2_out, and_3_out, and_4_out, and_5_out, and_6_out, and_7_out, and_8_out, and_9_out,
       and_10_out, and_11_out, and_12_out, and_13_out, and_14_out, and_15_out, comparator_1_gt,
       comparator_1_lt, comparator_2_eq, comparator_3_gt, comparator_3_lt, comparator_4_eq, comparator_5_gt,
       comparator_5_lt, comparator_6_eq, comparator_7_gt, comparator_7_lt, comparator_8_eq, comparator_9_gt,
       comparator_9_lt, comparator_10_eq, comparator_11_gt, comparator_11_lt, comparator_12_eq, not_2_out,
       or_1_out, or_2_out, or_3_out, or_4_out, or_5_out, or_6_out, or_7_out, or_8_out, or_9_out;

  Comparator #(.width(5)) comparator_1 (
    .a(RsD), .b({5{1'b0}}), .gt(comparator_1_gt), .lt(comparator_1_lt));  // open: eq
  Comparator #(.width(5)) comparator_2 (.a(RsD), .b(WriteRegM), .eq(comparator_2_eq));  // open: gt, lt
  Comparator #(.width(5)) comparator_3 (
    .a(RsD), .b({5{1'b0}}), .gt(comparator_3_gt), .lt(comparator_3_lt));  // open: eq
  Comparator #(.width(5)) comparator_4 (.a(RsD), .b(WriteRegE), .eq(comparator_4_eq));  // open: gt, lt
  Comparator #(.width(5)) comparator_5 (
    .a(RtD), .b({5{1'b0}}), .gt(comparator_5_gt), .lt(comparator_5_lt));  // open: eq
  Comparator #(.width(5)) comparator_6 (.a(RtD), .b(WriteRegM), .eq(comparator_6_eq));  // open: gt, lt
  Comparator #(.width(5)) comparator_7 (
    .a(RtD), .b({5{1'b0}}), .gt(comparator_7_gt), .lt(comparator_7_lt));  // open: eq
  Comparator #(.width(5)) comparator_8 (.a(RtD), .b(WriteRegE), .eq(comparator_8_eq));  // open: gt, lt
  Comparator #(.width(5)) comparator_9 (
    .a(RsD), .b({5{1'b0}}), .gt(comparator_9_gt), .lt(comparator_9_lt));  // open: eq
  Comparator #(.width(5)) comparator_10 (.a(RsD), .b(WriteRegE), .eq(comparator_10_eq));  // open: gt, lt
  Comparator #(.width(5)) comparator_11 (
    .a(RtD), .b({5{1'b0}}), .gt(comparator_11_gt), .lt(comparator_11_lt));  // open: eq
  Comparator #(.width(5)) comparator_12 (.a(RtD), .b(WriteRegE), .eq(comparator_12_eq));  // open: gt, lt
  or or_1 (or_1_out, comparator_1_gt, comparator_1_lt);
  or or_2 (or_2_out, comparator_3_gt, comparator_3_lt);
  or or_3 (or_3_out, comparator_5_gt, comparator_5_lt);
  or or_4 (or_4_out, comparator_7_gt, comparator_7_lt);
  or or_5 (or_5_out, comparator_9_gt, comparator_9_lt);
  or or_6 (or_6_out, comparator_11_gt, comparator_11_lt);
  and and_1 (and_1_out, or_1_out, comparator_2_eq, RegWriteM);
  and and_2 (and_2_out, or_2_out, comparator_4_eq, RegWriteE);
  and and_3 (and_3_out, or_3_out, comparator_6_eq, RegWriteM);
  and and_4 (and_4_out, or_4_out, comparator_8_eq, RegWriteE);
  and and_5 (and_5_out, or_5_out, comparator_10_eq, RegWriteE);
  and and_6 (and_6_out, or_6_out, comparator_12_eq, RegWriteE);
  or or_7 (or_7_out, and_5_out, and_6_out);
  and and_7 (and_7_out, RsRead, and_1_out);
  and and_8 (and_8_out, RsRead, and_2_out);
  and and_9 (and_9_out, RtRead, and_3_out);
  and and_10 (and_10_out, RtRead, and_4_out);
  and and_11 (and_11_out, or_7_out, MemReadE);
  and and_12 (and_12_out, MemReadM, and_7_out);
  and and_13 (and_13_out, MemReadM, and_9_out);
  not not_1 (StallD, and_11_out);
  or or_8 (or_8_out, JR, BranchE);
  Priority_Encoder #(.select(2)) priority_encoder_1 (
    .in0(1'b1), .in1(and_7_out), .in2(and_12_out), .in3(and_8_out), .out(RedirR1));  // open: gs, en_out, en_in
  Priority_Encoder #(.select(2)) priority_encoder_2 (
    .in0(1'b1), .in1(and_9_out), .in2(and_13_out), .in3(and_10_out), .out(RedirR2));  // open: gs, en_out, en_in
  or or_9 (or_9_out, and_11_out, or_8_out);
  not not_2 (not_2_out, RegWriteE);
  and and_14 (and_14_out, Jump, RegWriteE);
  and and_15 (and_15_out, not_2_out, Jump);
  or or_10 (FlushE, or_9_out, and_15_out);
  or or_11 (FlushD, or_8_out, and_14_out, and_15_out);

  assign FlushM = 1'b0;
  assign StallEX = 1'b1;
  assign StallF = StallD;
  assign StallMem = 1'b1;
endmodule

module statics (
  input  op0,
  input  op1,
  input  op2,
  input  op3,
  input  op4,
  input  op5,
  output R,
  output I,
  output J
);

  wire and_2_out, and_3_out, and_4_out, and_5_out, and_6_out, and_7_out, and_8_out, and_9_out, and_10_out,
       and_11_out, and_12_out, not_1_out, not_2_out, not_3_out, not_4_out, not_5_out, not_6_out, not_7_out,
       not_8_out, not_9_out, not_10_out, not_11_out, not_12_out, not_13_out, not_14_out, not_15_out,
       not_16_out, not_17_out, not_18_out, not_19_out, not_20_out, not_21_out, not_22_out, not_23_out,
       not_24_out, not_25_out, not_26_out, not_27_out, not_28_out, not_29_out, not_30_out, not_31_out,
       not_32_out, not_33_out, not_34_out, not_35_out, not_36_out, not_37_out, not_38_out, not_39_out,
       not_40_out, not_41_out, not_42_out, not_43_out, not_44_out, not_45_out, not_46_out, not_47_out,
       not_48_out, not_49_out;

  not not_1 (not_1_out, op0);
  not not_2 (not_2_out, op1);
  not not_3 (not_3_out, op2);
  not not_4 (not_4_out, op3);
  not not_5 (not_5_out, op4);
  not not_6 (not_6_out, op5);
  not not_7 (not_7_out, op0);
  not not_8 (not_8_out, op1);
  not not_9 (not_9_out, op3);
  not not_10 (not_10_out, op4);
  not not_11 (not_11_out, op5);
  not not_12 (not_12_out, op0);
  not not_13 (not_13_out, op1);
  not not_14 (not_14_out, op3);
  not not_15 (not_15_out, op4);
  not not_16 (not_16_out, op0);
  not not_17 (not_17_out, op1);
  not not_18 (not_18_out, op4);
  not not_19 (not_19_out, op5);
  not not_20 (not_20_out, op0);
  not not_21 (not_21_out, op1);
  not not_22 (not_22_out, op4);
  not not_23 (not_23_out, op1);
  not not_24 (not_24_out, op2);
  not not_25 (not_25_out, op3);
  not not_26 (not_26_out, op1);
  not not_27 (not_27_out, op3);
  not not_28 (not_28_out, op0);
  not not_29 (not_29_out, op1);
  not not_30 (not_30_out, op2);
  not not_31 (not_31_out, op4);
  not not_32 (not_32_out, op0);
  not not_33 (not_33_out, op1);
  not not_34 (not_34_out, op2);
  not not_35 (not_35_out, op4);
  not not_36 (not_36_out, op5);
  not not_37 (not_37_out, op0);
  not not_38 (not_38_out, op1);
  not not_39 (not_39_out, op3);
  not not_40 (not_40_out, op5);
  not not_41 (not_41_out, op0);
  not not_42 (not_42_out, op1);
  not not_43 (not_43_out, op2);
  not not_44 (not_44_out, op3);
  not not_45 (not_45_out, op0);
  not not_46 (not_46_out, op1);
  not not_47 (not_47_out, op2);
  not not_48 (not_48_out, op3);
  not not_49 (not_49_out, op5);
  and and_1 (R, not_1_out, not_2_out, not_3_out, not_4_out, not_5_out, not_6_out);
  and and_2 (and_2_out, not_7_out, not_8_out, op2, not_9_out, not_10_out, not_11_out);
  and and_3 (and_3_out, not_12_out, not_13_out, op2, not_14_out, not_15_out, op5);
  and and_4 (and_4_out, not_16_out, not_17_out, op2, op3, not_18_out, not_19_out);
  and and_5 (and_5_out, not_20_out, not_21_out, op2, op3, not_22_out, op5);
  and and_6 (and_6_out, op0, not_23_out, not_24_out, not_25_out, op4, op5);
  and and_7 (and_7_out, op0, not_26_out, op2, not_27_out, op4, op5);
  and and_8 (and_8_out, not_28_out, not_29_out, not_30_out, op3, not_31_out, op5);
  and and_9 (and_9_out, not_32_out, not_33_out, not_34_out, op3, not_35_out, not_36_out);
  and and_10 (and_10_out, not_37_out, not_38_out, op2, not_39_out, op4, not_40_out);
  and and_11 (and_11_out, not_41_out, not_42_out, not_43_out, not_44_out, op4, op5);
  and and_12 (and_12_out, not_45_out, not_46_out, not_47_out, not_48_out, op4, not_49_out);
  or or_1 (I, and_2_out, and_3_out, and_4_out, and_5_out, and_6_out, and_7_out, and_8_out, and_9_out, and_10_out);
  or or_2 (J, and_11_out, and_12_out);
endmodule

module CP0 (
  input  IsERET,
  input  [31:0] CP0Din,
  input  [31:0] PCin,
  input  IsSpecial,
  input  [4:0] CP0R1_num,
  input  [4:0] CP0W_num,
  input  Cause,
  input  Clk,
  input  [4:0] Instruction,
  input  [31:0] InterruptNumIn,
  output [31:0] CP0R1,
  output [31:0] PCout,
  output Shield,
  output MFC0,
  output MTC0,
  output Interrupt,
  output [31:0] InterruptNumOut
);

  wire and_1_out, buffer_1_out, buffer_2_out, buffer_3_out, comparator_3_eq, multiplexer_4_out, not_1_out,
       not_2_out, not_3_out, not_4_out, not_5_out, not_6_out, not_7_out, not_8_out, not_9_out, not_10_out,
       or_1_out, or_2_out;
  wire [4:0] multiplexer_1_out, multiplexer_2_out;
  wire [7:0] counter_1_q;
  wire [31:0] CP0R2, main_1_reg1, multiplexer_3_out;

  not not_1 (not_1_out, Clk);
  not not_2 (not_2_out, Instruction[4]);
  not not_3 (not_3_out, Instruction[3]);
  not not_4 (not_4_out, Instruction[1]);
  not not_5 (not_5_out, Instruction[0]);
  not not_6 (not_6_out, Instruction[4]);
  not not_7 (not_7_out, Instruction[3]);
  not not_8 (not_8_out, Instruction[2]);
  not not_9 (not_9_out, Instruction[1]);
  not not_10 (not_10_out, Instruction[0]);
  and and_1 (and_1_out, IsERET, not_1_out);
  or or_1 (or_1_out, and_1_out, Cause);
  Counter counter_1 (.load(and_1_out), .Q(counter_1_q), .clk(or_1_out));  // open: D, count, carry, clr
  and and_2 (MTC0, IsSpecial, not_2_out, not_3_out, Instruction[2], not_4_out, not_5_out);
  and and_3 (MFC0, IsSpecial, not_6_out, not_7_out, not_8_out, not_9_out, not_10_out);
  Comparator comparator_1 (.a(counter_1_q), .b({8{1'b0}}), .gt(Interrupt));  // open: eq, lt
  Multiplexer #(.width(5)) multiplexer_1 (
    .in0(CP0R1_num), .in1({5{1'b1}}), .out(multiplexer_1_out), .sel(IsERET), .en(1'b1));
  Multiplexer #(.width(5)) multiplexer_2 (
    .in0(CP0W_num), .in1({5{1'b1}}), .out(multiplexer_2_out), .sel(Cause), .en(1'b1));
  buf buffer_1 (buffer_1_out, buffer_2_out);
  buf buffer_2 (buffer_2_out, buffer_3_out);
  buf buffer_3 (buffer_3_out, multiplexer_4_out);
  or or_2 (or_2_out, MTC0, Cause);
  Multiplexer #(.width(32)) multiplexer_3 (.in0(PCin), .in1(CP0Din), .out(multiplexer_3_out), .sel(MTC0), .en(1'b1));
  Register #(.width(32)) register_1 (.D(InterruptNumIn), .Q(InterruptNumOut), .clk(Clk));  // open: en, clr
  regfile2_main main_1 (
    .Reg1_num(multiplexer_1_out), .Reg2(5'b11110), .Write_Reg_num(multiplexer_2_out),
    .Din(multiplexer_3_out), .Write_Enable(or_2_out), .Clock(buffer_1_out), .Reg1(main_1_reg1),
    .Reg2_2(CP0R2), .ra_Value(PCout));  // open: s0_Value, s1_Value, s2_Value
  Multiplexer multiplexer_4 (.in0(Clk), .in1(Cause), .out(multiplexer_4_out), .sel(Cause), .en(1'b1));
  Comparator #(.width(32)) comparator_2 (.a(CP0R2), .b(32'h1), .eq(Shield));  // open: gt, lt
  Comparator #(.width(5), .mode("unsigned")) comparator_3 (
    .a(5'b10110), .b(multiplexer_1_out), .eq(comparator_3_eq));  // open: gt, lt
  Multiplexer #(.width(32)) multiplexer_5 (
    .in0(main_1_reg1), .in1(InterruptNumOut), .out(CP0R1), .sel(comparator_3_eq), .en(1'b1));

  // Other names for the same wires on the sheet: Insruction[4:0] = Instruction
endmodule

module ButtonCtrl (
  input  Button1,
  input  Button2,
  input  Shield,
  input  Button3,
  input  Halt,
  input  [31:0] InterruptNumIn,
  output [31:0] InterruptNumOut,
  output Cause
);

  wire and_1_out, and_2_out, and_3_out, not_1_out, not_2_out, not_3_out, not_4_out, not_5_out, or_1_out,
       or_2_out;
  wire [31:0] controlled_buffer_1_out;

  not not_1 (not_1_out, InterruptNumIn[0]);
  not not_2 (not_2_out, InterruptNumIn[1]);
  not not_3 (not_3_out, InterruptNumIn[2]);
  assign controlled_buffer_1_out = and_1_out ? 32'h1 : 32'bz;  // Controlled_Buffer controlled_buffer_1
  and and_1 (and_1_out, Button1, not_1_out);
  and and_2 (and_2_out, Button2, not_2_out);
  and and_3 (and_3_out, Button3, not_3_out);
  assign controlled_buffer_1_out = and_2_out ? 32'h3 : 32'bz;  // Controlled_Buffer controlled_buffer_2
  assign controlled_buffer_1_out = and_3_out ? 32'h7 : 32'bz;  // Controlled_Buffer controlled_buffer_3
  Register #(.width(32)) register_1 (
    .D(controlled_buffer_1_out), .Q(InterruptNumOut), .clk(or_1_out));  // open: en, clr
  or or_1 (or_1_out, and_1_out, and_2_out, and_3_out);
  or or_2 (or_2_out, and_1_out, and_2_out, and_3_out);
  not not_4 (not_4_out, Shield);
  not not_5 (not_5_out, Halt);
  and and_4 (Cause, or_2_out, not_4_out, not_5_out);
endmodule
