// Logisim project Test.circ as structural Verilog: 1 circuit, main circuit main
module main (
);

  wire and_1_out, clock_1_out, comparator_1_eq, comparator_2_gt, comparator_2_lt, controlled_buffer_1_out,
       main_1_p2, main_1_p4, multiplexer_1_out, nor_1_out;
  wire [15:0] counter_1_q;
  wire [31:0] cpu_1_p2, main_1_p3;

  Clock clock_1 (.out(clock_1_out));
  Counter #(.width(16), .max('hffff)) counter_1 (
    .Q(counter_1_q), .clk(controlled_buffer_1_out));  // open: load, D, count, carry, clr
  assign controlled_buffer_1_out = and_1_out ? clock_1_out : 1'bz;  // Controlled_Buffer controlled_buffer_1
  // Probe on counter_1_q
  // CPU cpu_1: pin names not known; wires that end beside it: controlled_buffer_1_out, cpu_1_p2
  // MIPS_CPU_pipelined_redirection2___副本_main main_1: pin names not known; wires that end beside it: controlled_buffer_1_out, main_1_p2, main_1_p3, main_1_p4
  and and_1 (and_1_out, comparator_1_eq, multiplexer_1_out);
  // Probe on cpu_1_p2
  // Probe on main_1_p3
  Comparator #(.width(1)) comparator_1 (.a(main_1_p2), .b(main_1_p4), .eq(comparator_1_eq));  // open: gt, lt
  Comparator #(.width(32), .mode("unsigned")) comparator_2 (
    .a(cpu_1_p2), .b(main_1_p3), .gt(comparator_2_gt), .lt(comparator_2_lt));  // open: eq
  Multiplexer multiplexer_1 (.in0(1'b1), .in1(nor_1_out), .out(multiplexer_1_out), .sel(main_1_p2));  // open: en
  nor nor_1 (nor_1_out, comparator_2_gt, comparator_2_lt);
endmodule
