// Logisim project regfile.circ as structural Verilog: 1 circuit, main circuit main
module main (
  input  [4:0] Reg1_num,
  input  [4:0] Reg2,
  input  [4:0] Write_Reg_num,
  input  [31:0] Din,
  input  Write_Enable,
  input  Clock,
  output [31:0] Reg1,
  output [31:0] s0_Value,
  output [31:0] a0_Value,
  output [31:0] v0_Value,
  output [31:0] ra_Value,
  output [31:0] Reg2_2
);

  wire demultiplexer_2_out0, demultiplexer_2_out1, demultiplexer_2_out2, demultiplexer_2_out3,
       demultiplexer_2_out4, demultiplexer_2_out5, demultiplexer_2_out6, demultiplexer_2_out7,
       demultiplexer_2_out8, demultiplexer_2_out9, demultiplexer_2_out10, demultiplexer_2_out11,
       demultiplexer_2_out12, demultiplexer_2_out13, demultiplexer_2_out14, demultiplexer_2_out15,
       demultiplexer_2_out16, demultiplexer_2_out17, demultiplexer_2_out18, demultiplexer_2_out19,
       demultiplexer_2_out20, demultiplexer_2_out21, demultiplexer_2_out22, demultiplexer_2_out23,
       demultiplexer_2_out24, demultiplexer_2_out25, demultiplexer_2_out26, demultiplexer_2_out27,
       demultiplexer_2_out28, demultiplexer_2_out29, demultiplexer_2_out30, demultiplexer_2_out31;
  wire [31:0] _0__zero_q, _1__at_q, _3__v1_q, _5__a1_q, _6__a2_q, _7__a3_q, _8__t0_q, _9__t1_q, _10__t2_q,
       _11__t3_q, _12__t4_q, _13__t5_q, _14__t6_q, _15__t7_q, _17__s1_q, _18___s2_q, _19___s3_q, _20___s4_q,
       _21__s5_q, _22__s6_q, _23__s7_q, _24__t8_q, _25__t9_q, _26__k0_q, _27__k1_q, _28__gp_q, _29__sp_q,
       _30__fp_q, demultiplexer_1_out1, demultiplexer_1_out2, demultiplexer_1_out3, demultiplexer_1_out4,
       demultiplexer_1_out5, demultiplexer_1_out6, demultiplexer_1_out7, demultiplexer_1_out8,
       demultiplexer_1_out9, demultiplexer_1_out10, demultiplexer_1_out11, demultiplexer_1_out12,
       demultiplexer_1_out13, demultiplexer_1_out14, demultiplexer_1_out15, demultiplexer_1_out16,
       demultiplexer_1_out17, demultiplexer_1_out18, demultiplexer_1_out19, demultiplexer_1_out20,
       demultiplexer_1_out21, demultiplexer_1_out22, demultiplexer_1_out23, demultiplexer_1_out24,
       demultiplexer_1_out25, demultiplexer_1_out26, demultiplexer_1_out27, demultiplexer_1_out28,
       demultiplexer_1_out29, demultiplexer_1_out30, demultiplexer_1_out31;

  Demultiplexer #(.select(5), .width(32)) demultiplexer_1 (
    .out1(demultiplexer_1_out1), .out2(demultiplexer_1_out2), .out3(demultiplexer_1_out3),
    .out4(demultiplexer_1_out4), .out5(demultiplexer_1_out5), .out6(demultiplexer_1_out6),
    .out7(demultiplexer_1_out7), .out8(demultiplexer_1_out8), .out9(demultiplexer_1_out9),
    .out10(demultiplexer_1_out10), .out11(demultiplexer_1_out11), .out12(demultiplexer_1_out12),
    .out13(demultiplexer_1_out13), .out14(demultiplexer_1_out14), .out15(demultiplexer_1_out15),
    .out16(demultiplexer_1_out16), .out17(demultiplexer_1_out17), .out18(demultiplexer_1_out18),
    .out19(demultiplexer_1_out19), .out20(demultiplexer_1_out20), .out21(demultiplexer_1_out21),
    .out22(demultiplexer_1_out22), .out23(demultiplexer_1_out23), .out24(demultiplexer_1_out24),
    .out25(demultiplexer_1_out25), .out26(demultiplexer_1_out26), .out27(demultiplexer_1_out27),
    .out28(demultiplexer_1_out28), .out29(demultiplexer_1_out29), .out30(demultiplexer_1_out30),
    .out31(demultiplexer_1_out31), .in(Din), .sel(Write_Reg_num), .en(1'b1));  // open: out0
  Demultiplexer #(.select(5)) demultiplexer_2 (
    .out0(demultiplexer_2_out0), .out1(demultiplexer_2_out1), .out2(demultiplexer_2_out2),
    .out3(demultiplexer_2_out3), .out4(demultiplexer_2_out4), .out5(demultiplexer_2_out5),
    .out6(demultiplexer_2_out6), .out7(demultiplexer_2_out7), .out8(demultiplexer_2_out8),
    .out9(demultiplexer_2_out9), .out10(demultiplexer_2_out10), .out11(demultiplexer_2_out11),
    .out12(demultiplexer_2_out12), .out13(demultiplexer_2_out13), .out14(demultiplexer_2_out14),
    .out15(demultiplexer_2_out15), .out16(demultiplexer_2_out16), .out17(demultiplexer_2_out17),
    .out18(demultiplexer_2_out18), .out19(demultiplexer_2_out19), .out20(demultiplexer_2_out20),
    .out21(demultiplexer_2_out21), .out22(demultiplexer_2_out22), .out23(demultiplexer_2_out23),
    .out24(demultiplexer_2_out24), .out25(demultiplexer_2_out25), .out26(demultiplexer_2_out26),
    .out27(demultiplexer_2_out27), .out28(demultiplexer_2_out28), .out29(demultiplexer_2_out29),
    .out30(demultiplexer_2_out30), .out31(demultiplexer_2_out31), .in(Write_Enable), .sel(Write_Reg_num),
    .en(1'b1));
  Register #(.width(32)) _0__zero (.D({32{1'b0}}), .en(demultiplexer_2_out0), .Q(_0__zero_q), .clk(Clock), .clr(1'b0));
  Register #(.width(32)) _1__at (
    .D(demultiplexer_1_out1), .en(demultiplexer_2_out1), .Q(_1__at_q), .clk(Clock), .clr(1'b0));
  Register #(.width(32)) _2__v0 (
    .D(demultiplexer_1_out2), .en(demultiplexer_2_out2), .Q(v0_Value), .clk(Clock), .clr(1'b0));
  Register #(.width(32)) _3__v1 (
    .D(demultiplexer_1_out3), .en(demultiplexer_2_out3), .Q(_3__v1_q), .clk(Clock), .clr(1'b0));
  Register #(.width(32)) _4__a0 (
    .D(demultiplexer_1_out4), .en(demultiplexer_2_out4), .Q(a0_Value), .clk(Clock), .clr(1'b0));
  Register #(.width(32)) _5__a1 (
    .D(demultiplexer_1_out5), .en(demultiplexer_2_out5), .Q(_5__a1_q), .clk(Clock), .clr(1'b0));
  Register #(.width(32)) _6__a2 (
    .D(demultiplexer_1_out6), .en(demultiplexer_2_out6), .Q(_6__a2_q), .clk(Clock), .clr(1'b0));
  Register #(.width(32)) _7__a3 (
    .D(demultiplexer_1_out7), .en(demultiplexer_2_out7), .Q(_7__a3_q), .clk(Clock), .clr(1'b0));
  Register #(.width(32)) _8__t0 (
    .D(demultiplexer_1_out8), .en(demultiplexer_2_out8), .Q(_8__t0_q), .clk(Clock), .clr(1'b0));
  Register #(.width(32)) _9__t1 (
    .D(demultiplexer_1_out9), .en(demultiplexer_2_out9), .Q(_9__t1_q), .clk(Clock), .clr(1'b0));
  Register #(.width(32)) _10__t2 (
    .D(demultiplexer_1_out10), .en(demultiplexer_2_out10), .Q(_10__t2_q), .clk(Clock), .clr(1'b0));
  Register #(.width(32)) _11__t3 (
    .D(demultiplexer_1_out11), .en(demultiplexer_2_out11), .Q(_11__t3_q), .clk(Clock), .clr(1'b0));
  Register #(.width(32)) _12__t4 (
    .D(demultiplexer_1_out12), .en(demultiplexer_2_out12), .Q(_12__t4_q), .clk(Clock), .clr(1'b0));
  Register #(.width(32)) _13__t5 (
    .D(demultiplexer_1_out13), .en(demultiplexer_2_out13), .Q(_13__t5_q), .clk(Clock), .clr(1'b0));
  Register #(.width(32)) _14__t6 (
    .D(demultiplexer_1_out14), .en(demultiplexer_2_out14), .Q(_14__t6_q), .clk(Clock), .clr(1'b0));
  Register #(.width(32)) _15__t7 (
    .D(demultiplexer_1_out15), .en(demultiplexer_2_out15), .Q(_15__t7_q), .clk(Clock), .clr(1'b0));
  Register #(.width(32)) _16__s0 (
    .D(demultiplexer_1_out16), .en(demultiplexer_2_out16), .Q(s0_Value), .clk(Clock), .clr(1'b0));
  Register #(.width(32)) _17__s1 (
    .D(demultiplexer_1_out17), .en(demultiplexer_2_out17), .Q(_17__s1_q), .clk(Clock), .clr(1'b0));
  Register #(.width(32)) _18___s2 (
    .D(demultiplexer_1_out18), .en(demultiplexer_2_out18), .Q(_18___s2_q), .clk(Clock), .clr(1'b0));
  Register #(.width(32)) _19___s3 (
    .D(demultiplexer_1_out19), .en(demultiplexer_2_out19), .Q(_19___s3_q), .clk(Clock), .clr(1'b0));
  Register #(.width(32)) _20___s4 (
    .D(demultiplexer_1_out20), .en(demultiplexer_2_out20), .Q(_20___s4_q), .clk(Clock), .clr(1'b0));
  Register #(.width(32)) _21__s5 (
    .D(demultiplexer_1_out21), .en(demultiplexer_2_out21), .Q(_21__s5_q), .clk(Clock), .clr(1'b0));
  Register #(.width(32)) _22__s6 (
    .D(demultiplexer_1_out22), .en(demultiplexer_2_out22), .Q(_22__s6_q), .clk(Clock), .clr(1'b0));
  Register #(.width(32)) _23__s7 (
    .D(demultiplexer_1_out23), .en(demultiplexer_2_out23), .Q(_23__s7_q), .clk(Clock), .clr(1'b0));
  Register #(.width(32)) _24__t8 (
    .D(demultiplexer_1_out24), .en(demultiplexer_2_out24), .Q(_24__t8_q), .clk(Clock), .clr(1'b0));
  Register #(.width(32)) _25__t9 (
    .D(demultiplexer_1_out25), .en(demultiplexer_2_out25), .Q(_25__t9_q), .clk(Clock), .clr(1'b0));
  Register #(.width(32)) _26__k0 (
    .D(demultiplexer_1_out26), .en(demultiplexer_2_out26), .Q(_26__k0_q), .clk(Clock), .clr(1'b0));
  Register #(.width(32)) _27__k1 (
    .D(demultiplexer_1_out27), .en(demultiplexer_2_out27), .Q(_27__k1_q), .clk(Clock), .clr(1'b0));
  Register #(.width(32)) _28__gp (
    .D(demultiplexer_1_out28), .en(demultiplexer_2_out28), .Q(_28__gp_q), .clk(Clock), .clr(1'b0));
  Register #(.width(32)) _29__sp (
    .D(demultiplexer_1_out29), .en(demultiplexer_2_out29), .Q(_29__sp_q), .clk(Clock), .clr(1'b0));
  Register #(.width(32)) _30__fp (
    .D(demultiplexer_1_out30), .en(demultiplexer_2_out30), .Q(_30__fp_q), .clk(Clock), .clr(1'b0));
  Register #(.width(32)) _31__ra (
    .D(demultiplexer_1_out31), .en(demultiplexer_2_out31), .Q(ra_Value), .clk(Clock), .clr(1'b0));
  // Probe on _0__zero_q
  // Probe on _1__at_q
  // Probe on v0_Value
  // Probe on _3__v1_q
  // Probe on a0_Value
  // Probe on _5__a1_q
  // Probe on _6__a2_q
  // Probe on _7__a3_q
  // Probe on _8__t0_q
  // Probe on _9__t1_q
  // Probe on _10__t2_q
  // Probe on _11__t3_q
  // Probe on _12__t4_q
  // Probe on _13__t5_q
  // Probe on _14__t6_q
  // Probe on _15__t7_q
  // Probe on s0_Value
  // Probe on _17__s1_q
  // Probe on _18___s2_q
  // Probe on _19___s3_q
  // Probe on _20___s4_q
  // Probe on _21__s5_q
  // Probe on _22__s6_q
  // Probe on _23__s7_q
  // Probe on _24__t8_q
  // Probe on _25__t9_q
  // Probe on _26__k0_q
  // Probe on _27__k1_q
  // Probe on _28__gp_q
  // Probe on _29__sp_q
  // Probe on _30__fp_q
  // Probe on ra_Value
  Multiplexer #(.select(5), .width(32)) multiplexer_1 (
    .in0(_0__zero_q), .in1(_1__at_q), .in2(v0_Value), .in3(_3__v1_q), .in4(a0_Value), .in5(_5__a1_q),
    .in6(_6__a2_q), .in7(_7__a3_q), .in8(_8__t0_q), .in9(_9__t1_q), .in10(_10__t2_q), .in11(_11__t3_q),
    .in12(_12__t4_q), .in13(_13__t5_q), .in14(_14__t6_q), .in15(_15__t7_q), .in16(s0_Value),
    .in17(_17__s1_q), .in18(_18___s2_q), .in19(_19___s3_q), .in20(_20___s4_q), .in21(_21__s5_q),
    .in22(_22__s6_q), .in23(_23__s7_q), .in24(_24__t8_q), .in25(_25__t9_q), .in26(_26__k0_q),
    .in27(_27__k1_q), .in28(_28__gp_q), .in29(_29__sp_q), .in30(_30__fp_q), .in31(ra_Value), .out(Reg2_2),
    .sel(Reg2), .en(1'b1));
  Multiplexer #(.select(5), .width(32)) multiplexer_2 (
    .in0(_0__zero_q), .in1(_1__at_q), .in2(v0_Value), .in3(_3__v1_q), .in4(a0_Value), .in5(_5__a1_q),
    .in6(_6__a2_q), .in7(_7__a3_q), .in8(_8__t0_q), .in9(_9__t1_q), .in10(_10__t2_q), .in11(_11__t3_q),
    .in12(_12__t4_q), .in13(_13__t5_q), .in14(_14__t6_q), .in15(_15__t7_q), .in16(s0_Value),
    .in17(_17__s1_q), .in18(_18___s2_q), .in19(_19___s3_q), .in20(_20___s4_q), .in21(_21__s5_q),
    .in22(_22__s6_q), .in23(_23__s7_q), .in24(_24__t8_q), .in25(_25__t9_q), .in26(_26__k0_q),
    .in27(_27__k1_q), .in28(_28__gp_q), .in29(_29__sp_q), .in30(_30__fp_q), .in31(ra_Value), .out(Reg1),
    .sel(Reg1_num), .en(1'b1));

  // Other names for the same wires on the sheet: a0[31:0] = a0_Value; clk = Clock; ra[31:0] = ra_Value;
  //   reg2_num[4:0] = Reg2; reg2_t[31:0] = Reg2_2; s0[31:0] = s0_Value; v0[31:0] = v0_Value; WE = Write_Enable;
  //   write_data[31:0] = Din

  // Notes on the sheet:
  //   输入引脚
  //   输出引脚
  //   请在下方利用上方输入输出引脚的隧道信号构建ALU电路，ctrl+d复制选择部件
  //   Debug引脚，便于观测寄存器值
  //   请勿修改引脚以及封装，直接使用隧道连接电路
endmodule
