// Logisim project MIPS CPU2.circ as structural Verilog: 3 circuits, main circuit main
module main (
);

  wire ALUSrc, and_1_out, BNE, Branch, CLK, clock_1_out, comparator_1_gt, controlled_buffer_1_out, Equal,
       Jump, MemRead, MemtoReg, MemWrite, multiplexer_3_out, nCLK, not_1_out, not_2_out, not_4_out, RegDst,
       RegWrite, SYSCALL;
  wire [1:0] AluOP;
  wire [3:0] aluop_1_alu;
  wire [4:0] multiplexer_1_out;
  wire [15:0] counter_2_q;
  wire [31:0] adder_1_out, adder_2_out, alu_1_result, bit_extender_1_out, counter_1_q, main_1_reg1,
       main_1_reg2_2, multiplexer_2_out, multiplexer_4_out, multiplexer_5_out, PC_q, ram_1_data, rom_1_data,
       shifter_1_out;

  Register #(.width(32)) PC (.D(multiplexer_4_out), .en(1'b1), .Q(PC_q), .clk(controlled_buffer_1_out));  // open: clr
  assign controlled_buffer_1_out = not_1_out ? CLK : 1'bz;  // Controlled_Buffer controlled_buffer_1
  not not_1 (not_1_out, comparator_1_gt);
  Counter #(.width(32), .max('hffffffff)) counter_1 (
    .load(1'b0), .count(1'b1), .Q(counter_1_q), .clk(CLK));  // open: D, carry, clr
  Comparator #(.width(32), .mode("unsigned")) comparator_1 (
    .a(32'h1), .b(counter_1_q), .gt(comparator_1_gt));  // open: eq, lt
  Adder #(.width(32)) adder_1 (.a(PC_q), .b(32'h4), .out(adder_1_out));  // open: cin, cout
  ROM #(.addrWidth(10), .dataWidth(32)) rom_1 (.addr(PC_q[11:2]), .data(rom_1_data));  // open: sel
  Control control_1 (
    .OP(rom_1_data[31:26]), .Funct(rom_1_data[5:0]), .RegDst(RegDst), .RegWrite(RegWrite), .AluOP(AluOP),
    .Branch(Branch), .Jump(Jump), .MemRead(MemRead), .MemWrite(MemWrite), .MemtoReg(MemtoReg),
    .ALUSrc(ALUSrc), .SYSCALL(SYSCALL), .BNE(BNE));
  assign CLK = not_2_out ? clock_1_out : 1'bz;  // Controlled_Buffer controlled_buffer_2
  not not_2 (not_2_out, SYSCALL);
  Clock clock_1 (.out(clock_1_out));
  not not_3 (nCLK, CLK);
  Counter #(.width(16), .max('hffff)) counter_2 (.Q(counter_2_q), .clk(CLK));  // open: load, D, count, carry, clr
  Multiplexer #(.width(5)) multiplexer_1 (
    .in0(rom_1_data[15:11]), .in1(rom_1_data[20:16]), .out(multiplexer_1_out), .sel(RegDst), .en(1'b1));
  AluOP aluop_1 (.Funct(rom_1_data[5:0]), .ALU(aluop_1_alu), .AluOP(AluOP));
  assign bit_extender_1_out = {{16{rom_1_data[15]}}, rom_1_data[15:0]};  // Bit_Extender bit_extender_1
  // Probe on counter_2_q
  regfile_main main_1 (
    .Reg1_num(rom_1_data[25:21]), .Reg2(rom_1_data[20:16]), .Write_Reg_num(multiplexer_1_out),
    .Din(multiplexer_5_out), .Write_Enable(RegWrite), .Clock(nCLK), .Reg1(main_1_reg1), .Reg2_2(main_1_reg2_2));  // open: s0_Value, s1_Value, s2_Value, ra_Value
  Shifter #(.width(32)) shifter_1 (.in(bit_extender_1_out), .\dist (5'b00010), .out(shifter_1_out));
  not not_4 (not_4_out, Equal);
  Multiplexer #(.width(32)) multiplexer_2 (
    .in0(main_1_reg2_2), .in1(bit_extender_1_out), .out(multiplexer_2_out), .sel(ALUSrc), .en(1'b1));
  Adder #(.width(32)) adder_2 (.a(adder_1_out), .b(shifter_1_out), .out(adder_2_out), .cin(1'b0));  // open: cout
  Multiplexer multiplexer_3 (.in0(Equal), .in1(not_4_out), .out(multiplexer_3_out), .sel(BNE), .en(1'b1));
  ALU alu_1 (
    .AluOP(aluop_1_alu), .X(main_1_reg1), .Equal(Equal), .Result(alu_1_result), .Y(multiplexer_2_out));  // open: Signed_Overflow, Result_2, UnSigned_Overflow
  and and_1 (and_1_out, Branch, multiplexer_3_out);
  Multiplexer #(.width(32)) multiplexer_4 (
    .in0(adder_1_out), .in1(adder_2_out), .out(multiplexer_4_out), .sel(and_1_out), .en(1'b1));
  RAM #(.addrWidth(16), .dataWidth(32), .bus("separate")) ram_1 (
    .addr(alu_1_result[17:2]), .din(main_1_reg2_2), .data(ram_1_data), .str(MemWrite), .sel(1'b1),
    .clk(nCLK), .ld(MemRead), .clr(1'b0));
  Multiplexer #(.width(32)) multiplexer_5 (
    .in0(ram_1_data), .in1(alu_1_result), .out(multiplexer_5_out), .sel(MemtoReg), .en(1'b1));

  // Notes on the sheet:
  //   contents of rom_1 (hex, n*v repeats v):
  //   2010ffff 20110000 ae300000 22100001 22310004 ae300000 22100001 22310004 ae300000 22100001 22310004
  //   ae300000 22100001 22310004 ae300000 22100001 22310004 ae300000 22100001 22310004 ae300000 22100001
  //   22310004 ae300000 22100001 22310004 ae300000 22100001 22310004 ae300000 22100001 22310004 ae300000
  //   22100001 22310004 ae300000 22100001 22310004 ae300000 22100001 22310004 ae300000 22100001 22310004
  //   ae300000 22100001 22310004 ae300000 22100001 22310004 22100001 8020 2011003c 8e130000 8e340000
  //   274402a 11000002 ae330000 ae140000 2231fffc 1611fff8 22100004 2011003c 1611fff5 2002000a c
endmodule

module Control (
  input  [5:0] OP,
  input  [5:0] Funct,
  output SYSCALL,
  output MemRead,
  output RegDst,
  output BNE,
  output MemWrite,
  output RegWrite,
  output MemtoReg,
  output [1:0] AluOP,
  output ALUSrc,
  output Branch,
  output Jump
);

  wire ADD, ADDI, BEQ, not_1_out, not_2_out, not_3_out, not_4_out, not_5_out, not_6_out, not_7_out,
       not_8_out, not_9_out, not_10_out, not_11_out, not_12_out, not_13_out, not_14_out, not_15_out,
       not_16_out, not_17_out, not_18_out, not_19_out, not_20_out, not_21_out, not_22_out, not_23_out,
       not_24_out, not_25_out, not_26_out, not_27_out, not_28_out, not_29_out, not_30_out, not_31_out,
       not_32_out, not_33_out, not_34_out, not_35_out, not_36_out, not_37_out, Q, SLT;
  wire [1:1] or_1_out;

  not not_1 (not_1_out, OP[5]);
  not not_2 (not_2_out, OP[4]);
  not not_3 (not_3_out, OP[3]);
  not not_4 (not_4_out, OP[2]);
  not not_5 (not_5_out, OP[1]);
  not not_6 (not_6_out, OP[0]);
  not not_7 (not_7_out, OP[5]);
  not not_8 (not_8_out, OP[4]);
  not not_9 (not_9_out, OP[2]);
  not not_10 (not_10_out, OP[1]);
  not not_11 (not_11_out, OP[0]);
  not not_12 (not_12_out, OP[4]);
  not not_13 (not_13_out, OP[3]);
  not not_14 (not_14_out, OP[2]);
  not not_15 (not_15_out, OP[4]);
  not not_16 (not_16_out, OP[2]);
  not not_17 (not_17_out, OP[5]);
  not not_18 (not_18_out, OP[4]);
  not not_19 (not_19_out, OP[3]);
  not not_20 (not_20_out, OP[1]);
  not not_21 (not_21_out, OP[5]);
  not not_22 (not_22_out, OP[4]);
  not not_23 (not_23_out, OP[3]);
  not not_24 (not_24_out, OP[1]);
  not not_25 (not_25_out, OP[0]);
  and u_Q (Q, not_1_out, not_2_out, not_3_out, not_4_out, not_5_out, not_6_out);
  and u_ADDI (ADDI, not_7_out, not_8_out, OP[3], not_9_out, not_10_out, not_11_out);
  and LW (MemRead, OP[5], not_12_out, not_13_out, not_14_out, OP[1], OP[0]);
  and SW (MemWrite, OP[5], not_15_out, OP[3], not_16_out, OP[1], OP[0]);
  and u_BNE (BNE, not_17_out, not_18_out, not_19_out, OP[2], not_20_out, OP[0]);
  and u_BEQ (BEQ, not_21_out, not_22_out, not_23_out, OP[2], not_24_out, not_25_out);
  or or_1 (or_1_out[1], ADD, SLT);
  not not_26 (not_26_out, Funct[4]);
  not not_27 (not_27_out, Funct[3]);
  not not_28 (not_28_out, Funct[2]);
  not not_29 (not_29_out, Funct[1]);
  not not_30 (not_30_out, Funct[0]);
  not not_31 (not_31_out, Funct[4]);
  not not_32 (not_32_out, Funct[2]);
  not not_33 (not_33_out, Funct[0]);
  not not_34 (not_34_out, Funct[5]);
  not not_35 (not_35_out, Funct[4]);
  not not_36 (not_36_out, Funct[1]);
  not not_37 (not_37_out, Funct[0]);
  or or_2 (RegDst, ADDI, MemRead);
  or or_3 (RegWrite, ADD, ADDI, MemRead, SLT);
  Multiplexer #(.select(2), .width(2)) multiplexer_1 (
    .in0(2'b00), .in1(2'b01), .in2(2'b10), .out(AluOP), .sel({or_1_out[1], 1'b0}), .en(1'b1));  // open: in3
  or or_4 (Branch, BNE, BEQ);
  and u_ADD (ADD, Funct[5], not_26_out, not_27_out, not_28_out, not_29_out, not_30_out, Q);
  and u_SLT (SLT, Funct[5], not_31_out, Funct[3], not_32_out, Funct[1], not_33_out, Q);
  and u_SYSCALL (SYSCALL, not_34_out, not_35_out, Funct[3], Funct[2], not_36_out, not_37_out, Q);
  not not_38 (MemtoReg, MemRead);
  or or_5 (ALUSrc, ADDI, MemRead, MemWrite);

  assign Jump = 1'b0;

  // Other names for the same wires on the sheet: LW = MemRead; SW = MemWrite
endmodule

module AluOP (
  input  [5:0] Funct,
  input  [1:0] AluOP,
  output [3:0] ALU
);

  wire not_1_out, not_2_out, not_3_out, SLT;
  wire [3:0] multiplexer_1_out;

  Multiplexer #(.width(4)) multiplexer_1 (.in0(4'b0101), .in1(4'b1011), .out(multiplexer_1_out), .sel(SLT), .en(1'b1));
  not not_1 (not_1_out, Funct[4]);
  not not_2 (not_2_out, Funct[2]);
  not not_3 (not_3_out, Funct[0]);
  Multiplexer #(.select(2), .width(4)) multiplexer_2 (
    .in0(4'b0101), .in1(4'b0110), .in2(multiplexer_1_out), .out(ALU), .sel(AluOP), .en(1'b1));  // open: in3
  and u_SLT (SLT, Funct[5], not_1_out, Funct[3], not_2_out, Funct[1], not_3_out);
endmodule
