// Logisim project MIPS CPU_single circle - 副本.circ as structural Verilog: 8 circuits, main circuit main
module main (
);

  wire A, and_3_out, B, Branch, CLK, clock_1_out, comparator_1_gt, comparator_2_eq, controlled_buffer_1_out,
       Disp, Equal, Halt, IsBNE, IsSyscall, JR, Jump, MemRead, MemtoReg, MemWrite, multiplexer_10_out, nCLK,
       not_1_out, not_2_out, not_4_out, not_5_out, R1_num, R2_num, RegWrite;
  wire [1:0] Din, S_EXT, W_num;
  wire [3:0] adder_1_out_2, AluOp;
  wire [4:0] multiplexer_2_out, multiplexer_3_out, multiplexer_4_out, multiplexer_6_out;
  wire [15:0] counter_2_q, multiplexer_5_out;
  wire [27:0] adder_1_out;
  wire [27:2] rom_1_data_2;
  wire [31:0] a0, adder_2_out, alu_1_result, bit_extender_1_out, counter_1_q, main_1_reg2_2,
       multiplexer_1_out, multiplexer_7_out, multiplexer_8_out, multiplexer_9_out, multiplexer_11_out,
       multiplexer_12_out, PC_q, ram_1_data, register_1_q, shifter_1_out;
  wire [31:26] rom_1_data;

  Multiplexer #(.width(32)) multiplexer_1 (
    .in0(multiplexer_9_out), .in1(a0), .out(multiplexer_1_out), .sel(JR), .en(1'b1));
  Register #(.width(32)) PC (.D(multiplexer_1_out), .en(1'b1), .Q(PC_q), .clk(controlled_buffer_1_out));  // open: clr
  assign controlled_buffer_1_out = not_1_out ? CLK : 1'bz;  // Controlled_Buffer controlled_buffer_1
  not not_1 (not_1_out, comparator_1_gt);
  Counter #(.width(32), .max('hffffffff)) counter_1 (
    .load(1'b0), .count(1'b1), .Q(counter_1_q), .clk(CLK));  // open: D, carry, clr
  Comparator #(.width(32), .mode("unsigned")) comparator_1 (
    .a(32'h1), .b(counter_1_q), .gt(comparator_1_gt));  // open: eq, lt
  Adder #(.width(32)) adder_1 (.a(PC_q), .b(32'h4), .out({adder_1_out_2, adder_1_out}));  // open: cin, cout
  ROM #(.addrWidth(10), .dataWidth(32)) rom_1 (.addr(PC_q[11:2]), .data({rom_1_data, rom_1_data_2}));  // open: sel
  Control control_1 (
    .OP(rom_1_data), .Funct(rom_1_data_2[7:2]), .R1_num(R1_num), .R2_num(R2_num), .W_num(W_num), .Din(Din),
    .S_EXT(S_EXT), .A(A), .B(B), .AluOP(AluOp), .Branch(Branch), .Jump(Jump), .RegWrite(RegWrite),
    .MemRead(MemRead), .MemWrite(MemWrite), .MemtoReg(MemtoReg), .IsBNE(IsBNE), .IsSyscall(IsSyscall), .JR(JR));
  Multiplexer #(.width(5)) multiplexer_2 (
    .in0(rom_1_data_2[27:23]), .in1(rom_1_data_2[22:18]), .out(multiplexer_2_out), .sel(R1_num), .en(1'b1));
  Multiplexer #(.select(2), .width(5)) multiplexer_3 (
    .in0(rom_1_data_2[17:13]), .in1(rom_1_data_2[22:18]), .in2({5{1'b1}}), .out(multiplexer_3_out),
    .sel(W_num), .en(1'b1));  // open: in3
  assign CLK = not_2_out ? clock_1_out : 1'bz;  // Controlled_Buffer controlled_buffer_2
  not not_2 (not_2_out, Halt);
  Clock clock_1 (.out(clock_1_out));
  Multiplexer #(.width(5)) multiplexer_4 (
    .in0(multiplexer_2_out), .in1(5'b00100), .out(multiplexer_4_out), .sel(R2_num), .en(1'b1));
  Multiplexer #(.select(2), .width(16)) multiplexer_5 (
    .in0(rom_1_data_2[17:2]), .in1({{11{1'b0}}, rom_1_data_2[12:8]}), .in2(16'ha), .out(multiplexer_5_out),
    .sel(S_EXT), .en(1'b1));  // open: in3
  not not_3 (nCLK, CLK);
  Multiplexer #(.width(5)) multiplexer_6 (
    .in0(rom_1_data_2[22:18]), .in1(5'b00010), .out(multiplexer_6_out), .sel(R2_num), .en(1'b1));
  assign bit_extender_1_out = {{16{multiplexer_5_out[15]}}, multiplexer_5_out};  // Bit_Extender bit_extender_1
  Counter #(.width(16), .max('hffff)) counter_2 (.Q(counter_2_q), .clk(CLK));  // open: load, D, count, carry, clr
  regfile_main main_1 (
    .Reg1_num(multiplexer_4_out), .Reg2(multiplexer_6_out), .Write_Reg_num(multiplexer_3_out),
    .Din(multiplexer_11_out), .Write_Enable(RegWrite), .Clock(nCLK), .Reg1(a0), .Reg2_2(main_1_reg2_2));  // open: s0_Value, s1_Value, s2_Value, ra_Value
  // Probe on counter_2_q
  not not_4 (not_4_out, comparator_2_eq);
  Comparator #(.width(32)) comparator_2 (.a(32'ha), .b(main_1_reg2_2), .eq(comparator_2_eq));  // open: gt, lt
  Multiplexer #(.width(32)) multiplexer_7 (.in0(a0), .in1(main_1_reg2_2), .out(multiplexer_7_out), .sel(A), .en(1'b1));
  and and_1 (Disp, IsSyscall, not_4_out);
  and and_2 (Halt, IsSyscall, comparator_2_eq);
  Hex_Digit_Display hex_digit_display_1 (.value(register_1_q[31:28]), .dp(1'b0));
  Register #(.width(32)) register_1 (.D(a0), .en(Disp), .Q(register_1_q), .clk(CLK), .clr(1'b0));
  Multiplexer #(.width(32)) multiplexer_8 (
    .in0(main_1_reg2_2), .in1(bit_extender_1_out), .out(multiplexer_8_out), .sel(B), .en(1'b1));
  Hex_Digit_Display hex_digit_display_2 (.value(register_1_q[27:24]), .dp(1'b0));
  Hex_Digit_Display hex_digit_display_3 (.value(register_1_q[23:20]), .dp(1'b0));
  ALU alu_1 (
    .AluOP(AluOp), .X(multiplexer_7_out), .Equal(Equal), .Result(alu_1_result), .Y(multiplexer_8_out));  // open: Signed_Overflow, Result_2, UnSigned_Overflow
  Hex_Digit_Display hex_digit_display_4 (.value(register_1_q[19:16]), .dp(1'b0));
  Hex_Digit_Display hex_digit_display_5 (.value(register_1_q[15:12]), .dp(1'b0));
  Multiplexer #(.width(32)) multiplexer_9 (
    .in0(multiplexer_12_out), .in1({adder_1_out_2, rom_1_data_2, 2'b00}), .out(multiplexer_9_out),
    .sel(Jump), .en(1'b1));
  Hex_Digit_Display hex_digit_display_6 (.value(register_1_q[7:4]), .dp(1'b0));
  Hex_Digit_Display hex_digit_display_7 (.value(register_1_q[11:8]), .dp(1'b0));
  Hex_Digit_Display hex_digit_display_8 (.value(register_1_q[3:0]), .dp(1'b0));
  Shifter #(.width(32)) shifter_1 (.in(bit_extender_1_out), .\dist (5'b00010), .out(shifter_1_out));
  Adder #(.width(32)) adder_2 (
    .a({adder_1_out_2, adder_1_out}), .b(shifter_1_out), .out(adder_2_out), .cin(1'b0));  // open: cout
  Multiplexer multiplexer_10 (.in0(Equal), .in1(not_5_out), .out(multiplexer_10_out), .sel(IsBNE), .en(1'b1));
  not not_5 (not_5_out, Equal);
  RAM #(.addrWidth(16), .dataWidth(32), .bus("separate")) ram_1 (
    .addr(alu_1_result[17:2]), .din(main_1_reg2_2), .data(ram_1_data), .str(MemWrite), .sel(1'b1),
    .clk(nCLK), .ld(MemRead), .clr(1'b0));
  and and_3 (and_3_out, Branch, multiplexer_10_out);
  Multiplexer #(.select(2), .width(32)) multiplexer_11 (
    .in0(alu_1_result), .in1(ram_1_data), .in2({adder_1_out_2, adder_1_out}), .out(multiplexer_11_out),
    .sel(Din), .en(1'b1));  // open: in3
  Multiplexer #(.width(32)) multiplexer_12 (
    .in0({adder_1_out_2, adder_1_out}), .in1(adder_2_out), .out(multiplexer_12_out), .sel(and_3_out),
    .en(1'b1));

  // Notes on the sheet:
  //   contents of rom_1 (hex, n*v repeats v):
  //   2010ffff 20110000 ae300000 22100001 22310004 ae300000 22100001 22310004 ae300000 22100001 22310004
  //   ae300000 22100001 22310004 ae300000 22100001 22310004 ae300000 22100001 22310004 ae300000 22100001
  //   22310004 ae300000 22100001 22310004 ae300000 22100001 22310004 ae300000 22100001 22310004 ae300000
  //   22100001 22310004 ae300000 22100001 22310004 ae300000 22100001 22310004 ae300000 22100001 22310004
  //   ae300000 22100001 22310004 ae300000 22100001 22310004 22100001 8020 2011003c 8e130000 8e340000
  //   274402a 11000002 ae330000 ae140000 2231fffc 1611fff8 102020 20020022 c 22100004 2011003c 1611fff2
  //   2002000a c
endmodule

module Control (
  input  [5:0] OP,
  input  [5:0] Funct,
  output R1_num,
  output R2_num,
  output [1:0] W_num,
  output [3:0] AluOP,
  output [1:0] Din,
  output [1:0] S_EXT,
  output A,
  output B,
  output JR,
  output Branch,
  output Jump,
  output RegWrite,
  output MemRead,
  output MemWrite,
  output MemtoReg,
  output IsBNE,
  output IsSyscall
);

  wire controlsignal_funct_decoder1_1_a, controlsignal_funct_decoder1_1_b, controlsignal_funct_decoder1_1_r1,
       controlsignal_funct_decoder1_1_r2, controlsignal_funct_decoder2_1_branch,
       controlsignal_funct_decoder2_1_isbne, controlsignal_funct_decoder2_1_issyscall,
       controlsignal_funct_decoder2_1_jr, controlsignal_funct_decoder2_1_jump,
       controlsignal_funct_decoder2_1_memread, controlsignal_funct_decoder2_1_memtoreg,
       controlsignal_funct_decoder2_1_memwrite, controlsignal_funct_decoder2_1_regwrite,
       controlsignal_op_decoder1_1_a, controlsignal_op_decoder1_1_b, controlsignal_op_decoder1_1_r1,
       controlsignal_op_decoder1_1_r2, controlsignal_op_decoder2_1_branch, controlsignal_op_decoder2_1_isbne,
       controlsignal_op_decoder2_1_issyscall, controlsignal_op_decoder2_1_jr,
       controlsignal_op_decoder2_1_jump, controlsignal_op_decoder2_1_memread,
       controlsignal_op_decoder2_1_memtoreg, controlsignal_op_decoder2_1_memwrite,
       controlsignal_op_decoder2_1_regwrite, Is_R_Type;
  wire [1:0] controlsignal_funct_decoder1_1_din1, controlsignal_funct_decoder1_1_sext1,
       controlsignal_funct_decoder1_1_w1, controlsignal_op_decoder1_1_din1,
       controlsignal_op_decoder1_1_sext1, controlsignal_op_decoder1_1_w1;
  wire [3:0] alu_funct_decoder_1_aluop3, alu_op_decoder_1_aluop3;

  ALU_Op_Decoder alu_op_decoder_1 (
    .op0(OP[5]), .op1(OP[4]), .op2(OP[3]), .aluop0(alu_op_decoder_1_aluop3[3]), .op3(OP[2]), .op4(OP[1]),
    .op5(OP[0]), .aluop1(alu_op_decoder_1_aluop3[2]), .aluop2(alu_op_decoder_1_aluop3[1]),
    .aluop3(alu_op_decoder_1_aluop3[0]));
  ALU_Funct_Decoder alu_funct_decoder_1 (
    .funct0(Funct[5]), .funct1(Funct[4]), .funct2(Funct[3]), .funct3(Funct[2]), .funct4(Funct[1]),
    .funct5(Funct[0]), .aluop0(alu_funct_decoder_1_aluop3[3]), .aluop1(alu_funct_decoder_1_aluop3[2]),
    .aluop2(alu_funct_decoder_1_aluop3[1]), .aluop3(alu_funct_decoder_1_aluop3[0]));
  Controlsignal_Op_Decoder1 controlsignal_op_decoder1_1 (
    .op0(OP[5]), .op1(OP[4]), .R1(controlsignal_op_decoder1_1_r1), .op2(OP[3]),
    .R2(controlsignal_op_decoder1_1_r2), .op3(OP[2]), .W0(controlsignal_op_decoder1_1_w1[1]), .op4(OP[1]),
    .op5(OP[0]), .W1(controlsignal_op_decoder1_1_w1[0]), .Din0(controlsignal_op_decoder1_1_din1[1]),
    .Din1(controlsignal_op_decoder1_1_din1[0]), .SEXT0(controlsignal_op_decoder1_1_sext1[1]),
    .SEXT1(controlsignal_op_decoder1_1_sext1[0]), .A(controlsignal_op_decoder1_1_a),
    .B(controlsignal_op_decoder1_1_b));
  Controlsignal_Funct_Decoder1 controlsignal_funct_decoder1_1 (
    .funct0(Funct[5]), .funct1(Funct[4]), .funct2(Funct[3]), .funct3(Funct[2]), .funct4(Funct[1]),
    .R1(controlsignal_funct_decoder1_1_r1), .funct5(Funct[0]), .R2(controlsignal_funct_decoder1_1_r2),
    .W0(controlsignal_funct_decoder1_1_w1[1]), .W1(controlsignal_funct_decoder1_1_w1[0]),
    .Din0(controlsignal_funct_decoder1_1_din1[1]), .Din1(controlsignal_funct_decoder1_1_din1[0]),
    .SEXT0(controlsignal_funct_decoder1_1_sext1[1]), .SEXT1(controlsignal_funct_decoder1_1_sext1[0]),
    .A(controlsignal_funct_decoder1_1_a), .B(controlsignal_funct_decoder1_1_b));
  Controlsignal_Op_Decoder2 controlsignal_op_decoder2_1 (
    .op0(OP[5]), .JR(controlsignal_op_decoder2_1_jr), .op1(OP[4]), .op2(OP[3]), .op3(OP[2]),
    .Branch(controlsignal_op_decoder2_1_branch), .op4(OP[1]), .op5(OP[0]),
    .Jump(controlsignal_op_decoder2_1_jump), .RegWrite(controlsignal_op_decoder2_1_regwrite),
    .MemRead(controlsignal_op_decoder2_1_memread), .MemWrite(controlsignal_op_decoder2_1_memwrite),
    .MemtoReg(controlsignal_op_decoder2_1_memtoreg), .IsBNE(controlsignal_op_decoder2_1_isbne),
    .isSyscall(controlsignal_op_decoder2_1_issyscall));
  Controlsignal_Funct_Decoder2 controlsignal_funct_decoder2_1 (
    .funct0(Funct[5]), .funct1(Funct[4]), .JR(controlsignal_funct_decoder2_1_jr), .funct2(Funct[3]),
    .funct3(Funct[2]), .Branch(controlsignal_funct_decoder2_1_branch), .funct4(Funct[1]),
    .Jump(controlsignal_funct_decoder2_1_jump), .funct5(Funct[0]),
    .RegWrite(controlsignal_funct_decoder2_1_regwrite), .MemRead(controlsignal_funct_decoder2_1_memread),
    .MemWrite(controlsignal_funct_decoder2_1_memwrite), .MemtoReg(controlsignal_funct_decoder2_1_memtoreg),
    .IsBNE(controlsignal_funct_decoder2_1_isbne), .IsSyscall(controlsignal_funct_decoder2_1_issyscall));
  nor nor_1 (Is_R_Type, OP[5], OP[4], OP[3], OP[2], OP[1], OP[0]);
  Multiplexer #(.width(4)) multiplexer_1 (
    .in0(alu_op_decoder_1_aluop3), .in1(alu_funct_decoder_1_aluop3), .out(AluOP), .sel(Is_R_Type), .en(1'b1));
  Multiplexer multiplexer_2 (
    .in0(controlsignal_op_decoder1_1_r1), .in1(controlsignal_funct_decoder1_1_r1), .out(R1_num),
    .sel(Is_R_Type), .en(1'b1));
  Multiplexer multiplexer_3 (
    .in0(controlsignal_op_decoder1_1_r2), .in1(controlsignal_funct_decoder1_1_r2), .out(R2_num),
    .sel(Is_R_Type), .en(1'b1));
  Multiplexer #(.width(2)) multiplexer_4 (
    .in0(controlsignal_op_decoder1_1_w1), .in1(controlsignal_funct_decoder1_1_w1), .out(W_num),
    .sel(Is_R_Type), .en(1'b1));
  Multiplexer #(.width(2)) multiplexer_5 (
    .in0(controlsignal_op_decoder1_1_din1), .in1(controlsignal_funct_decoder1_1_din1), .out(Din),
    .sel(Is_R_Type), .en(1'b1));
  Multiplexer #(.width(2)) multiplexer_6 (
    .in0(controlsignal_op_decoder1_1_sext1), .in1(controlsignal_funct_decoder1_1_sext1), .out(S_EXT),
    .sel(Is_R_Type), .en(1'b1));
  Multiplexer multiplexer_7 (
    .in0(controlsignal_op_decoder1_1_a), .in1(controlsignal_funct_decoder1_1_a), .out(A), .sel(Is_R_Type),
    .en(1'b1));
  Multiplexer multiplexer_8 (
    .in0(controlsignal_op_decoder1_1_b), .in1(controlsignal_funct_decoder1_1_b), .out(B), .sel(Is_R_Type),
    .en(1'b1));
  Multiplexer multiplexer_9 (
    .in0(controlsignal_op_decoder2_1_jr), .in1(controlsignal_funct_decoder2_1_jr), .out(JR), .sel(Is_R_Type),
    .en(1'b1));
  Multiplexer multiplexer_10 (
    .in0(controlsignal_op_decoder2_1_branch), .in1(controlsignal_funct_decoder2_1_branch), .out(Branch),
    .sel(Is_R_Type), .en(1'b1));
  Multiplexer multiplexer_11 (
    .in0(controlsignal_op_decoder2_1_jump), .in1(controlsignal_funct_decoder2_1_jump), .out(Jump),
    .sel(Is_R_Type), .en(1'b1));
  Multiplexer multiplexer_12 (
    .in0(controlsignal_op_decoder2_1_regwrite), .in1(controlsignal_funct_decoder2_1_regwrite),
    .out(RegWrite), .sel(Is_R_Type), .en(1'b1));
  Multiplexer multiplexer_13 (
    .in0(controlsignal_op_decoder2_1_memread), .in1(controlsignal_funct_decoder2_1_memread), .out(MemRead),
    .sel(Is_R_Type), .en(1'b1));
  Multiplexer multiplexer_14 (
    .in0(controlsignal_op_decoder2_1_memwrite), .in1(controlsignal_funct_decoder2_1_memwrite),
    .out(MemWrite), .sel(Is_R_Type), .en(1'b1));
  Multiplexer multiplexer_15 (
    .in0(controlsignal_op_decoder2_1_memtoreg), .in1(controlsignal_funct_decoder2_1_memtoreg),
    .out(MemtoReg), .sel(Is_R_Type), .en(1'b1));
  Multiplexer multiplexer_16 (
    .in0(controlsignal_op_decoder2_1_isbne), .in1(controlsignal_funct_decoder2_1_isbne), .out(IsBNE),
    .sel(Is_R_Type), .en(1'b1));
  Multiplexer multiplexer_17 (
    .in0(controlsignal_op_decoder2_1_issyscall), .in1(controlsignal_funct_decoder2_1_issyscall),
    .out(IsSyscall), .sel(Is_R_Type), .en(1'b1));
endmodule

// ALU_Op
module ALU_Op_Decoder (
  input  op0,
  input  op1,
  input  op2,
  input  op3,
  input  op4,
  input  op5,
  output aluop0,
  output aluop1,
  output aluop2,
  output aluop3
);

  wire and_1_out, and_2_out, and_3_out, and_4_out, and_5_out, and_6_out, and_7_out, and_8_out, and_9_out,
       and_10_out, and_11_out, not_1_out, not_2_out, not_3_out, not_4_out, not_5_out, not_6_out, not_7_out,
       not_8_out, not_9_out, not_10_out, not_11_out, not_12_out, not_13_out, not_14_out, not_15_out,
       not_16_out, not_17_out, not_18_out, not_19_out, not_20_out, not_21_out, not_22_out, not_23_out,
       not_24_out, not_25_out, not_26_out, not_27_out, not_28_out, not_29_out, not_30_out, not_31_out,
       not_32_out, not_33_out, not_34_out, not_35_out, not_36_out, not_37_out, not_38_out, not_39_out;

  not not_1 (not_1_out, op0);
  not not_2 (not_2_out, op1);
  not not_3 (not_3_out, op4);
  not not_4 (not_4_out, op0);
  not not_5 (not_5_out, op1);
  not not_6 (not_6_out, op3);
  not not_7 (not_7_out, op5);
  not not_8 (not_8_out, op0);
  not not_9 (not_9_out, op1);
  not not_10 (not_10_out, op3);
  not not_11 (not_11_out, op4);
  not not_12 (not_12_out, op0);
  not not_13 (not_13_out, op1);
  not not_14 (not_14_out, op4);
  not not_15 (not_15_out, op5);
  not not_16 (not_16_out, op1);
  not not_17 (not_17_out, op3);
  not not_18 (not_18_out, op0);
  not not_19 (not_19_out, op1);
  not not_20 (not_20_out, op4);
  not not_21 (not_21_out, op5);
  not not_22 (not_22_out, op0);
  not not_23 (not_23_out, op1);
  not not_24 (not_24_out, op3);
  not not_25 (not_25_out, op5);
  not not_26 (not_26_out, op0);
  not not_27 (not_27_out, op1);
  not not_28 (not_28_out, op3);
  not not_29 (not_29_out, op4);
  not not_30 (not_30_out, op0);
  not not_31 (not_31_out, op1);
  not not_32 (not_32_out, op3);
  not not_33 (not_33_out, op5);
  not not_34 (not_34_out, op0);
  not not_35 (not_35_out, op1);
  not not_36 (not_36_out, op4);
  not not_37 (not_37_out, op5);
  not not_38 (not_38_out, op1);
  not not_39 (not_39_out, op3);
  and and_1 (and_1_out, not_1_out, not_2_out, op2, op3, not_3_out, op5);
  and and_2 (and_2_out, not_4_out, not_5_out, op2, not_6_out, op4, not_7_out);
  and and_3 (and_3_out, not_8_out, not_9_out, op2, not_10_out, not_11_out);
  and and_4 (and_4_out, not_12_out, not_13_out, op2, not_14_out, not_15_out);
  and and_5 (and_5_out, op0, not_16_out, not_17_out, op4, op5);
  and and_6 (and_6_out, not_18_out, not_19_out, op2, op3, not_20_out, not_21_out);
  and and_7 (and_7_out, not_22_out, not_23_out, op2, not_24_out, op4, not_25_out);
  and and_8 (and_8_out, not_26_out, not_27_out, op2, not_28_out, not_29_out);
  and and_9 (and_9_out, not_30_out, not_31_out, op2, not_32_out, not_33_out);
  and and_10 (and_10_out, not_34_out, not_35_out, op2, not_36_out, not_37_out);
  and and_11 (and_11_out, op0, not_38_out, not_39_out, op4, op5);
  or or_1 (aluop0, and_1_out, and_2_out);
  or or_2 (aluop1, and_3_out, and_4_out, and_5_out);
  or or_3 (aluop2, and_6_out, and_7_out);
  or or_4 (aluop3, and_8_out, and_9_out, and_10_out, and_11_out);
endmodule

// ALU_Funct
module ALU_Funct_Decoder (
  input  funct0,
  input  funct1,
  input  funct2,
  input  funct3,
  input  funct4,
  input  funct5,
  output aluop0,
  output aluop1,
  output aluop2,
  output aluop3
);

  wire and_1_out, and_2_out, and_3_out, and_4_out, and_5_out, and_6_out, and_7_out, and_8_out, and_9_out,
       and_10_out, and_11_out, and_12_out, and_13_out, and_14_out, and_15_out, and_16_out, and_17_out,
       and_18_out, and_19_out, not_1_out, not_2_out, not_3_out, not_4_out, not_5_out, not_6_out, not_7_out,
       not_8_out, not_9_out, not_10_out, not_11_out, not_12_out, not_13_out, not_14_out, not_15_out,
       not_16_out, not_17_out, not_18_out, not_19_out, not_20_out, not_21_out, not_22_out, not_23_out,
       not_24_out, not_25_out, not_26_out, not_27_out, not_28_out, not_29_out, not_30_out, not_31_out,
       not_32_out, not_33_out, not_34_out, not_35_out, not_36_out, not_37_out, not_38_out, not_39_out,
       not_40_out, not_41_out, not_42_out, not_43_out, not_44_out, not_45_out, not_46_out, not_47_out,
       not_48_out, not_49_out, not_50_out, not_51_out, not_52_out, not_53_out, not_54_out, not_55_out,
       not_56_out, not_57_out, not_58_out, not_59_out, not_60_out, not_61_out, not_62_out, not_63_out,
       not_64_out, not_65_out, not_66_out, not_67_out;

  not not_1 (not_1_out, funct1);
  not not_2 (not_2_out, funct2);
  not not_3 (not_3_out, funct4);
  not not_4 (not_4_out, funct1);
  not not_5 (not_5_out, funct2);
  not not_6 (not_6_out, funct1);
  not not_7 (not_7_out, funct3);
  not not_8 (not_8_out, funct5);
  not not_9 (not_9_out, funct1);
  not not_10 (not_10_out, funct3);
  not not_11 (not_11_out, funct1);
  not not_12 (not_12_out, funct2);
  not not_13 (not_13_out, funct3);
  not not_14 (not_14_out, funct4);
  not not_15 (not_15_out, funct5);
  not not_16 (not_16_out, funct1);
  not not_17 (not_17_out, funct2);
  not not_18 (not_18_out, funct3);
  not not_19 (not_19_out, funct4);
  not not_20 (not_20_out, funct1);
  not not_21 (not_21_out, funct2);
  not not_22 (not_22_out, funct4);
  not not_23 (not_23_out, funct5);
  not not_24 (not_24_out, funct1);
  not not_25 (not_25_out, funct2);
  not not_26 (not_26_out, funct3);
  not not_27 (not_27_out, funct5);
  not not_28 (not_28_out, funct1);
  not not_29 (not_29_out, funct3);
  not not_30 (not_30_out, funct1);
  not not_31 (not_31_out, funct2);
  not not_32 (not_32_out, funct4);
  not not_33 (not_33_out, funct5);
  not not_34 (not_34_out, funct0);
  not not_35 (not_35_out, funct1);
  not not_36 (not_36_out, funct2);
  not not_37 (not_37_out, funct3);
  not not_38 (not_38_out, funct5);
  not not_39 (not_39_out, funct1);
  not not_40 (not_40_out, funct2);
  not not_41 (not_41_out, funct3);
  not not_42 (not_42_out, funct5);
  not not_43 (not_43_out, funct1);
  not not_44 (not_44_out, funct2);
  not not_45 (not_45_out, funct1);
  not not_46 (not_46_out, funct3);
  not not_47 (not_47_out, funct5);
  not not_48 (not_48_out, funct1);
  not not_49 (not_49_out, funct2);
  not not_50 (not_50_out, funct3);
  not not_51 (not_51_out, funct4);
  not not_52 (not_52_out, funct5);
  not not_53 (not_53_out, funct1);
  not not_54 (not_54_out, funct2);
  not not_55 (not_55_out, funct3);
  not not_56 (not_56_out, funct4);
  not not_57 (not_57_out, funct1);
  not not_58 (not_58_out, funct2);
  not not_59 (not_59_out, funct4);
  not not_60 (not_60_out, funct5);
  not not_61 (not_61_out, funct0);
  not not_62 (not_62_out, funct1);
  not not_63 (not_63_out, funct2);
  not not_64 (not_64_out, funct3);
  not not_65 (not_65_out, funct1);
  not not_66 (not_66_out, funct3);
  not not_67 (not_67_out, funct5);
  and and_1 (and_1_out, funct0, not_1_out, not_2_out, funct3, not_3_out, funct5);
  and and_2 (and_2_out, funct0, not_4_out, not_5_out, funct3, funct4, funct5);
  and and_3 (and_3_out, funct0, not_6_out, funct2, not_7_out, funct4, not_8_out);
  and and_4 (and_4_out, funct0, not_9_out, funct2, not_10_out, funct4, funct5);
  and and_5 (and_5_out, funct0, not_11_out, not_12_out, not_13_out, not_14_out, not_15_out);
  and and_6 (and_6_out, funct0, not_16_out, not_17_out, not_18_out, not_19_out, funct5);
  and and_7 (and_7_out, funct0, not_20_out, not_21_out, funct3, not_22_out, not_23_out);
  and and_8 (and_8_out, funct0, not_24_out, not_25_out, not_26_out, funct4, not_27_out);
  and and_9 (and_9_out, funct0, not_28_out, funct2, not_29_out, funct4, funct5);
  and and_10 (and_10_out, funct0, not_30_out, not_31_out, funct3, not_32_out, not_33_out);
  and and_11 (and_11_out, not_34_out, not_35_out, not_36_out, not_37_out, funct4, not_38_out);
  and and_12 (and_12_out, funct0, not_39_out, not_40_out, not_41_out, funct4, not_42_out);
  and and_13 (and_13_out, funct0, not_43_out, not_44_out, funct3, funct4, funct5);
  and and_14 (and_14_out, funct0, not_45_out, funct2, not_46_out, funct4, not_47_out);
  and and_15 (and_15_out, funct0, not_48_out, not_49_out, not_50_out, not_51_out, not_52_out);
  and and_16 (and_16_out, funct0, not_53_out, not_54_out, not_55_out, not_56_out, funct5);
  and and_17 (and_17_out, funct0, not_57_out, not_58_out, funct3, not_59_out, not_60_out);
  and and_18 (and_18_out, not_61_out, not_62_out, not_63_out, not_64_out, funct4, funct5);
  and and_19 (and_19_out, funct0, not_65_out, funct2, not_66_out, funct4, not_67_out);
  or or_1 (aluop0, and_1_out, and_2_out, and_3_out, and_4_out);
  or or_2 (aluop1, and_5_out, and_6_out, and_7_out, and_8_out, and_9_out);
  or or_3 (aluop2, and_10_out, and_11_out, and_12_out, and_13_out, and_14_out);
  or or_4 (aluop3, and_15_out, and_16_out, and_17_out, and_18_out, and_19_out);
endmodule

// Signal_Op1
module Controlsignal_Op_Decoder1 (
  input  op0,
  input  op1,
  input  op2,
  input  op3,
  input  op4,
  input  op5,
  output R1,
  output R2,
  output W0,
  output W1,
  output Din0,
  output Din1,
  output SEXT0,
  output SEXT1,
  output A,
  output B
);

  wire and_1_out, and_2_out, and_3_out, and_4_out, and_5_out, and_6_out, and_8_out, and_9_out, and_10_out,
       and_11_out, and_12_out, and_13_out, and_14_out, not_1_out, not_2_out, not_3_out, not_4_out, not_5_out,
       not_6_out, not_7_out, not_8_out, not_9_out, not_10_out, not_11_out, not_12_out, not_13_out,
       not_14_out, not_15_out, not_16_out, not_17_out, not_18_out, not_19_out, not_20_out, not_21_out,
       not_22_out, not_23_out, not_24_out, not_25_out, not_26_out, not_27_out, not_28_out, not_29_out,
       not_30_out, not_31_out, not_32_out, not_33_out, not_34_out, not_35_out, not_36_out, not_37_out,
       not_38_out, not_39_out, not_40_out, not_41_out, not_42_out, not_43_out, not_44_out, not_45_out,
       not_46_out, not_47_out, not_48_out, not_49_out, not_50_out, not_51_out;

  not not_1 (not_1_out, op0);
  not not_2 (not_2_out, op1);
  not not_3 (not_3_out, op3);
  not not_4 (not_4_out, op4);
  not not_5 (not_5_out, op5);
  not not_6 (not_6_out, op0);
  not not_7 (not_7_out, op1);
  not not_8 (not_8_out, op3);
  not not_9 (not_9_out, op4);
  not not_10 (not_10_out, op0);
  not not_11 (not_11_out, op1);
  not not_12 (not_12_out, op4);
  not not_13 (not_13_out, op5);
  not not_14 (not_14_out, op0);
  not not_15 (not_15_out, op1);
  not not_16 (not_16_out, op4);
  not not_17 (not_17_out, op1);
  not not_18 (not_18_out, op2);
  not not_19 (not_19_out, op3);
  not not_20 (not_20_out, op0);
  not not_21 (not_21_out, op1);
  not not_22 (not_22_out, op3);
  not not_23 (not_23_out, op5);
  not not_24 (not_24_out, op1);
  not not_25 (not_25_out, op2);
  not not_26 (not_26_out, op3);
  not not_27 (not_27_out, op0);
  not not_28 (not_28_out, op1);
  not not_29 (not_29_out, op3);
  not not_30 (not_30_out, op4);
  not not_31 (not_31_out, op5);
  not not_32 (not_32_out, op0);
  not not_33 (not_33_out, op1);
  not not_34 (not_34_out, op3);
  not not_35 (not_35_out, op4);
  not not_36 (not_36_out, op0);
  not not_37 (not_37_out, op1);
  not not_38 (not_38_out, op4);
  not not_39 (not_39_out, op5);
  not not_40 (not_40_out, op0);
  not not_41 (not_41_out, op1);
  not not_42 (not_42_out, op4);
  not not_43 (not_43_out, op1);
  not not_44 (not_44_out, op2);
  not not_45 (not_45_out, op3);
  not not_46 (not_46_out, op1);
  not not_47 (not_47_out, op3);
  not not_48 (not_48_out, op0);
  not not_49 (not_49_out, op1);
  not not_50 (not_50_out, op3);
  not not_51 (not_51_out, op5);
  and and_1 (and_1_out, not_1_out, not_2_out, op2, not_3_out, not_4_out, not_5_out);
  and and_2 (and_2_out, not_6_out, not_7_out, op2, not_8_out, not_9_out, op5);
  and and_3 (and_3_out, not_10_out, not_11_out, op2, op3, not_12_out, not_13_out);
  and and_4 (and_4_out, not_14_out, not_15_out, op2, op3, not_16_out, op5);
  and and_5 (and_5_out, op0, not_17_out, not_18_out, not_19_out, op4, op5);
  and and_6 (and_6_out, not_20_out, not_21_out, op2, not_22_out, op4, not_23_out);
  and and_7 (Din1, op0, not_24_out, not_25_out, not_26_out, op4, op5);
  and and_8 (and_8_out, not_27_out, not_28_out, op2, not_29_out, not_30_out, not_31_out);
  and and_9 (and_9_out, not_32_out, not_33_out, op2, not_34_out, not_35_out, op5);
  and and_10 (and_10_out, not_36_out, not_37_out, op2, op3, not_38_out, not_39_out);
  and and_11 (and_11_out, not_40_out, not_41_out, op2, op3, not_42_out, op5);
  and and_12 (and_12_out, op0, not_43_out, not_44_out, not_45_out, op4, op5);
  and and_13 (and_13_out, op0, not_46_out, op2, not_47_out, op4, op5);
  and and_14 (and_14_out, not_48_out, not_49_out, op2, not_50_out, op4, not_51_out);
  or or_1 (W1, and_1_out, and_2_out, and_3_out, and_4_out, and_5_out, and_6_out);
  or or_2 (B, and_8_out, and_9_out, and_10_out, and_11_out, and_12_out, and_13_out, and_14_out);

  assign A = 1'b0;
  assign Din0 = 1'b0;
  assign R1 = 1'b0;
  assign R2 = 1'b0;
  assign SEXT0 = 1'b0;
  assign SEXT1 = 1'b0;
  assign W0 = 1'b0;
endmodule

// Signal_Funct1
module Controlsignal_Funct_Decoder1 (
  input  funct0,
  input  funct1,
  input  funct2,
  input  funct3,
  input  funct4,
  input  funct5,
  output R1,
  output R2,
  output W0,
  output W1,
  output Din0,
  output Din1,
  output SEXT0,
  output SEXT1,
  output A,
  output B
);

  wire and_1_out, and_2_out, and_3_out, and_8_out, and_9_out, and_10_out, and_12_out, and_13_out, and_14_out,
       and_15_out, not_1_out, not_2_out, not_3_out, not_4_out, not_5_out, not_6_out, not_7_out, not_8_out,
       not_9_out, not_10_out, not_11_out, not_12_out, not_13_out, not_14_out, not_15_out, not_16_out,
       not_17_out, not_18_out, not_19_out, not_20_out, not_21_out, not_22_out, not_23_out, not_24_out,
       not_25_out, not_26_out, not_27_out, not_28_out, not_29_out, not_30_out, not_31_out, not_32_out,
       not_33_out, not_34_out, not_35_out, not_36_out, not_37_out, not_38_out, not_39_out, not_40_out,
       not_41_out, not_42_out, not_43_out, not_44_out, not_45_out, not_46_out, not_47_out, not_48_out,
       not_49_out, not_50_out, not_51_out, not_52_out, not_53_out, not_54_out, not_55_out, not_56_out,
       not_57_out, not_58_out, not_59_out, not_60_out, not_61_out, not_62_out, not_63_out, not_64_out,
       not_65_out, not_66_out, not_67_out, not_68_out, not_69_out, not_70_out, not_71_out;

  not not_1 (not_1_out, funct0);
  not not_2 (not_2_out, funct1);
  not not_3 (not_3_out, funct2);
  not not_4 (not_4_out, funct3);
  not not_5 (not_5_out, funct4);
  not not_6 (not_6_out, funct5);
  not not_7 (not_7_out, funct0);
  not not_8 (not_8_out, funct1);
  not not_9 (not_9_out, funct2);
  not not_10 (not_10_out, funct3);
  not not_11 (not_11_out, funct0);
  not not_12 (not_12_out, funct1);
  not not_13 (not_13_out, funct2);
  not not_14 (not_14_out, funct3);
  not not_15 (not_15_out, funct5);
  not not_16 (not_16_out, funct0);
  not not_17 (not_17_out, funct1);
  not not_18 (not_18_out, funct4);
  not not_19 (not_19_out, funct5);
  not not_20 (not_20_out, funct0);
  not not_21 (not_21_out, funct1);
  not not_22 (not_22_out, funct3);
  not not_23 (not_23_out, funct4);
  not not_24 (not_24_out, funct5);
  not not_25 (not_25_out, funct0);
  not not_26 (not_26_out, funct1);
  not not_27 (not_27_out, funct3);
  not not_28 (not_28_out, funct4);
  not not_29 (not_29_out, funct5);
  not not_30 (not_30_out, funct0);
  not not_31 (not_31_out, funct1);
  not not_32 (not_32_out, funct4);
  not not_33 (not_33_out, funct5);
  not not_34 (not_34_out, funct0);
  not not_35 (not_35_out, funct1);
  not not_36 (not_36_out, funct2);
  not not_37 (not_37_out, funct3);
  not not_38 (not_38_out, funct4);
  not not_39 (not_39_out, funct5);
  not not_40 (not_40_out, funct0);
  not not_41 (not_41_out, funct1);
  not not_42 (not_42_out, funct2);
  not not_43 (not_43_out, funct3);
  not not_44 (not_44_out, funct0);
  not not_45 (not_45_out, funct1);
  not not_46 (not_46_out, funct2);
  not not_47 (not_47_out, funct3);
  not not_48 (not_48_out, funct5);
  not not_49 (not_49_out, funct0);
  not not_50 (not_50_out, funct1);
  not not_51 (not_51_out, funct4);
  not not_52 (not_52_out, funct5);
  not not_53 (not_53_out, funct0);
  not not_54 (not_54_out, funct1);
  not not_55 (not_55_out, funct2);
  not not_56 (not_56_out, funct3);
  not not_57 (not_57_out, funct4);
  not not_58 (not_58_out, funct5);
  not not_59 (not_59_out, funct0);
  not not_60 (not_60_out, funct1);
  not not_61 (not_61_out, funct2);
  not not_62 (not_62_out, funct3);
  not not_63 (not_63_out, funct0);
  not not_64 (not_64_out, funct1);
  not not_65 (not_65_out, funct2);
  not not_66 (not_66_out, funct3);
  not not_67 (not_67_out, funct5);
  not not_68 (not_68_out, funct0);
  not not_69 (not_69_out, funct1);
  not not_70 (not_70_out, funct4);
  not not_71 (not_71_out, funct5);
  and and_1 (and_1_out, not_1_out, not_2_out, not_3_out, not_4_out, not_5_out, not_6_out);
  and and_2 (and_2_out, not_7_out, not_8_out, not_9_out, not_10_out, funct4, funct5);
  and and_3 (and_3_out, not_11_out, not_12_out, not_13_out, not_14_out, funct4, not_15_out);
  and and_4 (R2, not_16_out, not_17_out, funct2, funct3, not_18_out, not_19_out);
  and and_5 (W0, not_20_out, not_21_out, funct2, not_22_out, not_23_out, not_24_out);
  and and_6 (Din0, not_25_out, not_26_out, funct2, not_27_out, not_28_out, not_29_out);
  and and_7 (SEXT0, not_30_out, not_31_out, funct2, funct3, not_32_out, not_33_out);
  and and_8 (and_8_out, not_34_out, not_35_out, not_36_out, not_37_out, not_38_out, not_39_out);
  and and_9 (and_9_out, not_40_out, not_41_out, not_42_out, not_43_out, funct4, funct5);
  and and_10 (and_10_out, not_44_out, not_45_out, not_46_out, not_47_out, funct4, not_48_out);
  and and_11 (A, not_49_out, not_50_out, funct2, funct3, not_51_out, not_52_out);
  and and_12 (and_12_out, not_53_out, not_54_out, not_55_out, not_56_out, not_57_out, not_58_out);
  and and_13 (and_13_out, not_59_out, not_60_out, not_61_out, not_62_out, funct4, funct5);
  and and_14 (and_14_out, not_63_out, not_64_out, not_65_out, not_66_out, funct4, not_67_out);
  and and_15 (and_15_out, not_68_out, not_69_out, funct2, funct3, not_70_out, not_71_out);
  or or_1 (R1, and_1_out, and_2_out, and_3_out);
  or or_2 (SEXT1, and_8_out, and_9_out, and_10_out);
  or or_3 (B, and_12_out, and_13_out, and_14_out, and_15_out);

  assign Din1 = 1'b0;
  assign W1 = 1'b0;
endmodule

// Signal_Op2
module Controlsignal_Op_Decoder2 (
  input  op0,
  input  op1,
  input  op2,
  input  op3,
  input  op4,
  input  op5,
  output JR,
  output Branch,
  output Jump,
  output RegWrite,
  output MemRead,
  output MemWrite,
  output MemtoReg,
  output IsBNE,
  output isSyscall
);

  wire and_1_out, and_2_out, and_3_out, and_4_out, and_5_out, and_6_out, and_7_out, not_1_out, not_2_out,
       not_3_out, not_4_out, not_5_out, not_6_out, not_7_out, not_8_out, not_9_out, not_10_out, not_11_out,
       not_12_out, not_13_out, not_14_out, not_15_out, not_16_out, not_17_out, not_18_out, not_19_out,
       not_20_out, not_21_out, not_22_out, not_23_out, not_24_out, not_25_out, not_26_out, not_27_out,
       not_28_out, not_29_out, not_30_out, not_31_out, not_32_out, not_33_out, not_34_out, not_35_out,
       not_36_out, not_37_out, not_38_out, not_39_out, not_40_out;

  not not_1 (not_1_out, op0);
  not not_2 (not_2_out, op1);
  not not_3 (not_3_out, op2);
  not not_4 (not_4_out, op4);
  not not_5 (not_5_out, op0);
  not not_6 (not_6_out, op1);
  not not_7 (not_7_out, op2);
  not not_8 (not_8_out, op4);
  not not_9 (not_9_out, op5);
  not not_10 (not_10_out, op0);
  not not_11 (not_11_out, op1);
  not not_12 (not_12_out, op2);
  not not_13 (not_13_out, op3);
  not not_14 (not_14_out, op5);
  not not_15 (not_15_out, op0);
  not not_16 (not_16_out, op1);
  not not_17 (not_17_out, op2);
  not not_18 (not_18_out, op3);
  not not_19 (not_19_out, op0);
  not not_20 (not_20_out, op1);
  not not_21 (not_21_out, op3);
  not not_22 (not_22_out, op5);
  not not_23 (not_23_out, op0);
  not not_24 (not_24_out, op1);
  not not_25 (not_25_out, op4);
  not not_26 (not_26_out, op1);
  not not_27 (not_27_out, op2);
  not not_28 (not_28_out, op3);
  not not_29 (not_29_out, op1);
  not not_30 (not_30_out, op2);
  not not_31 (not_31_out, op3);
  not not_32 (not_32_out, op1);
  not not_33 (not_33_out, op3);
  not not_34 (not_34_out, op1);
  not not_35 (not_35_out, op2);
  not not_36 (not_36_out, op3);
  not not_37 (not_37_out, op0);
  not not_38 (not_38_out, op1);
  not not_39 (not_39_out, op2);
  not not_40 (not_40_out, op4);
  and and_1 (and_1_out, not_1_out, not_2_out, not_3_out, op3, not_4_out, op5);
  and and_2 (and_2_out, not_5_out, not_6_out, not_7_out, op3, not_8_out, not_9_out);
  and and_3 (and_3_out, not_10_out, not_11_out, not_12_out, not_13_out, op4, not_14_out);
  and and_4 (and_4_out, not_15_out, not_16_out, not_17_out, not_18_out, op4, op5);
  and and_5 (and_5_out, not_19_out, not_20_out, op2, not_21_out, not_22_out);
  and and_6 (and_6_out, not_23_out, not_24_out, op2, not_25_out);
  and and_7 (and_7_out, op0, not_26_out, not_27_out, not_28_out, op4, op5);
  and and_8 (MemRead, op0, not_29_out, not_30_out, not_31_out, op4, op5);
  and and_9 (MemWrite, op0, not_32_out, op2, not_33_out, op4, op5);
  and and_10 (MemtoReg, op0, not_34_out, not_35_out, not_36_out, op4, op5);
  and and_11 (IsBNE, not_37_out, not_38_out, not_39_out, op3, not_40_out, op5);
  or or_1 (Branch, and_1_out, and_2_out);
  or or_2 (Jump, and_3_out, and_4_out);
  or or_3 (RegWrite, and_5_out, and_6_out, and_7_out);

  assign isSyscall = 1'b0;
  assign JR = 1'b0;
endmodule

// Signal_Funct2
module Controlsignal_Funct_Decoder2 (
  input  funct0,
  input  funct1,
  input  funct2,
  input  funct3,
  input  funct4,
  input  funct5,
  output JR,
  output Branch,
  output Jump,
  output RegWrite,
  output MemRead,
  output MemWrite,
  output MemtoReg,
  output IsBNE,
  output IsSyscall
);

  wire and_2_out, and_3_out, and_4_out, and_5_out, and_6_out, not_1_out, not_2_out, not_3_out, not_4_out,
       not_5_out, not_6_out, not_7_out, not_8_out, not_9_out, not_10_out, not_11_out, not_12_out, not_13_out,
       not_14_out, not_15_out, not_16_out, not_17_out, not_18_out, not_19_out, not_20_out, not_21_out,
       not_22_out, not_23_out, not_24_out;

  not not_1 (not_1_out, funct0);
  not not_2 (not_2_out, funct1);
  not not_3 (not_3_out, funct3);
  not not_4 (not_4_out, funct4);
  not not_5 (not_5_out, funct5);
  not not_6 (not_6_out, funct1);
  not not_7 (not_7_out, funct2);
  not not_8 (not_8_out, funct3);
  not not_9 (not_9_out, funct5);
  not not_10 (not_10_out, funct0);
  not not_11 (not_11_out, funct1);
  not not_12 (not_12_out, funct2);
  not not_13 (not_13_out, funct3);
  not not_14 (not_14_out, funct1);
  not not_15 (not_15_out, funct2);
  not not_16 (not_16_out, funct4);
  not not_17 (not_17_out, funct1);
  not not_18 (not_18_out, funct2);
  not not_19 (not_19_out, funct1);
  not not_20 (not_20_out, funct3);
  not not_21 (not_21_out, funct0);
  not not_22 (not_22_out, funct1);
  not not_23 (not_23_out, funct4);
  not not_24 (not_24_out, funct5);
  and and_1 (JR, not_1_out, not_2_out, funct2, not_3_out, not_4_out, not_5_out);
  and and_2 (and_2_out, not_6_out, not_7_out, not_8_out, not_9_out);
  and and_3 (and_3_out, not_10_out, not_11_out, not_12_out, not_13_out, funct4);
  and and_4 (and_4_out, funct0, not_14_out, not_15_out, not_16_out);
  and and_5 (and_5_out, funct0, not_17_out, not_18_out, funct3, funct5);
  and and_6 (and_6_out, funct0, not_19_out, funct2, not_20_out, funct4);
  and and_7 (IsSyscall, not_21_out, not_22_out, funct2, funct3, not_23_out, not_24_out);
  or or_1 (RegWrite, and_2_out, and_3_out, and_4_out, and_5_out, and_6_out);

  assign Branch = 1'b0;
  assign IsBNE = 1'b0;
  assign Jump = 1'b0;
  assign MemRead = 1'b0;
  assign MemtoReg = 1'b0;
  assign MemWrite = 1'b0;
endmodule
