// Logisim project alu.circ as structural Verilog: 17 circuits, main circuit ALU
module ALU (
  input  [31:0] X,
  input  [31:0] Y,
  input  [3:0] AluOP,
  output Signed_Overflow,
  output UnSigned_Overflow,
  output Equal,
  output [31:0] Result,
  output [31:0] Result_2
);

  wire Add_cf, Add_of, and_2_out, and_3_out, and_4_out, and_5_out, and_6_out, and_7_out, not_2_out,
       not_3_out, not_4_out, not_5_out, Sub_cf, Sub_of;
  wire [31:0] Add_result, AND_out, ASR_result, Div_result1, Div_result2, LSL_result, LSR_result, Mul_result1,
       Mul_result2, not_1_out, OR_out, SC_result, Sub_result, UC_result, XOR_out;

  // Probe on X
  // Probe on X
  // Probe on Y
  // Probe on Y
  Logical_Shift_Left LSL (.X(X), .Y(Y), .Result(LSL_result));
  Logical_Shift_Right LSR (.X(X), .Y(Y), .Result(LSR_result));
  Arithmetic_Shift_Right ASR (.X(X), .Y(Y), .Result(ASR_result));
  Multiplier Mul (.X(X), .Y(Y), .Result1(Mul_result1), .Result2(Mul_result2));
  Divider Div (.X(X), .Y(Y), .Result1(Div_result1), .Result2(Div_result2));
  Adder Add (.X(X), .Y(Y), .Result(Add_result), .CF(Add_cf), .OF(Add_of));
  Subtractor Sub (.X(X), .Y(Y), .Result(Sub_result), .CF(Sub_cf), .OF(Sub_of));
  assign AND_out = X & Y;  // AND_Gate AND, 32 bits wide
  assign OR_out = X | Y;  // OR_Gate OR, 32 bits wide
  assign XOR_out = X ^ Y;  // XOR_Gate XOR, 32 bits wide
  Signed_Compare SC (.X(X), .Y(Y), .Result(SC_result));
  Unsigned_Compare UC (.X(X), .Y(Y), .Result(UC_result));
  Comparator #(.width(32)) comparator_1 (.a(X), .b(Y), .eq(Equal));  // open: gt, lt
  // Probe on AluOP
  assign not_1_out = ~OR_out;  // NOT_Gate not_1, 32 bits wide
  // Probe on Result
  // Probe on Result
  Multiplexer #(.select(4), .width(32)) multiplexer_1 (
    .in0(LSL_result), .in1(ASR_result), .in2(LSR_result), .in3(Mul_result1), .in4(Div_result1),
    .in5(Add_result), .in6(Sub_result), .in7(AND_out), .in8(OR_out), .in9(XOR_out), .in10(not_1_out),
    .in11(SC_result), .in12(UC_result), .in13({32{1'b0}}), .in14({32{1'b0}}), .in15({32{1'b0}}),
    .out(Result), .sel(AluOP), .en(1'b1));
  // Probe on Result_2
  not not_2 (not_2_out, AluOP[1]);
  not not_3 (not_3_out, AluOP[3]);
  and and_2 (and_2_out, not_3_out, AluOP[2], not_2_out, AluOP[0]);
  Multiplexer #(.select(4), .width(32)) multiplexer_2 (
    .in0({32{1'b0}}), .in1({32{1'b0}}), .in2({32{1'b0}}), .in3(Mul_result2), .in4(Div_result2),
    .in5({32{1'b0}}), .in6({32{1'b0}}), .in7({32{1'b0}}), .in8({32{1'b0}}), .in9({32{1'b0}}),
    .in10({32{1'b0}}), .in11({32{1'b0}}), .in12({32{1'b0}}), .in13({32{1'b0}}), .in14({32{1'b0}}),
    .in15({32{1'b0}}), .out(Result_2), .sel(AluOP), .en(1'b1));
  not not_4 (not_4_out, AluOP[3]);
  and and_3 (and_3_out, not_4_out, AluOP[2], AluOP[1], not_5_out);
  not not_5 (not_5_out, AluOP[0]);
  and and_4 (and_4_out, Add_of, and_2_out);
  and and_5 (and_5_out, Sub_of, and_3_out);
  and and_6 (and_6_out, Add_cf, and_2_out);
  and and_7 (and_7_out, Sub_cf, and_3_out);
  or or_2 (Signed_Overflow, and_4_out, and_5_out);
  or or_3 (UnSigned_Overflow, and_6_out, and_7_out);

  // Other names for the same wires on the sheet: CF = UnSigned_Overflow; OF = Signed_Overflow;
  //   Result2[31:0] = Result_2; S[3:0] = AluOP

  // Notes on the sheet:
  //   不要改变此引脚区域内容，也不要改变ALU封装形式
  //   输入引脚
  //   请在下方利用上方输入输出引脚的隧道信号构建ALU电路，ctrl+d复制选择部件
  //   输出引脚
  //   探测区域
endmodule

module \演示电路  (
  input  [31:0] X,
  input  [31:0] Y,
  input  [3:0] ALUOP,
  output Signed_Overflow,
  output Unsigned_overflow,
  output [31:0] Result,
  output [31:0] Result_2,
  output Equal
);

  // Probe on X
  // Probe on X
  ALU alu_1 (
    .AluOP(ALUOP), .X(X), .Equal(Equal), .Result(Result), .Signed_Overflow(Signed_Overflow), .Y(Y),
    .Result_2(Result_2), .UnSigned_Overflow(Unsigned_overflow));
  // Probe on ALUOP
  // Probe on Y
  // Probe on Y
  // Probe on Result
  // Probe on Result
  // Probe on Result_2
endmodule

module \毛刺现象  (
  input  in_1
);

  wire and_1_out, not_1_out;

  not not_1 (not_1_out, in_1);
  and and_1 (and_1_out, in_1, not_1_out);
  Counter counter_1 (.clk(and_1_out));  // open: load, D, count, Q, carry, clr

  // Notes on the sheet:
  //   尝试反复点击输入引脚改变值，观察计算器的变化
  //   逻辑上应该为零，但计数器观察到了跳变
endmodule

module \震荡电路  (
  input  in_1,
  output out_2
);

  nand nand_1 (out_2, in_1, out_2);

  // Notes on the sheet:
  //   尝试修改输入引脚的电平,输入输出存在反馈，导致电路状态不稳定
  //   如出现类似情况，尝试去掉部分回路连接直至故障消除
  //   华中科技大学计算机学院 计算机组成原理
endmodule

module \信号冲突  (
  input  in_1,
  input  in_2,
  output out_3
);


  assign in_2 = in_1;
  assign out_3 = in_1;

  // Notes on the sheet:
  //   输入相同时无问题，不同时出错，红色显示
  //   华中科技大学计算机学院 计算机组成原理
endmodule

module \不同颜色信号线  (
  input  \引脚类型不对 ,
  input  [1:0] in_2,
  input  in_3
);

  wire undriven;
  wire [1:0] nand_2_out, undriven_3;
  wire [1:1] undriven_2;

  nand nand_1 (\引脚类型不对 , 1'b1, 1'b0, undriven, 1'b0);
  assign nand_2_out = ~(in_2 & undriven_3 & {undriven_2[1], in_3});  // NAND_Gate nand_2, 2 bits wide
  // Pins of 1 and 2 bits meet at {undriven_2[1], in_3}

  // Notes on the sheet:
  //   深绿色表示高电平
  //   蓝色表示未知状态
  //   灰色表示飞线
  //   亮绿色表示高电平
  //   红色表示信号冲突
  //   黑色表示多位总线
  //   橙色表示位宽不匹配
  //   华中科技大学计算机学院 计算机组成原理
endmodule

module \分线器使用  (
  input  [7:0] in_1
);


  // Notes on the sheet:
  //   分线器使用方法
  //   8分3，两个3位，一个2位
  //   分线器不分输入输出，可反向使用进行线缆汇总
  //   华中科技大学计算机学院 计算机组成原理
  //   8分二，高位在下
  //   8分二，高位在上
  //   只分部分位，位宽不对称
  //   只分1位，如取符号位
  //   8分8
endmodule

module Logical_Shift_Left (
  input  [31:0] X,
  input  [31:0] Y,
  output [31:0] Result
);

  Shifter #(.width(32)) shifter_1 (.in(X), .\dist (Y[4:0]), .out(Result));
endmodule

module Arithmetic_Shift_Right (
  input  [31:0] X,
  input  [31:0] Y,
  output [31:0] Result
);

  Shifter #(.width(32), .shift("ar")) shifter_1 (.in(X), .\dist (Y[4:0]), .out(Result));
endmodule

module Logical_Shift_Right (
  input  [31:0] X,
  input  [31:0] Y,
  output [31:0] Result
);

  Shifter #(.width(32), .shift("lr")) shifter_1 (.in(X), .\dist (Y[4:0]), .out(Result));
endmodule

module Multiplier (
  input  [31:0] X,
  input  [31:0] Y,
  output [31:0] Result1,
  output [31:0] Result2
);

  Multiplier_part #(.width(32)) multiplier_1 (.a(X), .b(Y), .out(Result1), .cin({32{1'b0}}), .cout(Result2));
endmodule

module Divider (
  input  [31:0] X,
  input  [31:0] Y,
  output [31:0] Result1,
  output [31:0] Result2
);

  Divider_part #(.width(32)) divider_1 (.a(X), .b(Y), .out(Result1), .upper({32{1'b0}}), .rem(Result2));
endmodule

module Adder (
  input  [31:0] X,
  input  [31:0] Y,
  output [31:0] Result,
  output CF,
  output OF
);

  wire adder_1_cout;

  Adder_part #(.width(31)) adder_1 (.a(X[30:0]), .b(Y[30:0]), .out(Result[30:0]), .cin(1'b0), .cout(adder_1_cout));
  Adder_part #(.width(1)) adder_2 (.a(X[31]), .b(Y[31]), .out(Result[31]), .cin(adder_1_cout), .cout(CF));
  xor xor_1 (OF, adder_1_cout, CF);
endmodule

module Subtractor (
  input  [31:0] X,
  input  [31:0] Y,
  output [31:0] Result,
  output CF,
  output OF
);

  wire subtractor_1_bout;

  Subtractor_part #(.width(31)) subtractor_1 (
    .a(X[30:0]), .b(Y[30:0]), .out(Result[30:0]), .bin(1'b0), .bout(subtractor_1_bout));
  Subtractor_part #(.width(1)) subtractor_2 (
    .a(X[31]), .b(Y[31]), .out(Result[31]), .bin(subtractor_1_bout), .bout(CF));
  xor xor_1 (OF, subtractor_1_bout, CF);
endmodule

module Signed_Compare (
  input  [31:0] X,
  input  [31:0] Y,
  output [31:0] Result
);

  wire comparator_1_lt;

  Comparator #(.width(32)) comparator_1 (.a(X), .b(Y), .lt(comparator_1_lt));  // open: gt, eq
  Multiplexer #(.width(32)) multiplexer_1 (
    .in0({32{1'b0}}), .in1(32'h1), .out(Result), .sel(comparator_1_lt), .en(1'b1));
endmodule

module Unsigned_Compare (
  input  [31:0] X,
  input  [31:0] Y,
  output [31:0] Result
);

  wire comparator_1_lt;

  Comparator #(.width(32), .mode("unsigned")) comparator_1 (.a(X), .b(Y), .lt(comparator_1_lt));  // open: gt, eq
  Multiplexer #(.width(32)) multiplexer_1 (
    .in0({32{1'b0}}), .in1(32'h1), .out(Result), .sel(comparator_1_lt), .en(1'b1));
endmodule

module \扩展_等差数列求和  (
  input  [31:0] \初始值 ,
  input  [31:0] \等差值 
);

  wire \清零按钮_out , \脉冲_out ;
  wire [31:0] alu_1_result, alu_2_result, alu_3_result, \寄存器_q , \计数_q ;

  ALU alu_1 (
    .AluOP(4'b0101), .X(\初始值 ), .Result(alu_1_result), .Y(alu_2_result));  // open: Equal, Signed_Overflow, Result_2, UnSigned_Overflow
  ALU alu_2 (
    .AluOP(4'b0011), .X(\等差值 ), .Result(alu_2_result), .Y(\计数_q ));  // open: Equal, Signed_Overflow, Result_2, UnSigned_Overflow
  Counter #(.width(32), .max('hffffffff)) \u_计数  (
    .load(1'b0), .count(1'b1), .Q(\计数_q ), .clk(\脉冲_out ), .clr(\清零按钮_out ));  // open: D, carry
  Clock \u_脉冲  (.out(\脉冲_out ));
  ALU alu_3 (
    .AluOP(4'b0101), .X(\寄存器_q ), .Result(alu_3_result), .Y(alu_1_result));  // open: Equal, Signed_Overflow, Result_2, UnSigned_Overflow
  Button \u_清零按钮  (.out(\清零按钮_out ));
  Register #(.width(32)) \u_寄存器  (.D(alu_3_result), .en(1'b1), .Q(\寄存器_q ), .clk(\脉冲_out ), .clr(\清零按钮_out ));
  Hex_Digit_Display hex_digit_display_1 (.value(\寄存器_q [31:28]), .dp(1'b0));
  Hex_Digit_Display hex_digit_display_2 (.value(\寄存器_q [23:20]), .dp(1'b0));
  Hex_Digit_Display hex_digit_display_3 (.value(\寄存器_q [27:24]), .dp(1'b0));
  Hex_Digit_Display hex_digit_display_4 (.value(\寄存器_q [19:16]), .dp(1'b0));
  Hex_Digit_Display hex_digit_display_5 (.value(\寄存器_q [15:12]), .dp(1'b0));
  Hex_Digit_Display hex_digit_display_6 (.value(\寄存器_q [7:4]), .dp(1'b0));
  Hex_Digit_Display hex_digit_display_7 (.value(\寄存器_q [11:8]), .dp(1'b0));
  Hex_Digit_Display hex_digit_display_8 (.value(\寄存器_q [3:0]), .dp(1'b0));
endmodule
